// Logisim project 16bit RAM.circ as structural Verilog: 1 circuit, main circuit main
module main (
  input  [15:0] Address_bus,
  input  Byte_Enable_1,
  input  Byte_Enable_0,
  input  R_W_,
  output [15:0] Databus
);

  RAM #(.addrWidth(15), .bus("asynch")) ram_1 (
    .addr(Address_bus[15:1]), .data(Databus[15:8]), .sel(Byte_Enable_1), .ld(R_W_));  // open: clr
  RAM #(.addrWidth(15), .bus("asynch")) ram_2 (
    .addr(Address_bus[15:1]), .data(Databus[7:0]), .sel(Byte_Enable_0), .ld(R_W_));  // open: clr
endmodule
