// Logisim project Zora.circ as structural Verilog: 68 circuits, main circuit main
module reworked_main (
);

  wire and_1_out, and_2_out, and_3_out, and_4_out, and_5_out, and_6_out, and_7_out, buffer_1_out,
       buffer_2_out, clock_1_out, Instruction_Decode_cin_en, IRQ_Controller_nint, magic_cu_1_alu_ctrl,
       magic_cu_1_ir_ctrl, magic_cu_1_ncli_rst, magic_cu_1_nfetching, magic_cu_1_nsei, magic_cu_1_nshft_en,
       magic_cu_1_tmp_ctrl, or_1_out, or_2_out, or_3_out, or_4_out, pull_resistor_1_node,
       pull_resistor_2_node;
  wire [1:0] magic_cu_1_ar_ctrl;
  wire [2:0] magic_cu_1_decode_ctrl, magic_cu_1_flag_ctrl;
  wire [3:0] CLKs, magic_cu_1_io_mem_ctrl, nCLKs;
  wire [4:0] magic_cu_1_pc_ctrl;
  wire [5:0] magic_cu_1_sp_ctrl;
  wire [7:0] alu_1_flags_out, alu_1_out_6, DATABUS, flag_register_1_flags, Instruction_Decode_clks,
       Instruction_Decode_noes, IR_q, Log_Shifter_r0_out, mux_8bit_1_out_5, r0_q, Temporary_q;
  wire [15:0] address_register_1_addrbus;

  Pull_Resistor #(.pull(1)) pull_resistor_1 (.node(pull_resistor_1_node));
  Pull_Resistor pull_resistor_2 (.node(pull_resistor_2_node));
  Clock clock_1 (.out(clock_1_out));
  Simple_IRQ_Controller IRQ_Controller (
    .nRESET(magic_cu_1_ncli_rst), .nIRQ_CLK(nCLKs[0]), .nIRQ(pull_resistor_1_node),
    .nCLI(magic_cu_1_ncli_rst), .nSEI(magic_cu_1_nsei), .nINT(IRQ_Controller_nint), .nT0(magic_cu_1_nfetching));  // open: INT
  Clock_Generator clock_generator_1 (
    .EXTCLK(clock_1_out), .PHASE(CLKs), .HLT(pull_resistor_2_node), .INVERTED_PHASE(nCLKs));
  // Probe on CLKs
  Magic_CU magic_cu_1 (
    .CLK(CLKs), .nINT(IRQ_Controller_nint), .FLAGS(flag_register_1_flags), .IR(IR_q),
    .nCLI_RST(magic_cu_1_ncli_rst), .nSEI(magic_cu_1_nsei), .IO_MEM_CTRL(magic_cu_1_io_mem_ctrl),
    .ALU_CTRL(magic_cu_1_alu_ctrl), .FLAG_CTRL(magic_cu_1_flag_ctrl), .nSHFT_EN(magic_cu_1_nshft_en),
    .TMP_CTRL(magic_cu_1_tmp_ctrl), .IR_CTRL(magic_cu_1_ir_ctrl), .DECODE_CTRL(magic_cu_1_decode_ctrl),
    .AR_CTRL(magic_cu_1_ar_ctrl), .PC_CTRL(magic_cu_1_pc_ctrl), .SP_CTRL(magic_cu_1_sp_ctrl),
    .nFETCHING(magic_cu_1_nfetching));
  // Probe on IR_q
  _8bit_register IR (.D(DATABUS), .nOE(1'b0), .CLK(and_1_out), .Q(IR_q));
  and and_1 (and_1_out, magic_cu_1_ir_ctrl, CLKs[1]);
  Pull_Resistor pull_resistor_3 (.node(DATABUS));
  Decode Instruction_Decode (
    .IR(IR_q), .OE(magic_cu_1_decode_ctrl[0]), .nSRC_CLKs(nCLKs), .IE(magic_cu_1_decode_ctrl[1]),
    .nOEs(Instruction_Decode_noes), .CLKs(Instruction_Decode_clks), .Cin_EN(Instruction_Decode_cin_en),
    .nr0_OVERRIDE(magic_cu_1_decode_ctrl[2]));
  Log_Shifter Log_Shifter (.r0_IN(r0_q), .DATABUS_IN(DATABUS), .L_R(IR_q[0]), .r0_OUT(Log_Shifter_r0_out));
  _8bit_register r0 (.D(mux_8bit_1_out_5), .nOE(1'b0), .CLK(Instruction_Decode_clks[0]), .Q(r0_q));
  MUX_8bit mux_8bit_1 (
    .A(Log_Shifter_r0_out), .B(DATABUS), .nE(1'b0), .S(magic_cu_1_nshft_en), .out_5(mux_8bit_1_out_5));
  Buffer_tri_state_8bit buffer_tri_state_8bit_1 (.IN(r0_q), .OE(Instruction_Decode_noes[0]), .OUT(DATABUS));
  _8bit_register Temporary (.D(DATABUS), .nOE(1'b0), .CLK(and_2_out), .Q(Temporary_q));
  and and_2 (and_2_out, magic_cu_1_tmp_ctrl, CLKs[1]);
  // Probe on address_register_1_addrbus
  // Probe on r0_q
  // Probe on Temporary_q
  and and_3 (and_3_out, magic_cu_1_ar_ctrl[0], CLKs[1]);
  Address_Register address_register_1 (
    .DATABUS_IN(DATABUS), .ADDRBUS(address_register_1_addrbus), .nOE(magic_cu_1_ar_ctrl[1]), .CLK(and_3_out));
  // Probe on flag_register_1_flags
  // Probe on alu_1_flags_out
  Flag_Register flag_register_1 (
    .DATABUS_IN(DATABUS), .ALU_FLAGS_IN(alu_1_flags_out), .DATABUS_OUT(DATABUS),
    .FLAGS(flag_register_1_flags), .CLK(and_4_out), .ALU__DB(magic_cu_1_flag_ctrl[2]),
    .nDATABUS_OE(magic_cu_1_flag_ctrl[1]));
  and and_4 (and_4_out, CLKs[1], magic_cu_1_flag_ctrl[0]);
  Program_Counter program_counter_1 (
    .DATABUS_OUT(DATABUS), .C_CLK(and_5_out), .ADDRBUS_OUT(address_register_1_addrbus),
    .ADDRBUS_IN(address_register_1_addrbus), .COUNT__PRESET(magic_cu_1_pc_ctrl[1]),
    .nA_OE(magic_cu_1_pc_ctrl[2]), .nH_OE(magic_cu_1_pc_ctrl[4]), .nL_OE(magic_cu_1_pc_ctrl[3]));
  ALU alu_1 (
    .Op(IR_q[2:0]), .A(r0_q), .B(Temporary_q), .out_6(alu_1_out_6), .Flags_in(flag_register_1_flags),
    .Pass_carry(Instruction_Decode_cin_en), .Flags_out(alu_1_flags_out));
  and and_5 (and_5_out, magic_cu_1_pc_ctrl[0], CLKs[2]);
  Buffer_tri_state_8bit buffer_tri_state_8bit_2 (.IN(alu_1_out_6), .OE(magic_cu_1_alu_ctrl), .OUT(DATABUS));
  Stack_Pointer stack_pointer_1 (
    .ADDRBUS_OUT(address_register_1_addrbus), .nA_OE(magic_cu_1_sp_ctrl[3]), .nH_OE(magic_cu_1_sp_ctrl[5]),
    .nL_OE(magic_cu_1_sp_ctrl[4]), .DATABUS_OUT(DATABUS), .ADDRBUS_IN(address_register_1_addrbus),
    .nSP_LD(or_1_out), .nSP_plus_plus(or_2_out), .nSP_minus_minus(or_3_out));
  or or_1 (or_1_out, magic_cu_1_sp_ctrl[2], nCLKs[1]);
  or or_2 (or_2_out, magic_cu_1_sp_ctrl[1], nCLKs[0]);
  and and_6 (and_6_out, magic_cu_1_io_mem_ctrl[1], CLKs[1]);
  GP_Register_Bank gp_register_bank_1 (
    .D(DATABUS), .Q(DATABUS), .DCD_nOEs(Instruction_Decode_noes), .DCD_CLKs(Instruction_Decode_clks));
  // Probe on DATABUS
  or or_3 (or_3_out, magic_cu_1_sp_ctrl[0], nCLKs[2]);
  and and_7 (and_7_out, magic_cu_1_io_mem_ctrl[0], or_4_out);
  or or_4 (or_4_out, and_6_out, magic_cu_1_io_mem_ctrl[3]);
  buf buffer_1 (buffer_1_out, magic_cu_1_io_mem_ctrl[3]);
  buf buffer_2 (buffer_2_out, buffer_1_out);
  RAM #(.addrWidth(16), .bus("asynch")) ram_1 (
    .addr(address_register_1_addrbus), .data(DATABUS), .sel(and_7_out), .ld(buffer_2_out));  // open: clr

  // Notes on the sheet:
  //   Real SRAM simulating logic
  //   This logic is just to simulate real async SRAM
endmodule

module risc_main (
  input  in_1
);

  wire and_1_out, and_2_out, and_3_out, buffer_1_out, buffer_2_out, clock_1_out, CU_nt0, D_CLK, Decode_p5,
       Decode_p6, io_interface_1_w_clk, io_interface_2_re_2, keyboard_1_avail, nIRQ, or_1_out, PC_CLK,
       program_counter_1_p1, simple_irq_controller_1_int, undriven_3;
  wire [0:0] undriven;
  wire [2:0] IR_q;
  wire [3:0] nSRC_CLKS, SRC_CLKS;
  wire [6:0] keyboard_1_data;
  wire [7:0] Accumulator__r0_q, alu_1_flags_out, alu_1_out_6, DATABUS, DC_CLKs, DC_nOEs, FLAGS, TEMP_q;
  wire [7:3] IR_q_2;
  wire [10:0] CTRL;
  wire [13:13] undriven_2;
  wire [14:14] nOEs;
  wire [15:0] ADDRBUS, CU_clk_lines, CU_noe_lines;

  Clock clock_1 (.out(clock_1_out));
  // Clock_Generator clock_generator_1: pin names not known; wires that end beside it: clock_1_out, in_1, CTRL[10], {SRC_CLKS[3], PC_CLK, D_CLK, SRC_CLKS[0]}, nSRC_CLKS
  Pull_Resistor #(.pull(1)) pull_resistor_1 (.node(nIRQ));
  Simple_IRQ_Controller simple_irq_controller_1 (
    .nRESET(CTRL[9]), .nIRQ_CLK(nSRC_CLKS[0]), .nIRQ(nIRQ), .nCLI(CU_noe_lines[12]), .nSEI(CU_noe_lines[13]),
    .INT(simple_irq_controller_1_int), .nT0(CU_nt0));  // open: nINT
  Simple_Control_Unit CU (
    .IR({IR_q_2, IR_q}), .Flags(FLAGS), .nOE_LINES(CU_noe_lines), .CLK_LINES(CU_clk_lines),
    .INT(simple_irq_controller_1_int), .nT0(CU_nt0), .CTRL(CTRL),
    .SRC_CLKs({SRC_CLKS[3], PC_CLK, D_CLK, SRC_CLKS[0]}), .nSRC_CLKs(nSRC_CLKS));  // open: ALUOP, T_state
  Register_8bit IR (.D(DATABUS), .nOE(1'b0), .CLK(CU_clk_lines[12]), .Q({IR_q_2, IR_q}));
  // Decode Decode: pin names not known; wires that end beside it: nSRC_CLKS, {IR_q_2, IR_q}, DC_nOEs, DC_CLKs, Decode_p5, Decode_p6
  Address_Register address_register_1 ();  // open: DATABUS_IN, ADDRBUS, nOE, CLK
  Register_8bit Accumulator__r0 (.D(DATABUS), .nOE(1'b0), .CLK(undriven[0]), .Q(Accumulator__r0_q));
  Buffer_tri_state_8bit buffer_tri_state_8bit_1 (.IN(Accumulator__r0_q), .OE(undriven_3), .OUT(DATABUS));
  Register_8bit TEMP (.D(DATABUS), .nOE(1'b0), .CLK(undriven_2[13]), .Q(TEMP_q));
  // Program_Counter program_counter_1: pin names not known; wires that end beside it: program_counter_1_p1, CU_noe_lines, CTRL, DATABUS, PC_CLK, ADDRBUS, DATABUS
  ALU alu_1 (
    .Op(IR_q), .A(Accumulator__r0_q), .B(TEMP_q), .out_6(alu_1_out_6), .Flags_in(FLAGS),
    .Pass_carry(Decode_p6), .Flags_out(alu_1_flags_out));
  // Flag_Register flag_register_1: pin names not known; wires that end beside it: CU_clk_lines, CU_noe_lines, FLAGS, alu_1_flags_out, DATABUS, DATABUS
  // Stack_Pointer stack_pointer_1: pin names not known; wires that end beside it: CU_clk_lines, DATABUS, CU_noe_lines, DATABUS, CTRL, ADDRBUS
  Buffer_tri_state_8bit buffer_tri_state_8bit_2 (.IN(alu_1_out_6), .OE(CU_noe_lines[0]), .OUT(DATABUS));
  Pull_Resistor pull_resistor_2 (.node(DATABUS));
  and and_1 (and_1_out, CTRL[6], D_CLK);
  // GP_Register_Bank gp_register_bank_1: pin names not known; wires that end beside it: Decode_p5, ADDRBUS, DC_nOEs, DATABUS, DC_CLKs, DATABUS
  or or_1 (or_1_out, and_1_out, CTRL[7]);
  and and_2 (and_2_out, CTRL[8], or_1_out);
  buf buffer_1 (buffer_1_out, CTRL[7]);
  buf buffer_2 (buffer_2_out, buffer_1_out);
  RAM #(.addrWidth(16), .bus("asynch")) ram_1 (
    .addr(ADDRBUS), .data(DATABUS), .sel(and_2_out), .ld(buffer_2_out));  // open: clr
  TTY tty_1 (.data(DATABUS[6:0]), .clk(io_interface_1_w_clk), .we(CTRL[6]));  // open: clr
  IO_interface io_interface_1 (
    .ADDR(8'h1), .ADDRBUS(ADDRBUS), .WE(CTRL[6]), .D_CLK(D_CLK), .RE(CTRL[7]), .IO_M(CTRL[8]),
    .W_CLK(io_interface_1_w_clk));  // open: RE_2
  Keyboard keyboard_1 (
    .clk(and_3_out), .re(io_interface_2_re_2), .avail(keyboard_1_avail), .data(keyboard_1_data));  // open: clr
  IRQ_interface irq_interface_1 (
    .IVECT(8'h4), .INT(keyboard_1_avail), .nINTA(nOEs[14]), .DATABUS(DATABUS), .nIRQ(nIRQ));  // open: nINTA_OUT
  IO_interface io_interface_2 (
    .ADDR(8'h2), .ADDRBUS(ADDRBUS), .WE(CTRL[6]), .D_CLK(D_CLK), .RE(CTRL[7]), .IO_M(CTRL[8]),
    .RE_2(io_interface_2_re_2));  // open: W_CLK
  and and_3 (and_3_out, io_interface_2_re_2, PC_CLK);
  assign DATABUS[6:0] = io_interface_2_re_2 ? keyboard_1_data : 7'bz;  // Controlled_Buffer controlled_buffer_1

  // Other names for the same wires on the sheet: WE = CTRL[6]; RE = CTRL[7]; IO_M = CTRL[8];
  //   SRC_CLKS[2:1] = {PC_CLK, D_CLK}

  // Notes on the sheet:
  //   This logic is just to simulate real async SRAM
endmodule

module main (
  input  [1:0] INT,
  input  in_2,
  input  in_3,
  input  in_4,
  input  in_5,
  input  in_6,
  input  in_7,
  input  in_8,
  input  in_9,
  input  in_10,
  input  in_11,
  input  in_12,
  input  [3:0] in_13,
  input  in_14,
  input  [2:0] in_15,
  input  [15:0] in_16
);

  wire and_1_out, and_2_out, and_3_out, BE0, BE1, BYTE, CLK_IN, CLK_OUT, CONT, DMA, DMA_RE, DMA_WE, F_CLK,
       F_IE, HLT, INT_IE, INTA, INTE, IO__M, IR_CLK, IR_IE, IRQ, MAR_CLK, MAR_IE, nALU_OE, nIMM_L_OE,
       nIMM_R_OE, NORM, not_1_out, not_2_out, not_3_out, not_4_out, not_5_out, not_6_out, nTEMP_L_OE,
       or_1_out, or_2_out, PASS_CARRY, pull_resistor_2_node, pull_resistor_3_node, pull_resistor_4_node, RE,
       REG_CLK, SWAP, WE;
  wire [1:0] IMM, TEMP_L_S;
  wire [2:0] ALU_OP, IE, OE;
  wire [4:0] ALU_F_OUT, FLAGS;
  wire [7:0] decode_1_out_8, decode_1_out_9, INSTRUCTION_H, INSTRUCTION_L, INTM;
  wire [15:0] ADDR, alu_1_p7, DATA, left_bank_1_leftbus, Right_Bus;

  Clock clock_1 (.out(CLK_IN));
  Counter #(.width(32), .max('hffffffff)) counter_1 (.clk(CLK_OUT));  // open: load, D, count, Q, carry, clr
  Control_Unit control_unit_1 (
    .CLK_IN(CLK_IN), .HALT(HLT), .CONT(CONT), .DMA(DMA), .Instruction_L(INSTRUCTION_L), .Flags(FLAGS),
    .Instruction_H(INSTRUCTION_H), .RST_NMI_IRQ({INT, IRQ}), .MAR_0(ADDR[0]), .OE0(OE[0]), .OE1(OE[1]),
    .OE2(OE[2]), .IE0(IE[0]), .IE1(IE[1]), .IE2(IE[2]), .W_IR(IR_IE), .W_MAR(MAR_IE), .OE_ALU(nALU_OE),
    .ALU_0(ALU_OP[0]), .ALU_1(ALU_OP[1]), .ALU_2(ALU_OP[2]), .W_F(F_IE), .R_CARRY(PASS_CARRY),
    .TEMP_L_S0(TEMP_L_S[0]), .TEMP_L_S1(TEMP_L_S[1]), .R_TEMP_L(nTEMP_L_OE), .IO__M(IO__M), .RE(RE), .WE(WE),
    .IMM0(IMM[0]), .IMM1(IMM[1]), .OE_IMM_R(nIMM_R_OE), .OE_IMM_L(nIMM_L_OE), .BYTE(BYTE), .INTA(INTA),
    .INT_IE(INT_IE), .CLK_OUT(CLK_OUT), .BE0(BE0), .BE1(BE1), .NORM(NORM), .SWAP(SWAP));  // open: HLTA, reserved
  DMA_Interface dma_interface_1 (
    .HALT(in_2), .CONT(in_3), .DMA(in_12), .EXEC(in_14), .ACTION(in_13), .INPUT(in_16), .REGSEL(in_15),
    .HALT_2(HLT), .CONT_2(CONT), .DMA_2(DMA), .DATABUS(DATA), .DATA_CLK(DMA_WE), .RE(DMA_RE),
    .ADDR_BUS(ADDR), .REG_CLK(REG_CLK), .OE(OE), .IE(IE));
  Decode_2 decode_1 (
    .CLK(CLK_OUT), .out_8(decode_1_out_8), .out_9(decode_1_out_9), .FLAGS_IE(F_IE), .FLAGS_CLK(F_CLK),
    .INSTRUCTION_CLK(IR_CLK), .INSTRUCTION_IE(IR_IE), .MAR_CLK(MAR_CLK), .MAR_IE(MAR_IE), .DMA_CLK(REG_CLK),
    .OE(OE), .IE(IE));
  Right_Bank right_bank_1 (
    .DATABUS(DATA), .OE_LINES(decode_1_out_8), .CLK_LINES(decode_1_out_9), .RIGHTBUS(Right_Bus), .IMM(IMM),
    .nIMM_R_OE(nIMM_R_OE), .FLAGS_IN(ALU_F_OUT), .FLAGS_OUT(FLAGS), .F_CLK(F_CLK), .INTM(INTM), .INTE(INTE),
    .NORM(NORM), .SWAP(SWAP));
  // Register_8bit register_8bit_1: pin names not known; wires that end beside it: DATA, DMA, IR_CLK, {INSTRUCTION_H, INSTRUCTION_L}
  Left_Bank left_bank_1 (
    .DATABUS(DATA), .nTEMP_OE(nTEMP_L_OE), .IMM(IMM), .nIMM_L_OE(nIMM_L_OE), .LEFTBUS(left_bank_1_leftbus),
    .CLK(CLK_OUT), .S(TEMP_L_S));
  IRQ_Controller irq_controller_1 (
    .INTE(INTE), .IRQ5(in_9), .IRQ4(in_8), .IRQ3(in_7), .IRQ2(in_6), .IRQ1(in_5), .IRQ0(in_4), .IRQ7(in_11),
    .IRQ6(in_10), .INTM(INTM), .INTA(INTA), .INT_IE(INT_IE), .IRQ(IRQ), .DATABUS(DATA));
  // ALU alu_1: pin names not known; wires that end beside it: Right_Bus, left_bank_1_leftbus, ALU_OP, FLAGS[3], PASS_CARRY, ALU_F_OUT, alu_1_p7
  Buffer_tri_state_16bit buffer_tri_state_16bit_1 (.IN(alu_1_p7), .nOE(nALU_OE), .OUT(DATA));
  Pull_Resistor pull_resistor_1 (.node(DATA));
  // Register_8bit register_8bit_2: pin names not known; wires that end beside it: Right_Bus, DMA, MAR_CLK, ADDR
  Pull_Resistor #(.pull(1)) pull_resistor_2 (.node(pull_resistor_2_node));
  Pull_Resistor #(.pull(1)) pull_resistor_3 (.node(pull_resistor_3_node));
  Pull_Resistor #(.pull(1)) pull_resistor_4 (.node(pull_resistor_4_node));
  _7405 u_7405_1 (
    .I0(RE), .I1(DMA_RE), .I2(BE0), .I3(DMA_WE), .I4(BE1), .I5(DMA_WE), .O0(pull_resistor_2_node),
    .O1(pull_resistor_2_node), .O2(pull_resistor_3_node), .O3(pull_resistor_3_node),
    .O4(pull_resistor_4_node), .O5(pull_resistor_4_node));
  not not_1 (not_1_out, pull_resistor_3_node);
  not not_2 (not_2_out, pull_resistor_2_node);
  not not_3 (not_3_out, pull_resistor_4_node);
  not not_4 (not_4_out, pull_resistor_2_node);
  TTY tty_1 (.data(DATA[6:0]), .clk(CLK_OUT), .we(and_1_out));  // open: clr
  and and_1 (and_1_out, IO__M, WE);
  not not_5 (not_5_out, IO__M);
  or or_1 (or_1_out, not_1_out, not_2_out);
  not not_6 (not_6_out, IO__M);
  or or_2 (or_2_out, not_3_out, not_4_out);
  and and_2 (and_2_out, not_5_out, or_1_out);
  and and_3 (and_3_out, not_6_out, or_2_out);
  RAM #(.addrWidth(15), .bus("asynch")) ram_1 (
    .addr(ADDR[15:1]), .data(DATA[7:0]), .sel(and_2_out), .ld(not_2_out));  // open: clr
  RAM #(.addrWidth(15), .bus("asynch")) ram_2 (
    .addr(ADDR[15:1]), .data(DATA[15:8]), .sel(and_3_out), .ld(not_4_out));  // open: clr

  // Other names for the same wires on the sheet: MAR_0 = ADDR[0]

  // Notes on the sheet:
  //   Perform write cycles in two clocks? keep data on bus on the second cycle to ensure data is written
  //   This logic is just to simulate real async SRAM
endmodule

module ALU (
  input  [2:0] Op,
  input  [7:0] Flags_in,
  input  Pass_carry,
  input  [7:0] A,
  input  [7:0] B,
  output [7:0] out_6,
  output [7:0] Flags_out
);

  wire and_1_out, nand_1_out, nor_1_out, nor_2_out, xor_1_out;

  // Probe on A
  // Probe on B
  nand nand_1 (nand_1_out, Op[0], Op[1]);
  and and_1 (and_1_out, Flags_in[3], Pass_carry);
  xor xor_1 (xor_1_out, and_1_out, nand_1_out);
  Am25LS2517 am25ls2517_1 (
    .Cn(xor_1_out), .A(A[3:0]), .B(B[3:0]), .Cn_4(Flags_out[4]), .Out(out_6[3:0]), .Op(Op));  // open: OVR
  Am25LS2517 am25ls2517_2 (
    .Cn(Flags_out[4]), .A(A[7:4]), .B(B[7:4]), .Cn_4(Flags_out[3]), .OVR(Flags_out[2]),
    .Out({Flags_out[0], out_6[6:4]}), .Op(Op));
  nor nor_1 (nor_1_out, out_6[0], out_6[1], out_6[2], out_6[3]);
  nor nor_2 (nor_2_out, out_6[4], out_6[5], out_6[6], Flags_out[0]);
  and and_2 (Flags_out[1], nor_2_out, nor_1_out);
  // Probe on {Flags_out[0], out_6[6:0]}

  assign Flags_out[7:5] = 3'b000;
  assign out_6[7] = Flags_out[0];

  // Notes on the sheet:
  //   Flags: A, C, V, Z, S
endmodule

module Magic_CU (
  input  [3:0] CLK,
  input  nINT,
  input  [7:0] FLAGS,
  input  [7:0] IR,
  output nCLI_RST,
  output nSEI,
  output [3:0] IO_MEM_CTRL,
  output ALU_CTRL,
  output [2:0] FLAG_CTRL,
  output nSHFT_EN,
  output TMP_CTRL,
  output IR_CTRL,
  output [2:0] DECODE_CTRL,
  output [1:0] AR_CTRL,
  output [4:0] PC_CTRL,
  output [5:0] SP_CTRL,
  output nFETCHING
);

  wire bus_to_8bit_1_out_2, bus_to_8bit_1_out_3, bus_to_8bit_1_out_4, bus_to_8bit_1_out_5,
       bus_to_8bit_1_out_6, bus_to_8bit_1_out_7, bus_to_8bit_1_out_8, bus_to_8bit_1_out_9,
       n7474_dual_d_ffs_1_q1_2, n74151_1_y, n74151_1_y_2, n74151_2_y, nand_2_out, nBRANCH_EN, nBRANCH_RST,
       nHLT, or_1_out;
  wire [3:0] n74148_1_g5__14;
  wire [7:0] buffer_tri_state_8bit_1_out, Current_q, rom_5_data;
  wire [8:8] nand_1_out;

  _7474_Dual_D_FFs u_7474_dual_d_ffs_1 (
    .PRE1(nBRANCH_EN), .CLR1(nBRANCH_RST), .CLK1(1'b0), .D1(1'b0), .PRE2(1'b1), .CLR2(1'b1), .CLK2(1'b0),
    .D2(1'b0), .Q1_2(n7474_dual_d_ffs_1_q1_2));  // open: Q1, Q2, Q2_2
  bus_to_8bit bus_to_8bit_1 (
    .in_1(FLAGS), .out_2(bus_to_8bit_1_out_2), .out_3(bus_to_8bit_1_out_3), .out_4(bus_to_8bit_1_out_4),
    .out_5(bus_to_8bit_1_out_5), .out_6(bus_to_8bit_1_out_6), .out_7(bus_to_8bit_1_out_7),
    .out_8(bus_to_8bit_1_out_8), .out_9(bus_to_8bit_1_out_9));
  or or_1 (or_1_out, n7474_dual_d_ffs_1_q1_2, n74151_2_y);
  _74151 u_74151_1 (
    .I0(bus_to_8bit_1_out_2), .I1(bus_to_8bit_1_out_3), .I2(bus_to_8bit_1_out_4), .I3(bus_to_8bit_1_out_5),
    .I4(bus_to_8bit_1_out_6), .I5(bus_to_8bit_1_out_7), .I6(bus_to_8bit_1_out_8), .I7(bus_to_8bit_1_out_9),
    .Y(n74151_1_y), .Y_2(n74151_1_y_2), .S0(IR[0]), .S1(IR[1]), .S2(IR[2]), .E(1'b0));
  _74148 u_74148_1 (
    ._0__10(1'b1), ._1__11(1'b1), ._2__12(n7474_dual_d_ffs_1_q1_2), ._3__13(1'b1), ._4__1(or_1_out),
    ._5__2(1'b1), ._6__3(1'b1), ._7__4(nINT), .EI__5(1'b0), .G5__14(n74148_1_g5__14[0]),
    .A0__9(n74148_1_g5__14[1]), .A1__7(n74148_1_g5__14[2]), .A2__6(n74148_1_g5__14[3]));  // open: EO__15
  _74151 u_74151_2 (
    .I0(n74151_1_y_2), .I1(n74151_1_y), .I2(1'b0), .I3(1'b0), .I4(1'b0), .I5(1'b0), .I6(1'b0), .I7(1'b0),
    .Y(n74151_2_y), .S0(IR[4]), .S1(1'b0), .S2(1'b0), .E(1'b0));  // open: Y_2
  // Probe on {4'b0000, n74148_1_g5__14}
  // Probe on buffer_tri_state_8bit_1_out
  Buffer_tri_state_8bit buffer_tri_state_8bit_1 (
    .IN({4'b0000, n74148_1_g5__14}), .OE(nFETCHING), .OUT(buffer_tri_state_8bit_1_out));
  Buffer_tri_state_8bit buffer_tri_state_8bit_2 (.IN(IR), .OE(nand_1_out[8]), .OUT(buffer_tri_state_8bit_1_out));
  nand nand_1 (nand_1_out[8], Current_q[0], Current_q[1], Current_q[2], Current_q[3], Current_q[4], Current_q[5], Current_q[6], Current_q[7]);
  or or_2 (nFETCHING, Current_q[0], Current_q[1], Current_q[2], Current_q[3], Current_q[4], Current_q[5], Current_q[6], Current_q[7]);
  ROM #(.addrWidth(9)) rom_1 (
    .addr({nand_1_out[8], buffer_tri_state_8bit_1_out}),
    .data({nBRANCH_EN, nHLT, nCLI_RST, nSEI, IO_MEM_CTRL}));  // open: sel
  ROM #(.addrWidth(9)) rom_2 (
    .addr({nand_1_out[8], buffer_tri_state_8bit_1_out}),
    .data({ALU_CTRL, FLAG_CTRL, nSHFT_EN, nBRANCH_RST, TMP_CTRL, IR_CTRL}));  // open: sel
  ROM #(.addrWidth(9)) rom_3 (
    .addr({nand_1_out[8], buffer_tri_state_8bit_1_out}), .data({DECODE_CTRL, AR_CTRL, PC_CTRL[4:2]}));  // open: sel
  ROM #(.addrWidth(9)) rom_4 (
    .addr({nand_1_out[8], buffer_tri_state_8bit_1_out}), .data({PC_CTRL[1:0], SP_CTRL}));  // open: sel
  ROM #(.addrWidth(9)) rom_5 (.addr({nand_1_out[8], buffer_tri_state_8bit_1_out}), .data(rom_5_data));  // open: sel
  // Probe on Current_q
  Register_8bit Current (.D(rom_5_data), .nOE(1'b0), .CLK(CLK[3]), .Q(Current_q));
  nand nand_2 (nand_2_out, nFETCHING, nand_1_out[8]);
  Buffer_tri_state_8bit buffer_tri_state_8bit_3 (.IN(Current_q), .OE(nand_2_out), .OUT(buffer_tri_state_8bit_1_out));

  // Other names for the same wires on the sheet: NEXT_T_CLK = CLK[3]

  // Notes on the sheet:
  //   Flags: A, C, V, Z, S
  //   IRQ ACK: when fetch && CLKs=IRQ latch
  //   clks: 0 irq, 1 data, 2 postinc, 3 nextT
  //   /BRANCH MISS
  //   /BRANCH HIT
  //   00: encoder 1xx
  //   ff: IR 0xx
  //   else: next 1xx
  //   Next
  //   contents of rom_1 (hex, n*v repeats v):
  //   8*f1 5*71 f9 f9 f9 5*71 11*f1 8*f9 222*f1 f9 8*f1 f9 f1 f9 f3 f3 f1 f9 f9 233*f1
  //   contents of rom_2 (hex, n*v repeats v):
  //   130*ec 5*ee ec ec ec 5*ee ec ec ec 5*ee ec ec ec 5*ee ec ec ec 5*ee ec ec ec 5*ee ec ec ec 5*ee ec
  //   ec ec 5*ee ec ec ec ee ee e4 e4 4*ec ee ee e4 e4 4*ec ee ee e4 e4 4*ec ee ee e4 e4 4*ec ee ee e4 e4
  //   4*ec ee ee e4 e4 4*ec ee ee e4 e4 4*ec ee ee e4 e4 13*ec e8 ec ec ec ed 6*ec e8 7c 232*ec
  //   contents of rom_3 (hex, n*v repeats v):
  //   13*97 9e 9f 9e 16*97 8*d6 24*97 64*f7 97 97 5*b7 97 97 97 5*b7 97 97 97 5*b7 97 97 97 5*b7 97 97 97
  //   5*b7 97 97 97 5*b7 97 97 97 5*b7 97 97 97 5*b7 97 97 97 b7 b7 77 77 4*97 b7 b7 77 77 4*97 b7 b7 77
  //   77 4*97 b7 b7 77 77 4*97 b7 b7 77 77 4*97 b7 b7 77 77 4*97 b7 b7 77 77 4*97 b7 b7 77 77 8*97 9e 8*97
  //   96 87 9e 93 95 97 9f 9e 57 232*97
  //   contents of rom_4 (hex, n*v repeats v):
  //   13*bf ff b5 ff 16*bf 8*ff 222*bf ff bf bf bf ff ff bf bf bf ff 7f ff b6 b6 bf b5 ff 233*bf
  //   contents of rom_5 (hex, n*v repeats v):
  //   13*0 11 15 16 114*0 5*17 0 0 0 5*17 0 0 0 5*17 0 0 0 5*17 0 0 0 5*17 0 0 0 5*17 0 0 0 5*17 0 0 0
  //   5*17 0 0 0 17 17 6*0 17 17 6*0 17 17 6*0 17 17 6*0 17 17 6*0 17 17 6*0 17 17 6*0 17 17 10*0 16 0 0 0
  //   b 4*0 ff 0 12 13 10 0 10 10
endmodule

module Orthogonal_CU (
  input  [3:0] CLKs,
  input  [7:0] IR,
  output PC_C__P,
  output F_ALU__DB_SEL,
  output IO_M,
  output WE,
  output RE,
  output AR_A_OE,
  output SP_A_OE,
  output PC_A_OE,
  output OE,
  output IE,
  output RESET,
  output [7:0] DBUS_OEs,
  output [7:0] CLKs_2,
  output [7:0] CLKs_3
);

  wire bus_to_8bit_1_out_2, bus_to_8bit_1_out_3, bus_to_8bit_1_out_4, bus_to_8bit_1_out_5,
       bus_to_8bit_1_out_6, bus_to_8bit_1_out_7, bus_to_8bit_1_out_8, bus_to_8bit_1_out_9, Clocked_2_y0,
       Clocked_2_y1, Clocked_2_y2, Clocked_2_y3, Clocked_2_y4, Clocked_2_y5, Clocked_2_y6, Clocked_2_y7,
       Clocked_y0, Clocked_y1, Clocked_y2, Clocked_y3, Clocked_y4, Clocked_y5, Clocked_y6, Clocked_y7,
       DBUS_OE_y0, DBUS_OE_y1, DBUS_OE_y2, DBUS_OE_y3, DBUS_OE_y4, DBUS_OE_y5, DBUS_OE_y6, DBUS_OE_y7;
  wire [3:0] n74161_1_q0;
  wire [7:0] rom_1_data, rom_2_data, rom_3_data, rom_4_data;

  _74161 u_74161_1 (
    .CET(1'b1), .CEP(1'b1), .PE(1'b1), .CLK(CLKs[3]), .MR(1'b1), .D0(1'b1), .D1(1'b1), .D2(1'b1), .D3(1'b1),
    .Q0(n74161_1_q0[0]), .Q1(n74161_1_q0[1]), .Q2(n74161_1_q0[2]), .Q3(n74161_1_q0[3]));  // open: TC
  ROM rom_1 (.addr(IR), .data(rom_1_data));  // open: sel
  Pull_Resistor pull_resistor_1 (.node(rom_1_data[3:0]));
  ROM rom_2 (.addr({rom_1_data[3:0], n74161_1_q0}), .data(rom_2_data));  // open: sel
  ROM rom_3 (.addr({rom_1_data[3:0], n74161_1_q0}), .data(rom_3_data));  // open: sel
  ROM rom_4 (.addr({rom_1_data[3:0], n74161_1_q0}), .data(rom_4_data));  // open: sel
  bus_to_8bit bus_to_8bit_1 (
    .in_1(rom_4_data), .out_2(bus_to_8bit_1_out_2), .out_3(bus_to_8bit_1_out_3), .out_4(bus_to_8bit_1_out_4),
    .out_5(bus_to_8bit_1_out_5), .out_6(bus_to_8bit_1_out_6), .out_7(bus_to_8bit_1_out_7),
    .out_8(bus_to_8bit_1_out_8), .out_9(bus_to_8bit_1_out_9));
  _74138 DBUS_OE (
    .nE1(bus_to_8bit_1_out_5), .nE2(1'b0), .E3(1'b1), .A0(bus_to_8bit_1_out_2), .A1(bus_to_8bit_1_out_3),
    .A2(bus_to_8bit_1_out_4), .Y0(DBUS_OE_y0), .Y1(DBUS_OE_y1), .Y2(DBUS_OE_y2), .Y3(DBUS_OE_y3),
    .Y4(DBUS_OE_y4), .Y5(DBUS_OE_y5), .Y6(DBUS_OE_y6), .Y7(DBUS_OE_y7));
  _74238 Clocked (
    .A0(bus_to_8bit_1_out_6), .A1(bus_to_8bit_1_out_7), .A2(bus_to_8bit_1_out_8), .nE1(bus_to_8bit_1_out_9),
    .nE2(1'b0), .E3(CLKs[1]), .Y0(Clocked_y0), .Y1(Clocked_y1), .Y2(Clocked_y2), .Y3(Clocked_y3),
    .Y4(Clocked_y4), .Y5(Clocked_y5), .Y6(Clocked_y6), .Y7(Clocked_y7));
  _74138 Clocked_2 (
    .nE1(bus_to_8bit_1_out_9), .nE2(1'b0), .E3(CLKs[1]), .A0(bus_to_8bit_1_out_6), .A1(bus_to_8bit_1_out_7),
    .A2(bus_to_8bit_1_out_8), .Y0(Clocked_2_y0), .Y1(Clocked_2_y1), .Y2(Clocked_2_y2), .Y3(Clocked_2_y3),
    .Y4(Clocked_2_y4), .Y5(Clocked_2_y5), .Y6(Clocked_2_y6), .Y7(Clocked_2_y7));
  bus_to_8bit bus_to_8bit_2 (
    .in_1(rom_2_data), .out_2(PC_C__P), .out_3(F_ALU__DB_SEL), .out_4(IO_M), .out_5(WE), .out_6(RE),
    .out_7(AR_A_OE), .out_8(SP_A_OE), .out_9(PC_A_OE));
  bus_to_8bit bus_to_8bit_3 (
    .in_1(rom_3_data), .out_2(OE), .out_3(IE), .out_4(RESET));  // open: out_5, out_6, out_7, out_8, out_9
  _8bit_to_bus u_8bit_to_bus_1 (
    .in_1(DBUS_OE_y0), .in_2(DBUS_OE_y1), .in_3(DBUS_OE_y2), .in_4(DBUS_OE_y3), .in_5(DBUS_OE_y4),
    .in_6(DBUS_OE_y5), .in_7(DBUS_OE_y6), .in_8(DBUS_OE_y7), .out_9(DBUS_OEs));
  _8bit_to_bus u_8bit_to_bus_2 (
    .in_1(Clocked_y0), .in_2(Clocked_y1), .in_3(Clocked_y2), .in_4(Clocked_y3), .in_5(Clocked_y4),
    .in_6(Clocked_y5), .in_7(Clocked_y6), .in_8(Clocked_y7), .out_9(CLKs_2));
  _8bit_to_bus u_8bit_to_bus_3 (
    .in_1(Clocked_2_y0), .in_2(Clocked_2_y1), .in_3(Clocked_2_y2), .in_4(Clocked_2_y3), .in_5(Clocked_2_y4),
    .in_6(Clocked_2_y5), .in_7(Clocked_2_y6), .in_8(Clocked_2_y7), .out_9(CLKs_3));

  // Notes on the sheet:
  //   clks: 0 irq, 1 data, 2 postinc, 3 nextT
  //   interrupt = flags push then call? reti = ret -> pop flags?. No: up to programmer to follow convention. IRQ=>CLI, RETI=SEI+RET
  //   etc
  //   conditional branch indicator
  //   PC
  //   #SP P
  //   #SP U
  //   #SP D
  //   AR
  //   IR
  //   FLAGS
  //   TMP
  //   /PC H OE -> DATABUS
  //   /PC L OE -> DATABUS
  //   /SP H OE -> DATABUS
  //   /SP L OE -> DATABUS
  //   /F OE -> DATABUS
  //   /ALU OE -> DATABUS
endmodule

module Decode (
  input  [7:0] IR,
  input  OE,
  input  nr0_OVERRIDE,
  input  [3:0] nSRC_CLKs,
  input  IE,
  output Cin_EN,
  output [7:0] nOEs,
  output [7:0] CLKs
);

  wire and_1_out, and_2_out, and_3_out;

  and and_1 (and_1_out, IR[0], nr0_OVERRIDE);
  and and_2 (and_2_out, IR[1], nr0_OVERRIDE);
  and and_3 (and_3_out, IR[2], nr0_OVERRIDE);
  _74138 u_74138_1 (
    .nE1(1'b0), .nE2(1'b0), .E3(OE), .A0(IR[3]), .A1(IR[4]), .A2(IR[5]), .Y0(nOEs[0]), .Y1(nOEs[1]),
    .Y2(nOEs[2]), .Y3(nOEs[3]), .Y4(nOEs[4]), .Y5(nOEs[5]), .Y6(nOEs[6]), .Y7(nOEs[7]));
  _74238 u_74238_1 (
    .A0(and_1_out), .A1(and_2_out), .A2(and_3_out), .nE1(nSRC_CLKs[1]), .nE2(1'b0), .E3(IE), .Y0(CLKs[0]),
    .Y1(CLKs[1]), .Y2(CLKs[2]), .Y3(CLKs[3]), .Y4(CLKs[4]), .Y5(CLKs[5]), .Y6(CLKs[6]), .Y7(CLKs[7]));
  and and_4 (Cin_EN, IR[6], IR[7]);

  // Notes on the sheet:
  //   use the rest of the AND gates; total: 1 chip
endmodule

module Simple_Control_Unit (
  input  [7:0] Flags,
  input  [7:0] IR,
  input  INT,
  input  [3:0] SRC_CLKs,
  input  [3:0] nSRC_CLKs,
  output [3:0] T_state,
  output nT0,
  output [10:0] CTRL,
  output [3:0] ALUOP,
  output [15:0] nOE_LINES,
  output [15:0] CLK_LINES
);

  wire BRANCH_HIT, bus_to_8bit_1_out_2, bus_to_8bit_1_out_3, bus_to_8bit_1_out_4, bus_to_8bit_1_out_5,
       bus_to_8bit_1_out_6, bus_to_8bit_1_out_7, bus_to_8bit_1_out_8, bus_to_8bit_1_out_9, C_CLK, D_CLK,
       n74138_1_y0, n74138_1_y1, n74138_1_y2, n74138_1_y3, n74138_1_y4, n74138_1_y5, n74138_1_y6,
       n74138_1_y7, n74138_2_y0, n74138_2_y1, n74138_2_y2, n74138_2_y3, n74138_2_y4, n74138_2_y5,
       n74138_2_y6, n74138_2_y7, n74238_1_y0, n74238_1_y1, n74238_1_y2, n74238_1_y3, n74238_1_y4,
       n74238_1_y5, n74238_1_y6, n74238_1_y7, n74238_2_y1, n74238_2_y4, n74238_2_y5, n74238_2_y6,
       n74238_2_y7, n74238_3_y0, n74238_3_y2, n74238_3_y3, \nCOND_µJMP , or_1_out, T_CLK;
  wire [7:0] buffer_tri_state_8bit_1_out, rom_3_data;

  bus_to_8bit bus_to_8bit_1 (
    .in_1(Flags), .out_2(bus_to_8bit_1_out_2), .out_3(bus_to_8bit_1_out_3), .out_4(bus_to_8bit_1_out_4),
    .out_5(bus_to_8bit_1_out_5), .out_6(bus_to_8bit_1_out_6), .out_7(bus_to_8bit_1_out_7),
    .out_8(bus_to_8bit_1_out_8), .out_9(bus_to_8bit_1_out_9));
  _74161 counter (
    .CET(1'b1), .CEP(1'b1), .PE(or_1_out), .CLK(T_CLK), .MR(CTRL[9]), .D0(1'b1), .D1(1'b0), .D2(1'b1),
    .D3(1'b0), .Q0(T_state[0]), .Q1(T_state[1]), .Q2(T_state[2]));  // open: Q3, TC
  or or_1 (or_1_out, \nCOND_µJMP , BRANCH_HIT);
  _74151 u_74151_1 (
    .I0(bus_to_8bit_1_out_2), .I1(bus_to_8bit_1_out_3), .I2(bus_to_8bit_1_out_4), .I3(bus_to_8bit_1_out_5),
    .I4(bus_to_8bit_1_out_6), .I5(bus_to_8bit_1_out_7), .I6(bus_to_8bit_1_out_8), .I7(bus_to_8bit_1_out_9),
    .Y(BRANCH_HIT), .S0(IR[0]), .S1(IR[1]), .S2(IR[2]), .E(\nCOND_µJMP ));  // open: Y_2
  bus_to_8bit bus_to_8bit_2 (
    .in_1({nSRC_CLKs, SRC_CLKs}), .out_5(T_CLK), .out_7(D_CLK), .out_8(C_CLK));  // open: out_2, out_3, out_4, out_6, out_9
  Buffer_tri_state_8bit buffer_tri_state_8bit_1 (.IN(IR), .OE(INT), .OUT(buffer_tri_state_8bit_1_out));
  Pull_Resistor #(.pull(1)) pull_resistor_1 (.node(buffer_tri_state_8bit_1_out));
  or or_2 (nT0, T_state[0], T_state[1], T_state[2]);
  ROM #(.addrWidth(11)) rom_1 (.addr({buffer_tri_state_8bit_1_out, T_state[2:0]}), .data(CTRL[7:0]));  // open: sel
  ROM #(.addrWidth(11)) rom_2 (
    .addr({buffer_tri_state_8bit_1_out, T_state[2:0]}), .data({ALUOP, CTRL[10:8], \nCOND_µJMP }));  // open: sel
  ROM #(.addrWidth(11)) rom_3 (.addr({buffer_tri_state_8bit_1_out, T_state[2:0]}), .data(rom_3_data));  // open: sel
  _74138 u_74138_1 (
    .nE1(1'b0), .nE2(rom_3_data[3]), .E3(1'b1), .A0(rom_3_data[0]), .A1(rom_3_data[1]), .A2(rom_3_data[2]),
    .Y0(n74138_1_y0), .Y1(n74138_1_y1), .Y2(n74138_1_y2), .Y3(n74138_1_y3), .Y4(n74138_1_y4),
    .Y5(n74138_1_y5), .Y6(n74138_1_y6), .Y7(n74138_1_y7));
  _74138 u_74138_2 (
    .nE1(1'b0), .nE2(1'b0), .E3(rom_3_data[3]), .A0(rom_3_data[0]), .A1(rom_3_data[1]), .A2(rom_3_data[2]),
    .Y0(n74138_2_y0), .Y1(n74138_2_y1), .Y2(n74138_2_y2), .Y3(n74138_2_y3), .Y4(n74138_2_y4),
    .Y5(n74138_2_y5), .Y6(n74138_2_y6), .Y7(n74138_2_y7));
  _74238 u_74238_1 (
    .A0(rom_3_data[4]), .A1(rom_3_data[5]), .A2(rom_3_data[6]), .nE1(rom_3_data[7]), .nE2(D_CLK), .E3(1'b1),
    .Y0(n74238_1_y0), .Y1(n74238_1_y1), .Y2(n74238_1_y2), .Y3(n74238_1_y3), .Y4(n74238_1_y4),
    .Y5(n74238_1_y5), .Y6(n74238_1_y6), .Y7(n74238_1_y7));
  _74238 u_74238_2 (
    .A0(rom_3_data[4]), .A1(rom_3_data[5]), .A2(rom_3_data[6]), .nE1(D_CLK), .nE2(1'b0), .E3(rom_3_data[7]),
    .Y1(n74238_2_y1), .Y4(n74238_2_y4), .Y5(n74238_2_y5), .Y6(n74238_2_y6), .Y7(n74238_2_y7));  // open: Y0, Y2, Y3
  _74238 u_74238_3 (
    .A0(rom_3_data[4]), .A1(rom_3_data[5]), .A2(rom_3_data[6]), .nE1(C_CLK), .nE2(1'b0), .E3(rom_3_data[7]),
    .Y0(n74238_3_y0), .Y2(n74238_3_y2), .Y3(n74238_3_y3));  // open: Y1, Y4, Y5, Y6, Y7
  _8bit_to_bus u_8bit_to_bus_1 (
    .in_1(n74138_1_y0), .in_2(n74138_1_y1), .in_3(n74138_1_y2), .in_4(n74138_1_y3), .in_5(n74138_1_y4),
    .in_6(n74138_1_y5), .in_7(n74138_1_y6), .in_8(n74138_1_y7), .out_9(nOE_LINES[7:0]));
  _8bit_to_bus u_8bit_to_bus_2 (
    .in_1(n74138_2_y0), .in_2(n74138_2_y1), .in_3(n74138_2_y2), .in_4(n74138_2_y3), .in_5(n74138_2_y4),
    .in_6(n74138_2_y5), .in_7(n74138_2_y6), .in_8(n74138_2_y7), .out_9(nOE_LINES[15:8]));
  _8bit_to_bus u_8bit_to_bus_3 (
    .in_1(n74238_1_y0), .in_2(n74238_1_y1), .in_3(n74238_1_y2), .in_4(n74238_1_y3), .in_5(n74238_1_y4),
    .in_6(n74238_1_y5), .in_7(n74238_1_y6), .in_8(n74238_1_y7), .out_9(CLK_LINES[7:0]));
  _8bit_to_bus u_8bit_to_bus_4 (
    .in_1(n74238_3_y0), .in_2(n74238_2_y1), .in_3(n74238_3_y2), .in_4(n74238_3_y3), .in_5(n74238_2_y4),
    .in_6(n74238_2_y5), .in_7(n74238_2_y6), .in_8(n74238_2_y7), .out_9(CLK_LINES[15:8]));

  assign T_state[3] = 1'b0;

  // Other names for the same wires on the sheet: nRESET = CTRL[9]; NEGATE = IR[4]

  // Notes on the sheet:
  //   pull towards IRQ handler
  //   contents of rom_1 (hex, n*v repeats v):
  //   bb 7*1f bb 7*1f bb 7*1f bb 7*1f bb 1f bb 93 4*1f bb 1f bb 52 4*1f bb 1f 97 1f 87 11*1f bb 1f bb 8b
  //   1f 3f 3f 1f bb 1f bb 8b 1f 3f 3f 1f bb 1f bb 8b 1f 3f 3f 1f bb 1f bb 8b 1f 3f 3f 1f bb 1f bb 8b 1f
  //   3f 3f 1f bb bb 8b 5*1f bb 57 57 bb 8b 1f 1f 1f bb 1f 97 1f 87 3f 3f 41*1f bb 1e 6*1f bb 1e 6*1f bb
  //   1e 6*1f bb 1e 6*1f bb 1e 6*1f bb 1e 6*1f bb 1f 1d 5*1f bb 1f 1d 5*1f bb 1f 1d 5*1f bb 1f 1d 5*1f bb
  //   1f 1d 5*1f bb 1f 1d 197*1f bb bb 6*1f bb bb 6*1f bb bb 6*1f bb bb 6*1f bb bb 6*1f bb bb 6*1f bb bb
  //   6*1f bb bb bb 93 52*1f bb 1f 1f 93 44*1f bb bb bb 52 404*1f bb 1e 1c 1c 4*1f bb 1f 1c 1c 4*1f bb 1f
  //   1c 1c 996*1f 57 57 1f f 4*1f
  //   contents of rom_2 (hex, n*v repeats v):
  //   f b 7*f 7 b 8*f b 7*f b 7*f d b 6*f 8d b 8*f b 11*f e f f b f f b f e f f b f f b f e f f b f f b f
  //   e f f b f f b f e f f b f f b f f f b 9*f b 9*f b 41*f 8f b 6*f 8f b 6*f 8f b 6*f 8f b 6*f 8f b 6*f
  //   8f b 7*f 8f b 6*f 8f b 6*f 8f b 6*f 8f b 6*f 8f b 6*f 8f b 198*f b 7*f b 7*f b 7*f b 7*f b 7*f b 7*f
  //   b 9*f b 55*f b 46*f 8f b 404*f 8f 6f 6f b 5*f 6f 6f b 5*f 6f 6f b 999*f b f f f
  //   contents of rom_3 (hex, n*v repeats v):
  //   cf 7*ff cf 7*ff cf fc 6*ff cf fd 6*ff cf 9f ef f 4*ff cf 9f ef f0 4*ff cf af 9f af fd 11*ff cf ff 9f
  //   5*ff cf ff 9f 5*ff cf ff 9f 5*ff cf ff 9f 5*ff cf ff 9f 5*ff cf 9f 6*ff cf 8a 89 9f 4*ff cf af 9f af
  //   44*ff cf 10 6*ff cf 20 6*ff cf 30 6*ff cf 40 6*ff cf 50 6*ff cf 60 6*ff cf d1 0 5*ff cf d1 20 5*ff
  //   cf d1 30 5*ff cf d1 40 5*ff cf d1 50 5*ff cf d1 60 197*ff cf f 6*ff cf 1f 6*ff cf 2f 6*ff cf 3f 6*ff
  //   cf 4f 6*ff cf 5f 6*ff cf 6f 6*ff cf 9f ef f 52*ff cf 91 e2 f 44*ff cf 9f ef f0 404*ff cf d0 7f 0
  //   4*ff cf d1 7f 0 4*ff cf d2 7f 0 996*ff 8a 89 9c fe 4*ff
  //   0: ALU
  //   1-6: GP REGs
  //   7: FLAGS SEL
  //   8: FLAGS DBUS
  //   9: PC H
  //   A: PC L
  //   B: SP DBUS
  //   C: CLI
  //   D: SEI
  //   E: INTA
  //   0-6: GP REGs
  //   7: FLAGS
  //   8: SP D
  //   9: AR H
  //   A: SP U
  //   B: SP LOAD
  //   C: IR
  //   D: TMP
  //   E: AR L
endmodule

module GP_Register_Bank (
  input  [7:0] D,
  input  [7:0] DCD_nOEs,
  input  [7:0] DCD_CLKs,
  output [7:0] Q
);

  Register_8bit register_8bit_1 (.D(D), .nOE(DCD_nOEs[1]), .CLK(DCD_CLKs[1]), .Q(Q));
  Register_8bit register_8bit_2 (.D(D), .nOE(DCD_nOEs[2]), .CLK(DCD_CLKs[2]), .Q(Q));
  Register_8bit register_8bit_3 (.D(D), .nOE(DCD_nOEs[3]), .CLK(DCD_CLKs[3]), .Q(Q));
  Register_8bit register_8bit_4 (.D(D), .nOE(DCD_nOEs[4]), .CLK(DCD_CLKs[4]), .Q(Q));
  Register_8bit register_8bit_5 (.D(D), .nOE(DCD_nOEs[5]), .CLK(DCD_CLKs[5]), .Q(Q));
  Register_8bit register_8bit_6 (.D(D), .nOE(DCD_nOEs[6]), .CLK(DCD_CLKs[6]), .Q(Q));
  Register_8bit register_8bit_7 (.D(D), .nOE(DCD_nOEs[7]), .CLK(DCD_CLKs[7]), .Q(Q));
endmodule

module Program_Counter (
  input  nH_OE,
  input  nL_OE,
  input  [15:0] ADDRBUS_IN,
  input  COUNT__PRESET,
  input  C_CLK,
  input  nA_OE,
  output [7:0] DATABUS_OUT,
  output [15:0] ADDRBUS_OUT
);

  wire PC_L_tc;
  wire [7:0] PC_H_q, PC_L_q;

  _8bit_Counter_Register PC_H (
    .Count_Enable(PC_L_tc), .D(ADDRBUS_IN[15:8]), .nPreset(COUNT__PRESET), .nClear(1'b1), .CLK(C_CLK),
    .Q(PC_H_q));  // open: TC
  _8bit_Counter_Register PC_L (
    .Count_Enable(COUNT__PRESET), .D(ADDRBUS_IN[7:0]), .nPreset(COUNT__PRESET), .nClear(1'b1), .CLK(C_CLK),
    .Q(PC_L_q), .TC(PC_L_tc));
  Buffer_tri_state_8bit buffer_tri_state_8bit_1 (.IN(PC_H_q), .OE(nH_OE), .OUT(DATABUS_OUT));
  Buffer_tri_state_8bit buffer_tri_state_8bit_2 (.IN(PC_L_q), .OE(nL_OE), .OUT(DATABUS_OUT));
  Buffer_tri_state_8bit buffer_tri_state_8bit_3 (.IN(PC_H_q), .OE(nA_OE), .OUT(ADDRBUS_OUT[15:8]));
  Buffer_tri_state_8bit buffer_tri_state_8bit_4 (.IN(PC_L_q), .OE(nA_OE), .OUT(ADDRBUS_OUT[7:0]));
endmodule

module Stack_Pointer (
  input  nH_OE,
  input  nL_OE,
  input  [15:0] ADDRBUS_IN,
  input  nSP_LD,
  input  nSP_plus_plus,
  input  nA_OE,
  input  nSP_minus_minus,
  output [7:0] DATABUS_OUT,
  output [15:0] ADDRBUS_OUT
);

  wire n8bit_up_down_counter_register_2_ntcd, n8bit_up_down_counter_register_2_ntcu;
  wire [7:0] n8bit_up_down_counter_register_1_q, n8bit_up_down_counter_register_2_q;

  _8bit_up_down_counter_register u_8bit_up_down_counter_register_1 (
    .D(ADDRBUS_IN[15:8]), .CPU(n8bit_up_down_counter_register_2_ntcu),
    .CPD(n8bit_up_down_counter_register_2_ntcd), .nPL(nSP_LD), .MR(1'b0),
    .Q(n8bit_up_down_counter_register_1_q));  // open: nTCU, nTCD
  _8bit_up_down_counter_register u_8bit_up_down_counter_register_2 (
    .D(ADDRBUS_IN[7:0]), .CPU(nSP_plus_plus), .CPD(nSP_minus_minus), .nPL(nSP_LD), .MR(1'b0),
    .Q(n8bit_up_down_counter_register_2_q), .nTCU(n8bit_up_down_counter_register_2_ntcu),
    .nTCD(n8bit_up_down_counter_register_2_ntcd));
  Buffer_tri_state_8bit buffer_tri_state_8bit_1 (
    .IN(n8bit_up_down_counter_register_1_q), .OE(nH_OE), .OUT(DATABUS_OUT));
  Buffer_tri_state_8bit buffer_tri_state_8bit_2 (
    .IN(n8bit_up_down_counter_register_2_q), .OE(nL_OE), .OUT(DATABUS_OUT));
  Buffer_tri_state_8bit buffer_tri_state_8bit_3 (
    .IN(n8bit_up_down_counter_register_1_q), .OE(nA_OE), .OUT(ADDRBUS_OUT[15:8]));
  Buffer_tri_state_8bit buffer_tri_state_8bit_4 (
    .IN(n8bit_up_down_counter_register_2_q), .OE(nA_OE), .OUT(ADDRBUS_OUT[7:0]));

  // Notes on the sheet:
  //   counting should be done with one of the cnt dirs set to high, otherwise unpredictable behaviour will occur
endmodule

module Address_Register (
  input  [7:0] DATABUS_IN,
  input  CLK,
  input  nOE,
  output [15:0] ADDRBUS
);

  wire [7:0] H_q, L_q;

  Register_8bit L (.D(DATABUS_IN), .nOE(1'b0), .CLK(CLK), .Q(L_q));
  Register_8bit H (.D(L_q), .nOE(1'b0), .CLK(CLK), .Q(H_q));
  Buffer_tri_state_8bit buffer_tri_state_8bit_1 (.IN(H_q), .OE(nOE), .OUT(ADDRBUS[15:8]));
  Buffer_tri_state_8bit buffer_tri_state_8bit_2 (.IN(L_q), .OE(nOE), .OUT(ADDRBUS[7:0]));

  // Notes on the sheet:
  //   configuration: big endian
  //   Data is read in from the databus in two cycles; the registers act as shift registers which minimizes control signals
  //   PC/SP reads data from this register via ADDRBUS for instructions that alter them; this register is used as temporary storage of the new address
endmodule

// FLAG
module Flag_Register (
  input  [7:0] DATABUS_IN,
  input  [7:0] ALU_FLAGS_IN,
  input  ALU__DB,
  input  CLK,
  input  nDATABUS_OE,
  output [7:0] FLAGS,
  output [7:0] DATABUS_OUT
);

  wire [7:0] MUX_8bit_out_5;

  MUX_8bit MUX_8bit (.A(DATABUS_IN), .B(ALU_FLAGS_IN), .nE(1'b0), .S(ALU__DB), .out_5(MUX_8bit_out_5));
  Register_8bit u_Flags (.D(MUX_8bit_out_5), .nOE(1'b0), .CLK(CLK), .Q(FLAGS));
  Buffer_tri_state_8bit buffer_tri_state_8bit_1 (.IN(FLAGS), .OE(nDATABUS_OE), .OUT(DATABUS_OUT));

  // Notes on the sheet:
  //   no need to Implement as flip flops; interrupt flags are in IRQ controller
  //   Flags: A, C, V, Z, S
endmodule

module Log_Shifter (
  input  [7:0] r0_IN,
  input  [7:0] DATABUS_IN,
  input  L_R,
  output [7:0] r0_OUT
);

  wire [7:0] mux_8bit_1_out_5, mux_8bit_2_out_5, mux_8bit_3_out_5, mux_8bit_4_out_5, mux_8bit_5_out_5,
       mux_8bit_6_out_5;

  MUX_8bit mux_8bit_1 (.A(r0_IN), .B({r0_IN[6:0], 1'b0}), .nE(1'b0), .S(DATABUS_IN[0]), .out_5(mux_8bit_1_out_5));
  MUX_8bit mux_8bit_2 (.A(r0_IN), .B({1'b0, r0_IN[7:1]}), .nE(1'b0), .S(DATABUS_IN[0]), .out_5(mux_8bit_2_out_5));
  MUX_8bit mux_8bit_3 (
    .A(mux_8bit_1_out_5), .B({mux_8bit_1_out_5[5:0], 2'b00}), .nE(1'b0), .S(DATABUS_IN[1]),
    .out_5(mux_8bit_3_out_5));
  MUX_8bit mux_8bit_4 (
    .A(mux_8bit_2_out_5), .B({2'b00, mux_8bit_2_out_5[7:2]}), .nE(1'b0), .S(DATABUS_IN[1]),
    .out_5(mux_8bit_4_out_5));
  MUX_8bit mux_8bit_5 (
    .A(mux_8bit_3_out_5), .B({mux_8bit_3_out_5[3:0], 4'b0000}), .nE(1'b0), .S(DATABUS_IN[2]),
    .out_5(mux_8bit_5_out_5));
  MUX_8bit mux_8bit_6 (
    .A(mux_8bit_4_out_5), .B({4'b0000, mux_8bit_4_out_5[7:4]}), .nE(1'b0), .S(DATABUS_IN[2]),
    .out_5(mux_8bit_6_out_5));
  // Probe on mux_8bit_5_out_5
  // Probe on mux_8bit_6_out_5
  MUX_8bit mux_8bit_7 (.A(mux_8bit_5_out_5), .B(mux_8bit_6_out_5), .nE(1'b0), .S(L_R), .out_5(r0_OUT));

  // Notes on the sheet:
  //   SH1
  //   SH2
  //   SH4
endmodule

// CLK GEN
module Clock_Generator (
  input  EXTCLK,
  input  HLT,
  output [3:0] PHASE,
  output [3:0] INVERTED_PHASE
);

  wire nor_1_out, shift_register_1_q0, shift_register_1_q1, shift_register_1_q2, shift_register_1_q3;

  nor nor_1 (nor_1_out, shift_register_1_q0, shift_register_1_q1, shift_register_1_q2, HLT);
  Shift_Register shift_register_1 (
    .in(nor_1_out), .clk(EXTCLK), .q0(shift_register_1_q0), .q1(shift_register_1_q1),
    .q2(shift_register_1_q2), .q3(shift_register_1_q3));  // open: shift, out, load, clr, d0, d1, d2, d3, d4, q4, d5, q5, d6, q6, d7, q7
  _74175___4x_D_flip_flops u_74175_4x_d_flip_flops_1 (
    .D1(shift_register_1_q0), .D2(shift_register_1_q1), .D3(shift_register_1_q2), .D4(shift_register_1_q3),
    .CLK(EXTCLK), .nCLR(1'b1), .Q1(PHASE[0]), .nQ1(INVERTED_PHASE[0]), .Q2(PHASE[1]),
    .nQ2(INVERTED_PHASE[1]), .Q3(PHASE[2]), .nQ3(INVERTED_PHASE[2]), .Q4(PHASE[3]), .nQ4(INVERTED_PHASE[3]));

  // Notes on the sheet:
  //   1: data
  //   3: next t state
  //   use any shift reg
  //   RDY: connect to external pull up
  //   0: IRQ latch/pre decrement
  //   2: post increment
  //   Note: when an OP is in action, it will NOT be in fetch state
  //   (IRQ ACK: when fetch && CLKs=IRQ latch)
  //   thus, it is safe to use IRQ latch clock as pre decrement clock
endmodule

module Clock_Breaker (
  input  switch,
  input  [3:0] CLKs_in,
  input  [3:0] nCLKs_in,
  output [3:0] CLKs_out,
  output [3:0] nCLKs_out
);

  assign CLKs_out = switch ? CLKs_in : 4'bz;  // Controlled_Buffer controlled_buffer_1
  assign nCLKs_out = switch ? nCLKs_in : 4'bz;  // Controlled_Buffer controlled_buffer_2

  // Notes on the sheet:
  //   tri state buffers to simulate phyiscal switches
endmodule

module Simple_IRQ_Controller (
  input  nRESET,
  input  nIRQ_CLK,
  input  nIRQ,
  input  nT0,
  input  nCLI,
  input  nSEI,
  output INT,
  output nINT
);

  wire n7474_dual_d_ffs_1_q2, or_1_out;

  Pull_Resistor pull_resistor_1 (.node(nRESET));
  or or_1 (or_1_out, nIRQ_CLK, nIRQ, nT0, n7474_dual_d_ffs_1_q2);
  Pull_Resistor #(.pull(1)) pull_resistor_2 (.node(nSEI));
  Pull_Resistor pull_resistor_3 (.node(nCLI));
  _7474_Dual_D_FFs u_7474_dual_d_ffs_1 (
    .PRE1(nRESET), .CLR1(or_1_out), .CLK1(1'b0), .D1(1'b0), .PRE2(nCLI), .CLR2(nSEI), .CLK2(1'b0), .D2(1'b0),
    .Q1(nINT), .Q1_2(INT), .Q2(n7474_dual_d_ffs_1_q2));  // open: Q2_2

  // Notes on the sheet:
  //   needs external pull up
endmodule

module MUX_8bit (
  input  [7:0] A,
  input  [7:0] B,
  input  nE,
  input  S,
  output [7:0] out_5
);

  wire n74157_2_1_mux_1_y1, n74157_2_1_mux_1_y2, n74157_2_1_mux_1_y3, n74157_2_1_mux_1_y4,
       n74157_2_1_mux_2_y1, n74157_2_1_mux_2_y2, n74157_2_1_mux_2_y3, n74157_2_1_mux_2_y4;

  _74157_2_1_MUX u_74157_2_1_mux_1 (
    .S(S), .nE(nE), ._1B(B[0]), ._1A(A[0]), ._2B(B[1]), ._2A(A[1]), ._3B(B[2]), ._3A(A[2]), ._4B(B[3]),
    ._4A(A[3]), .Y1(n74157_2_1_mux_1_y1), .Y2(n74157_2_1_mux_1_y2), .Y3(n74157_2_1_mux_1_y3),
    .Y4(n74157_2_1_mux_1_y4));
  _74157_2_1_MUX u_74157_2_1_mux_2 (
    .S(S), .nE(nE), ._1B(B[4]), ._1A(A[4]), ._2B(B[5]), ._2A(A[5]), ._3B(B[6]), ._3A(A[6]), ._4B(B[7]),
    ._4A(A[7]), .Y1(n74157_2_1_mux_2_y1), .Y2(n74157_2_1_mux_2_y2), .Y3(n74157_2_1_mux_2_y3),
    .Y4(n74157_2_1_mux_2_y4));
  _8bit_to_bus u_8bit_to_bus_1 (
    .in_1(n74157_2_1_mux_1_y1), .in_2(n74157_2_1_mux_1_y2), .in_3(n74157_2_1_mux_1_y3),
    .in_4(n74157_2_1_mux_1_y4), .in_5(n74157_2_1_mux_2_y1), .in_6(n74157_2_1_mux_2_y2),
    .in_7(n74157_2_1_mux_2_y3), .in_8(n74157_2_1_mux_2_y4), .out_9(out_5));
endmodule

module MUX_4bit (
  input  [3:0] A,
  input  [3:0] B,
  input  nE,
  input  S,
  output [3:0] Y
);

  _74157_2_1_MUX u_74157_2_1_mux_1 (
    .S(S), .nE(nE), ._1B(B[0]), ._1A(A[0]), ._2B(B[1]), ._2A(A[1]), ._3B(B[2]), ._3A(A[2]), ._4B(B[3]),
    ._4A(A[3]), .Y1(Y[0]), .Y2(Y[1]), .Y3(Y[2]), .Y4(Y[3]));
endmodule

module _8bit_register (
  input  [7:0] D,
  input  nOE,
  input  CLK,
  output [7:0] Q
);

  wire bus_to_8bit_1_out_2, bus_to_8bit_1_out_3, bus_to_8bit_1_out_4, bus_to_8bit_1_out_5,
       bus_to_8bit_1_out_6, bus_to_8bit_1_out_7, bus_to_8bit_1_out_8, bus_to_8bit_1_out_9,
       n74574_8x_d_flip_flop_1_q0, n74574_8x_d_flip_flop_1_q1, n74574_8x_d_flip_flop_1_q2,
       n74574_8x_d_flip_flop_1_q3, n74574_8x_d_flip_flop_1_q4, n74574_8x_d_flip_flop_1_q5,
       n74574_8x_d_flip_flop_1_q6, n74574_8x_d_flip_flop_1_q7;

  _74574___8x_D_Flip_Flop u_74574_8x_d_flip_flop_1 (
    .Clk(CLK), .nOE(nOE), .D0(bus_to_8bit_1_out_2), .D1(bus_to_8bit_1_out_3), .D2(bus_to_8bit_1_out_4),
    .D3(bus_to_8bit_1_out_5), .D4(bus_to_8bit_1_out_6), .D5(bus_to_8bit_1_out_7), .D6(bus_to_8bit_1_out_8),
    .D7(bus_to_8bit_1_out_9), .Q0(n74574_8x_d_flip_flop_1_q0), .Q1(n74574_8x_d_flip_flop_1_q1),
    .Q2(n74574_8x_d_flip_flop_1_q2), .Q3(n74574_8x_d_flip_flop_1_q3), .Q4(n74574_8x_d_flip_flop_1_q4),
    .Q5(n74574_8x_d_flip_flop_1_q5), .Q6(n74574_8x_d_flip_flop_1_q6), .Q7(n74574_8x_d_flip_flop_1_q7));
  bus_to_8bit bus_to_8bit_1 (
    .in_1(D), .out_2(bus_to_8bit_1_out_2), .out_3(bus_to_8bit_1_out_3), .out_4(bus_to_8bit_1_out_4),
    .out_5(bus_to_8bit_1_out_5), .out_6(bus_to_8bit_1_out_6), .out_7(bus_to_8bit_1_out_7),
    .out_8(bus_to_8bit_1_out_8), .out_9(bus_to_8bit_1_out_9));
  _8bit_to_bus u_8bit_to_bus_1 (
    .in_1(n74574_8x_d_flip_flop_1_q0), .in_2(n74574_8x_d_flip_flop_1_q1), .in_3(n74574_8x_d_flip_flop_1_q2),
    .in_4(n74574_8x_d_flip_flop_1_q3), .in_5(n74574_8x_d_flip_flop_1_q4), .in_6(n74574_8x_d_flip_flop_1_q5),
    .in_7(n74574_8x_d_flip_flop_1_q6), .in_8(n74574_8x_d_flip_flop_1_q7), .out_9(Q));
endmodule

// 8bit U/D Ctr
module _8bit_up_down_counter_register (
  input  [7:0] D,
  input  CPU,
  input  CPD,
  input  nPL,
  input  MR,
  output [7:0] Q,
  output nTCU,
  output nTCD
);

  wire n74193_1_ntcd, n74193_1_ntcu;

  _74193 u_74193_1 (
    .nPL(nPL), .CPU(CPU), .CPD(CPD), .MR(MR), .nTCU(n74193_1_ntcu), .nTCD(n74193_1_ntcd), .D0(D[0]),
    .D1(D[1]), .D2(D[2]), .D3(D[3]), .Q0(Q[0]), .Q1(Q[1]), .Q2(Q[2]), .Q3(Q[3]));
  _74193 u_74193_2 (
    .nPL(nPL), .CPU(n74193_1_ntcu), .CPD(n74193_1_ntcd), .MR(MR), .nTCU(nTCU), .nTCD(nTCD), .D0(D[4]),
    .D1(D[5]), .D2(D[6]), .D3(D[7]), .Q0(Q[4]), .Q1(Q[5]), .Q2(Q[6]), .Q3(Q[7]));
endmodule

// 8bit cnt reg
module _8bit_Counter_Register (
  input  Count_Enable,
  input  [7:0] D,
  input  nPreset,
  input  nClear,
  input  CLK,
  output [7:0] Q,
  output TC
);

  wire n74161_1_tc;

  _74161 u_74161_1 (
    .CET(Count_Enable), .CEP(1'b1), .PE(nPreset), .CLK(CLK), .MR(nClear), .D0(D[0]), .D1(D[1]), .D2(D[2]),
    .D3(D[3]), .Q0(Q[0]), .Q1(Q[1]), .Q2(Q[2]), .Q3(Q[3]), .TC(n74161_1_tc));
  _74161 u_74161_2 (
    .CET(n74161_1_tc), .CEP(1'b1), .PE(nPreset), .CLK(CLK), .MR(nClear), .D0(D[4]), .D1(D[5]), .D2(D[6]),
    .D3(D[7]), .Q0(Q[4]), .Q1(Q[5]), .Q2(Q[6]), .Q3(Q[7]), .TC(TC));
endmodule

module IO_interface (
  input  [7:0] ADDR,
  input  [15:0] ADDRBUS,
  input  WE,
  input  D_CLK,
  input  RE,
  input  IO_M,
  output W_CLK,
  output RE_2
);

  wire and_1_out, comparator_1_eq, not_1_out;

  and and_1 (and_1_out, WE, D_CLK);
  not not_1 (not_1_out, IO_M);
  Comparator comparator_1 (.a(ADDR), .b(ADDRBUS[7:0]), .eq(comparator_1_eq));  // open: gt, lt
  and and_2 (W_CLK, comparator_1_eq, not_1_out, and_1_out);
  and and_3 (RE_2, comparator_1_eq, not_1_out, RE);
endmodule

module IRQ_interface (
  input  [7:0] IVECT,
  input  INT,
  input  nINTA,
  output [7:0] DATABUS,
  output nINTA_OUT,
  output nIRQ
);

  wire not_1_out, or_1_out;

  Buffer_tri_state_8bit INT_VECT_0 (.IN(IVECT), .OE(or_1_out), .OUT(DATABUS));
  or or_1 (or_1_out, nINTA, not_1_out);
  not not_1 (not_1_out, INT);
  or or_2 (nINTA_OUT, INT, nINTA);
  Pull_Resistor #(.pull(1)) pull_resistor_1 (.node(nIRQ));
  Transistor #(.\type ("n")) transistor_1 (.in(1'b0), .out(nIRQ), .gate(INT));
endmodule

module Left_Bank (
  input  [1:0] S,
  input  [15:0] DATABUS,
  input  nTEMP_OE,
  input  CLK,
  input  [1:0] IMM,
  input  nIMM_L_OE,
  output [15:0] LEFTBUS
);

  Temp_Left temp_left_1 (.DATABUS(DATABUS), .S(S), .CLK(CLK), .OE(nTEMP_OE), .LEFTBUS(LEFTBUS));
  Immediate_Register immediate_register_1 (.D(IMM), .nOE(nIMM_L_OE), .Q(LEFTBUS));

  // Notes on the sheet:
  //   Left Immediate Register
  //   Temporary Register
endmodule

module Right_Bank (
  input  [15:0] DATABUS,
  input  [7:0] OE_LINES,
  input  [7:0] CLK_LINES,
  input  [1:0] IMM,
  input  [4:0] FLAGS_IN,
  input  nIMM_R_OE,
  input  F_CLK,
  input  NORM,
  input  SWAP,
  output [15:0] RIGHTBUS,
  output [4:0] FLAGS_OUT,
  output [7:0] INTM,
  output INTE
);

  wire A_CLK, A_OE, B_CLK, B_OE, MSW_CLK, MSW_OE, PC_CLK, PC_OE, SP_CLK, SP_OE, TEMP_R_CLK, TEMP_R_OE, X_CLK,
       X_OE;
  wire [15:0] register_8bit_1_p4;

  bus_to_8bit bus_to_8bit_1 (
    .in_1(OE_LINES), .out_3(A_OE), .out_4(B_OE), .out_5(X_OE), .out_6(PC_OE), .out_7(SP_OE), .out_8(MSW_OE),
    .out_9(TEMP_R_OE));  // open: out_2
  bus_to_8bit bus_to_8bit_2 (
    .in_1(CLK_LINES), .out_3(A_CLK), .out_4(B_CLK), .out_5(X_CLK), .out_6(PC_CLK), .out_7(SP_CLK),
    .out_8(MSW_CLK), .out_9(TEMP_R_CLK));  // open: out_2
  // Register_8bit register_8bit_1: pin names not known; wires that end beside it: DATABUS, A_OE, A_CLK, register_8bit_1_p4
  // Register_8bit register_8bit_2: pin names not known; wires that end beside it: DATABUS, B_OE, B_CLK, register_8bit_1_p4
  // Register_8bit register_8bit_3: pin names not known; wires that end beside it: DATABUS, X_OE, X_CLK, RIGHTBUS
  // Register_8bit register_8bit_4: pin names not known; wires that end beside it: DATABUS, PC_OE, PC_CLK, RIGHTBUS
  // Register_8bit register_8bit_5: pin names not known; wires that end beside it: DATABUS, SP_OE, SP_CLK, RIGHTBUS
  MSW msw_1 (
    .IN(DATABUS), .nOE(MSW_OE), .Flags_CLK(F_CLK), .CLK(MSW_CLK), .OUT(RIGHTBUS), .INTM(INTM), .INTE(INTE),
    .Flags_IN(FLAGS_IN), .Flags_OUT(FLAGS_OUT));
  // Register_8bit register_8bit_6: pin names not known; wires that end beside it: DATABUS, TEMP_R_OE, TEMP_R_CLK, RIGHTBUS
  Buffer_tri_state_8bit buffer_tri_state_8bit_1 (.IN(register_8bit_1_p4[7:0]), .OE(NORM), .OUT(RIGHTBUS[7:0]));
  Buffer_tri_state_8bit buffer_tri_state_8bit_2 (.IN(register_8bit_1_p4[15:8]), .OE(NORM), .OUT(RIGHTBUS[15:8]));
  Buffer_tri_state_8bit buffer_tri_state_8bit_3 (.IN(register_8bit_1_p4[7:0]), .OE(SWAP), .OUT(RIGHTBUS[15:8]));
  Buffer_tri_state_8bit buffer_tri_state_8bit_4 (.IN(register_8bit_1_p4[15:8]), .OE(SWAP), .OUT(RIGHTBUS[7:0]));
  Immediate_Register immediate_register_1 (.D(IMM), .nOE(nIMM_R_OE), .Q(RIGHTBUS));

  // Other names for the same wires on the sheet: Normal = NORM; Swapped = SWAP

  // Notes on the sheet:
  //   A
  //   B
  //   X
  //   PC
  //   SP
  //   TEMP R
  //   Right Immediate Register
endmodule

module Register_Bank (
  input  [3:0] OE,
  input  [7:0] D,
  input  nOE_ENABLE,
  input  [3:0] IE,
  input  nIE_ENABLE,
  input  CLK,
  output [7:0] Q
);

  wire n74138_1_y0, n74138_1_y1, n74138_1_y2, n74138_1_y3, n74138_1_y4, n74138_1_y5, n74138_1_y6,
       n74138_1_y7, n74238_1_y0, n74238_1_y1, n74238_1_y2, n74238_1_y3, n74238_1_y4, n74238_1_y5,
       n74238_1_y6, n74238_1_y7;
  wire [7:0] n8bit_to_bus_1_out_9, n8bit_to_bus_2_out_9;

  _74138 u_74138_1 (
    .nE1(OE[3]), .nE2(nOE_ENABLE), .E3(1'b1), .A0(OE[0]), .A1(OE[1]), .A2(OE[2]), .Y0(n74138_1_y0),
    .Y1(n74138_1_y1), .Y2(n74138_1_y2), .Y3(n74138_1_y3), .Y4(n74138_1_y4), .Y5(n74138_1_y5),
    .Y6(n74138_1_y6), .Y7(n74138_1_y7));
  _74238 u_74238_1 (
    .A0(IE[0]), .A1(IE[1]), .A2(IE[2]), .nE1(IE[3]), .nE2(nIE_ENABLE), .E3(CLK), .Y0(n74238_1_y0),
    .Y1(n74238_1_y1), .Y2(n74238_1_y2), .Y3(n74238_1_y3), .Y4(n74238_1_y4), .Y5(n74238_1_y5),
    .Y6(n74238_1_y6), .Y7(n74238_1_y7));
  _8bit_to_bus u_8bit_to_bus_1 (
    .in_1(n74138_1_y0), .in_2(n74138_1_y1), .in_3(n74138_1_y2), .in_4(n74138_1_y3), .in_5(n74138_1_y4),
    .in_6(n74138_1_y5), .in_7(n74138_1_y6), .in_8(n74138_1_y7), .out_9(n8bit_to_bus_1_out_9));
  _8bit_to_bus u_8bit_to_bus_2 (
    .in_1(n74238_1_y0), .in_2(n74238_1_y1), .in_3(n74238_1_y2), .in_4(n74238_1_y3), .in_5(n74238_1_y4),
    .in_6(n74238_1_y5), .in_7(n74238_1_y6), .in_8(n74238_1_y7), .out_9(n8bit_to_bus_2_out_9));
  GP_Register_Bank _8x_regs ();  // open: D, Q, DCD_nOEs, DCD_CLKs

  // Notes on the sheet:
  //   OE decode
  //   activates on MSB = 0
  //   IE decode
  //   activates on MSB = 1
  //   Registers r0 to r7
endmodule

module Control_Unit (
  input  CLK_IN,
  input  HALT,
  input  CONT,
  input  DMA,
  input  [7:0] Instruction_L,
  input  [4:0] Flags,
  input  [7:0] Instruction_H,
  input  [2:0] RST_NMI_IRQ,
  input  MAR_0,
  output OE0,
  output OE1,
  output OE2,
  output IE0,
  output IE1,
  output IE2,
  output HLTA,
  output W_IR,
  output W_MAR,
  output OE_ALU,
  output ALU_0,
  output ALU_1,
  output ALU_2,
  output W_F,
  output R_CARRY,
  output TEMP_L_S0,
  output TEMP_L_S1,
  output R_TEMP_L,
  output IO__M,
  output RE,
  output WE,
  output IMM0,
  output IMM1,
  output OE_IMM_R,
  output OE_IMM_L,
  output BYTE,
  output reserved,
  output INTA,
  output INT_IE,
  output CLK_OUT,
  output BE0,
  output BE1,
  output NORM,
  output SWAP
);

  wire and_1_out, bus_to_8bit_1_out_2, bus_to_8bit_1_out_3, bus_to_8bit_1_out_4, bus_to_8bit_1_out_5,
       bus_to_8bit_1_out_6, bus_to_8bit_1_out_7, clear, CLK_OUT_t, \continue , halt_t, INT_LATCH,
       n7473_dual_jk_ffs_1__2_q, n7475_quad_latches_1_q0_2, n7475_quad_latches_1_q1_2,
       n7475_quad_latches_1_q2_2, n74574_8x_d_flip_flop_1_q0, n74574_8x_d_flip_flop_1_q1,
       n74574_8x_d_flip_flop_1_q2, nand_1_out, nand_2_out, nINT_OE, not_3_out, or_1_out, or_2_out, PRI_a0__9,
       PRI_a1__7, xor_1_out;
  wire [1:0] not_1_out;
  wire [3:0] CNT_q0;
  wire [7:0] rom_1_data, rom_2_data, rom_3_data, rom_4_data;
  wire [13:13] MUX_y;

  or or_1 (or_1_out, HALT, halt_t);
  or or_2 (or_2_out, CONT, \continue );
  _7473_Dual_JK_FFs u_7473_dual_jk_ffs_1 (
    ._1J(n7473_dual_jk_ffs_1__2_q), ._1K(1'b1), ._1CLK(CLK_IN), ._1_CLR(1'b1), ._2J(or_1_out),
    ._2K(or_2_out), ._2CLK(CLK_IN), ._2_CLR(1'b1), ._1Q(CLK_OUT), ._1_Q(CLK_OUT_t), ._2Q(HLTA),
    ._2_Q(n7473_dual_jk_ffs_1__2_q));
  _74574___8x_D_Flip_Flop u_74574_8x_d_flip_flop_1 (
    .Clk(and_1_out), .nOE(nINT_OE), .D0(RST_NMI_IRQ[0]), .D1(RST_NMI_IRQ[1]), .D2(RST_NMI_IRQ[2]), .D3(1'b0),
    .D4(1'b0), .D5(1'b0), .D6(1'b0), .D7(1'b0), .Q0(n74574_8x_d_flip_flop_1_q0),
    .Q1(n74574_8x_d_flip_flop_1_q1), .Q2(n74574_8x_d_flip_flop_1_q2));  // open: Q3, Q4, Q5, Q6, Q7
  and and_1 (and_1_out, INT_IE, CLK_OUT);
  Pull_Resistor #(.pull(1)) pull_resistor_1 (.node(Instruction_L));
  Pull_Resistor pull_resistor_2 (.node(Instruction_H));
  or or_3 (\continue , RST_NMI_IRQ[2], RST_NMI_IRQ[1], RST_NMI_IRQ[0]);
  Pull_Resistor pull_resistor_3 (.node(n74574_8x_d_flip_flop_1_q1));
  Pull_Resistor pull_resistor_4 (.node(n74574_8x_d_flip_flop_1_q2));
  Pull_Resistor pull_resistor_5 (.node(n74574_8x_d_flip_flop_1_q0));
  _74151 MUX (
    .I0(Flags[0]), .I1(Flags[1]), .I2(Flags[2]), .I3(Flags[3]), .I4(Flags[4]), .I5(1'b0), .I6(1'b0),
    .I7(1'b0), .Y(MUX_y[13]), .S0(Instruction_H[0]), .S1(Instruction_H[1]), .S2(Instruction_H[2]), .E(1'b0));  // open: Y_2
  _7475_Quad_Latches u_7475_quad_latches_1 (
    .D0(n74574_8x_d_flip_flop_1_q0), .D1(n74574_8x_d_flip_flop_1_q1), .D2(n74574_8x_d_flip_flop_1_q2),
    .Q0_2(n7475_quad_latches_1_q0_2), .E0_1(INT_LATCH), .Q1_2(n7475_quad_latches_1_q1_2),
    .Q2_2(n7475_quad_latches_1_q2_2), .E2_3(INT_LATCH));  // open: D3, Q0, Q1, Q2, Q3, Q2_3
  _74161 CNT (
    .CET(1'b1), .CEP(1'b1), .PE(1'b1), .CLK(CLK_OUT_t), .MR(clear), .D0(1'b0), .D1(1'b0), .D2(1'b0),
    .D3(1'b0), .Q0(CNT_q0[0]), .Q1(CNT_q0[1]), .Q2(CNT_q0[2]), .Q3(CNT_q0[3]));  // open: TC
  _74148 PRI (
    ._0__10(1'b1), ._1__11(n7475_quad_latches_1_q0_2), ._2__12(n7475_quad_latches_1_q1_2),
    ._3__13(n7475_quad_latches_1_q2_2), ._4__1(1'b1), ._5__2(1'b1), ._6__3(1'b1), ._7__4(1'b1), .EI__5(1'b0),
    .A0__9(PRI_a0__9), .A1__7(PRI_a1__7));  // open: EO__15, G5__14, A2__6
  not not_1 (not_1_out[0], PRI_a0__9);
  not not_2 (not_1_out[1], PRI_a1__7);
  nand nand_1 (nand_1_out, BYTE, MAR_0);
  not not_3 (not_3_out, MAR_0);
  ROM #(.addrWidth(16)) rom_1 (
    .addr({not_1_out, MUX_y[13], Instruction_L, 1'b0, CNT_q0}), .data(rom_1_data));  // open: sel
  ROM #(.addrWidth(16)) rom_2 (
    .addr({not_1_out, MUX_y[13], Instruction_L, 1'b0, CNT_q0}), .data(rom_2_data));  // open: sel
  ROM #(.addrWidth(16)) rom_3 (
    .addr({not_1_out, MUX_y[13], Instruction_L, 1'b0, CNT_q0}), .data(rom_3_data));  // open: sel
  ROM #(.addrWidth(16)) rom_4 (
    .addr({not_1_out, MUX_y[13], Instruction_L, 1'b0, CNT_q0}), .data(rom_4_data));  // open: sel
  nand nand_2 (nand_2_out, not_3_out, BYTE);
  bus_to_8bit bus_to_8bit_1 (
    .in_1(rom_1_data), .out_2(bus_to_8bit_1_out_2), .out_3(bus_to_8bit_1_out_3), .out_4(bus_to_8bit_1_out_4),
    .out_5(bus_to_8bit_1_out_5), .out_6(bus_to_8bit_1_out_6), .out_7(bus_to_8bit_1_out_7), .out_8(W_IR),
    .out_9(W_MAR));
  bus_to_8bit bus_to_8bit_2 (
    .in_1(rom_2_data), .out_2(OE_ALU), .out_3(ALU_0), .out_4(ALU_1), .out_5(ALU_2), .out_6(W_F),
    .out_7(R_CARRY), .out_8(TEMP_L_S0), .out_9(TEMP_L_S1));
  bus_to_8bit bus_to_8bit_3 (
    .in_1(rom_3_data), .out_2(R_TEMP_L), .out_3(IO__M), .out_4(RE), .out_5(WE), .out_6(IMM0), .out_7(IMM1),
    .out_8(OE_IMM_R), .out_9(OE_IMM_L));
  bus_to_8bit bus_to_8bit_4 (
    .in_1(rom_4_data), .out_2(BYTE), .out_3(reserved), .out_4(INTA), .out_5(nINT_OE), .out_6(INT_IE),
    .out_7(INT_LATCH), .out_8(halt_t), .out_9(clear));
  and and_2 (BE0, WE, nand_1_out);
  and and_3 (BE1, WE, nand_2_out);
  xor xor_1 (xor_1_out, Instruction_H[3], MAR_0);
  and and_4 (NORM, xor_1_out, BYTE);
  not not_4 (SWAP, NORM);
  _74541 u_74541_1 (
    .A0(bus_to_8bit_1_out_2), .A2(bus_to_8bit_1_out_3), .A3(bus_to_8bit_1_out_4), .A4(1'b0), .A5(1'b0),
    .A6(bus_to_8bit_1_out_5), .A7(bus_to_8bit_1_out_6), .A8(bus_to_8bit_1_out_7), .nOE1(DMA), .nOE2(DMA),
    .Y0(OE0), .Y1(OE1), .Y2(OE2), .Y5(IE0), .Y6(IE1), .Y7(IE2));  // open: Y3, Y4

  // Other names for the same wires on the sheet: H__L = Instruction_H[3]

  // Notes on the sheet:
  //   Normal system clock
  //   Anti phase system clock
  //   When DMA is set, IR OE is disabled, and pull resistors pulls to HLT state
  //   AT27C256R-45PU
  //   AT27C256R-45PU
  //   AT27C256R-45PU
  //   AT27C256R-45PU
  //   contents of rom_1 (hex, n*v repeats v):
  //   a4 40 30*0 a4 40 30*0 a4 40 11 29*0 a4 40 19 29*0 a4 40 21 29*0 a4 40 29 29*0 a4 40 31 29*0 a4 40 a
  //   29*0 a4 40 22 29*0 a4 40 2a 29*0 a4 40 1a 29*0 a4 40 32 285*0 a4 40 a4 8 28*0 a4 40 a4 38 87 8 26*0
  //   a4 40 83 8 60*0 a4 40 a4 10 28*0 a4 40 a4 38 87 10 90*0 a4 40 a4 38 87 1 58*0 a4 40 a4 0 3b 87 1
  //   25*0 a4 40 a4 38 87 2 90*0 a4 40 a4 38 87 1 26*0 a4 40 a4 18 156*0 a4 40 a4 38 87 1 26*0 a4 40 a4 38
  //   87 1 58*0 a4 40 ad 1 28*0 a4 40 ad 2 156*0 a4 40 2d 85 8 27*0 a4 40 2d 85 10 155*0 a4 40 a4 0 3d 87
  //   8 121*0 a4 40 2 9 28*0 a4 40 2 11 60*0 a4 40 a4 0 9 27*0 a4 40 a4 0 12 443*0 a4 40 1 9 28*0 a4 40 2
  //   12 28*0 a4 40 a4 38 87 38 7 25*0 a4 40 1 0 8 27*0 a4 40 2 0 10 27*0 a4 40 a4 38 87 91*0 a4 40 1b
  //   29*0 a4 40 1b 93*0 a4 40 1b 61*0 a4 40 2 1 28*0 a4 40 a4 0 1 27*0 a4 40 a4 0 2 27*0 a4 40 a4 0 3
  //   59*0 a4 40 2 61*0 a4 40 2 9 28*0 a4 40 2 11 28*0 a4 40 a4 0 9 27*0 a4 40 a4 0 12 27*0 a4 40 2 9 28*0
  //   a4 40 2 11 28*0 a4 40 a4 0 9 27*0 a4 40 a4 0 12 4315*0 a4 40 a4 20 28*0 a4 40 a4 29*0 a4 40 a4 20
  //   28*0 a4 40 ad 4 a4 20 90*0 a4 40 2d 85 20 27*0 a4 40 30*0 a4 40 2d 85 20 27*0 a4 40 2d 85 30 2d 85
  //   20 24*0 a4 40 0 ad 28*0 a4 40 0 ad 156*0 a4 40 30*0 a4 40 30*0 a4 40 11 29*0 a4 40 19 29*0 a4 40 21
  //   29*0 a4 40 29 29*0 a4 40 31 29*0 a4 40 a 29*0 a4 40 22 29*0 a4 40 2a 29*0 a4 40 1a 29*0 a4 40 32
  //   285*0 a4 40 a4 8 28*0 a4 40 a4 38 87 8 26*0 a4 40 83 8 60*0 a4 40 a4 10 28*0 a4 40 a4 38 87 10 90*0
  //   a4 40 a4 38 87 1 58*0 a4 40 a4 0 3b 87 1 25*0 a4 40 a4 38 87 2 90*0 a4 40 a4 38 87 1 26*0 a4 40 a4
  //   18 156*0 a4 40 a4 38 87 1 26*0 a4 40 a4 38 87 1 58*0 a4 40 ad 1 28*0 a4 40 ad 2 156*0 a4 40 2d 85 8
  //   27*0 a4 40 2d 85 10 155*0 a4 40 a4 0 3d 87 8 121*0 a4 40 2 9 28*0 a4 40 2 11 60*0 a4 40 a4 0 9 27*0
  //   a4 40 a4 0 12 443*0 a4 40 1 9 28*0 a4 40 2 12 28*0 a4 40 a4 38 87 38 7 25*0 a4 40 1 0 8 27*0 a4 40 2
  //   0 10 27*0 a4 40 a4 38 87 91*0 a4 40 1b 29*0 a4 40 1b 93*0 a4 40 1b 61*0 a4 40 2 1 28*0 a4 40 a4 0 1
  //   27*0 a4 40 a4 0 2 27*0 a4 40 a4 0 3 59*0 a4 40 2 61*0 a4 40 2 9 28*0 a4 40 2 11 28*0 a4 40 a4 0 9
  //   27*0 a4 40 a4 0 12 27*0 a4 40 2 9 28*0 a4 40 2 11 28*0 a4 40 a4 0 9 27*0 a4 40 a4 0 12 4315*0 a4 40
  //   a4 20 28*0 a4 40 a4 20 28*0 a4 40 a4 29*0 a4 40 ad 4 a4 20 90*0 a4 40 2d 85 20 27*0 a4 40 2d 85 20
  //   27*0 a4 40 30*0 a4 40 2d 85 30 2d 85 20 24*0 a4 40 0 ad 28*0 a4 40 0 ad 157*0 ad 4 ad 6 36 20 84 20
  //   24*0 ad 4 ad 6 36 20 84 20 24*0 ad 4 ad 6 36 20 84 20 24*0 ad 4 ad 6 36 20 84 20 24*0 ad 4 ad 6 36
  //   20 84 20 24*0 ad 4 ad 6 36 20 84 20 24*0 ad 4 ad 6 36 20 84 20 24*0 ad 4 ad 6 36 20 84 20 24*0 ad 4
  //   ad 6 36 20 84 20 24*0 ad 4 ad 6 36 20 84 20 24*0 ad 4 ad 6 36 20 84 20 24*0 ad 4 ad 6 36 20 84 20
  //   24*0 ad 4 ad 6 36 20 84 20 24*0 ad 4 ad 6 36 20 84 20 24*0 ad 4 ad 6 36 20 84 20 24*0 ad 4 ad 6 36
  //   20 84 20 24*0 ad 4 ad 6 36 20 84 20 24*0 ad 4 ad 6 36 20 84 20 24*0 ad 4 ad 6 36 20 84 20 24*0 ad 4
  //   ad 6 36 20 84 20 24*0 ad 4 ad 6 36 20 84 20 24*0 ad 4 ad 6 36 20 84 20 24*0 ad 4 ad 6 36 20 84 20
  //   24*0 ad 4 ad 6 36 20 84 20 24*0 ad 4 ad 6 36 20 84 20 24*0 ad 4 ad 6 36 20 84 20 24*0 ad 4 ad 6 36
  //   20 84 20 24*0 ad 4 ad 6 36 20 84 20 24*0 ad 4 ad 6 36 20 84 20 24*0 ad 4 ad 6 36 20 84 20 24*0 ad 4
  //   ad 6 36 20 84 20 24*0 ad 4 ad 6 36 20 84 20 24*0 ad 4 ad 6 36 20 84 20 24*0 ad 4 ad 6 36 20 84 20
  //   24*0 ad 4 ad 6 36 20 84 20 24*0 ad 4 ad 6 36 20 84 20 24*0 ad 4 ad 6 36 20 84 20 24*0 ad 4 ad 6 36
  //   20 84 20 24*0 ad 4 ad 6 36 20 84 20 24*0 ad 4 ad 6 36 20 84 20 24*0 ad 4 ad 6 36 20 84 20 24*0 ad 4
  //   ad 6 36 20 84 20 24*0 ad 4 ad 6 36 20 84 20 24*0 ad 4 ad 6 36 20 84 20 24*0 ad 4 ad 6 36 20 84 20
  //   24*0 ad 4 ad 6 36 20 84 20 24*0 ad 4 ad 6 36 20 84 20 24*0 ad 4 ad 6 36 20 84 20 24*0 ad 4 ad 6 36
  //   20 84 20 24*0 ad 4 ad 6 36 20 84 20 24*0 ad 4 ad 6 36 20 84 20 24*0 ad 4 ad 6 36 20 84 20 24*0 ad 4
  //   ad 6 36 20 84 20 24*0 ad 4 ad 6 36 20 84 20 24*0 ad 4 ad 6 36 20 84 20 24*0 ad 4 ad 6 36 20 84 20
  //   24*0 ad 4 ad 6 36 20 84 20 24*0 ad 4 ad 6 36 20 84 20 24*0 ad 4 ad 6 36 20 84 20 24*0 ad 4 ad 6 36
  //   20 84 20 24*0 ad 4 ad 6 36 20 84 20 24*0 ad 4 ad 6 36 20 84 20 24*0 ad 4 ad 6 36 20 84 20 24*0 ad 4
  //   ad 6 36 20 84 20 24*0 ad 4 ad 6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
  //   contents of rom_2 (hex, n*v repeats v):
  //   6 31*1 6 31*1 6 1 6 29*1 6 1 6 29*1 6 1 6 29*1 6 1 6 29*1 6 1 6 29*1 6 1 6 29*1 6 1 6 29*1 6 1 6
  //   29*1 6 1 6 29*1 6 1 6 285*1 6 1 6 29*1 6 1 6 29*1 6 63*1 6 1 6 29*1 6 1 6 93*1 6 1 6 1 1 6 58*1 6 1
  //   6 c1 16 1 6 25*1 6 1 6 1 1 6 90*1 6 1 6 1 1 6 26*1 6 1 6 157*1 6 1 6 1 1 6 26*1 6 1 6 1 1 6 58*1 6 1
  //   4 6 28*1 6 1 4 6 156*1 6 1 6 29*1 6 1 6 157*1 6 1 6 c1 4 123*1 6 1 c6 16 28*1 6 1 c6 16 60*1 6 1 6
  //   c1 16 27*1 6 1 6 c1 16 443*1 6 1 c6 16 28*1 6 1 c6 16 28*1 6 1 6 1 1 c1 16 25*1 6 1 c6 41 16 27*1 6
  //   1 c6 41 16 27*1 6 1 6 1 1 c1 41 16 88*1 6 1 16 29*1 6 1 16 93*1 6 1 14 61*1 6 1 c6 14 28*1 6 1 6 c1
  //   14 27*1 6 1 6 c1 14 27*1 6 1 6 c1 14 59*1 6 1 16 61*1 6 1 c6 1c 28*1 6 1 c6 1c 28*1 6 1 6 c1 1c 27*1
  //   6 1 6 c1 1c 27*1 6 1 c6 1a 28*1 6 1 c6 1a 28*1 6 1 6 c1 1a 27*1 6 1 6 c1 1a 4315*1 6 1 6 29*1 6 1 6
  //   29*1 6 1 6 29*1 6 1 4 6 6 91*1 6 1 6 29*1 6 31*1 6 1 6 29*1 6 1 6 1 1 6 26*1 6 1 c0 4 6 27*1 6 1 ca
  //   4 6 155*1 6 31*1 6 31*1 6 1 6 29*1 6 1 6 29*1 6 1 6 29*1 6 1 6 29*1 6 1 6 29*1 6 1 6 29*1 6 1 6 29*1
  //   6 1 6 29*1 6 1 6 29*1 6 1 6 285*1 6 1 6 29*1 6 1 6 29*1 6 63*1 6 1 6 29*1 6 1 6 93*1 6 1 6 1 1 6
  //   58*1 6 1 6 c1 16 1 6 25*1 6 1 6 1 1 6 90*1 6 1 6 1 1 6 26*1 6 1 6 157*1 6 1 6 1 1 6 26*1 6 1 6 1 1 6
  //   58*1 6 1 4 6 28*1 6 1 4 6 156*1 6 1 6 29*1 6 1 6 157*1 6 1 6 c1 4 123*1 6 1 c6 16 28*1 6 1 c6 16
  //   60*1 6 1 6 c1 16 27*1 6 1 6 c1 16 443*1 6 1 c6 16 28*1 6 1 c6 16 28*1 6 1 6 1 1 c1 16 25*1 6 1 c6 41
  //   16 27*1 6 1 c6 41 16 27*1 6 1 6 1 1 c1 41 16 88*1 6 1 16 29*1 6 1 16 93*1 6 1 14 61*1 6 1 c6 14 28*1
  //   6 1 6 c1 14 27*1 6 1 6 c1 14 27*1 6 1 6 c1 14 59*1 6 1 16 61*1 6 1 c6 1c 28*1 6 1 c6 1c 28*1 6 1 6
  //   c1 1c 27*1 6 1 6 c1 1c 27*1 6 1 c6 1a 28*1 6 1 c6 1a 28*1 6 1 6 c1 1a 27*1 6 1 6 c1 1a 4315*1 6 1 6
  //   29*1 6 1 6 29*1 6 1 6 29*1 6 1 4 6 6 91*1 6 1 6 29*1 6 1 6 29*1 6 31*1 6 1 6 1 1 6 26*1 6 1 ca 4 6
  //   27*1 6 1 c0 4 6 156*1 4 6 4 6 a 27*1 4 6 4 6 a 27*1 4 6 4 6 a 27*1 4 6 4 6 a 27*1 4 6 4 6 a 27*1 4 6
  //   4 6 a 27*1 4 6 4 6 a 27*1 4 6 4 6 a 27*1 4 6 4 6 a 27*1 4 6 4 6 a 27*1 4 6 4 6 a 27*1 4 6 4 6 a 27*1
  //   4 6 4 6 a 27*1 4 6 4 6 a 27*1 4 6 4 6 a 27*1 4 6 4 6 a 27*1 4 6 4 6 a 27*1 4 6 4 6 a 27*1 4 6 4 6 a
  //   27*1 4 6 4 6 a 27*1 4 6 4 6 a 27*1 4 6 4 6 a 27*1 4 6 4 6 a 27*1 4 6 4 6 a 27*1 4 6 4 6 a 27*1 4 6 4
  //   6 a 27*1 4 6 4 6 a 27*1 4 6 4 6 a 27*1 4 6 4 6 a 27*1 4 6 4 6 a 27*1 4 6 4 6 a 27*1 4 6 4 6 a 27*1 4
  //   6 4 6 a 27*1 4 6 4 6 a 27*1 4 6 4 6 a 27*1 4 6 4 6 a 27*1 4 6 4 6 a 27*1 4 6 4 6 a 27*1 4 6 4 6 a
  //   27*1 4 6 4 6 a 27*1 4 6 4 6 a 27*1 4 6 4 6 a 27*1 4 6 4 6 a 27*1 4 6 4 6 a 27*1 4 6 4 6 a 27*1 4 6 4
  //   6 a 27*1 4 6 4 6 a 27*1 4 6 4 6 a 27*1 4 6 4 6 a 27*1 4 6 4 6 a 27*1 4 6 4 6 a 27*1 4 6 4 6 a 27*1 4
  //   6 4 6 a 27*1 4 6 4 6 a 27*1 4 6 4 6 a 27*1 4 6 4 6 a 27*1 4 6 4 6 a 27*1 4 6 4 6 a 27*1 4 6 4 6 a
  //   27*1 4 6 4 6 a 27*1 4 6 4 6 a 27*1 4 6 4 6 a 27*1 4 6 4 6 a 27*1 4 6 4 6 a 27*1 4 6 4 6 a 27*1 4 6 4
  //   6 a 27*1 4 6 4 6 a 27*1 4 6 4 6 a 27*1 4 6 4 6 a 27*1 4 6 4 6 a 27*1 4 6 4 6 a 27*1 4 6 4 6 a 27*1 4
  //   6 4 6 a 27*1 4 6 4 6 a 27*1 4 6 4 6 a 27*1 4 6 4 6 a 27*1 4 6 4 6 a 27*1 4 6 4 6 a 27*1 4 6 4 6 a
  //   27*1 4 6 4 6 a 27*1 4 6 4 6 a 27*1 4 6 4 6 a 27*1 4 6 4 6 a 27*1 4 6 4 6 a 27*1 4 6 4 6 a 27*1 4 6 4
  //   6 a 27*1 4 6 4 6 a 27*1 4 6 4 6 a 27*1 4 6 4 6 a 27*1 4 6 4 6 a 27*1 4 6 4 6 a 27*1 4 6 4 6 a 27*1 4
  //   6 4 6 a 27*1 4 6 4 6 a 27*1 4 6 4 6 a 27*1 4 6 4 6 a 27*1 4 6 4 6 a 27*1 4 6 4 6 a 27*1 4 6 4 6 a
  //   27*1 4 6 4 6 a 27*1 4 6 4 6 a 27*1 4 6 4 6 a 27*1 4 6 4 6 a 27*1 4 6 4 6 a 27*1 4 6 4 6 a 27*1 4 6 4
  //   6 a 27*1 4 6 4 6 a 27*1 4 6 4 6 a 27*1 4 6 4 6 a 27*1 4 6 4 6 a 27*1 4 6 4 6 a 27*1 4 6 4 6 a 27*1 4
  //   6 4 6 a 27*1 4 6 4 6 a 27*1 4 6 4 6 a 27*1 4 6 4 6 a 27*1 4 6 4 6 a 27*1 4 6 4 6 a 27*1 4 6 4 6 a
  //   27*1 4 6 4 6 a 27*1 4 6 4 6 a 27*1 4 6 4 6 a 27*1 4 6 4 6 a 27*1 4 6 4 6 a 27*1 4 6 4 6 a 27*1 4 6 4
  //   6 a 27*1 4 6 4 6 a 27*1 4 6 4 6 a 27*1 4 6 4 6 a 27*1 4 6 4 6 a 27*1 4 6 4 6 a 27*1 4 6 4 6 a 27*1 4
  //   6 4 6 a 27*1 4 6 4 6 a 27*1 4 6 4 6 a 27*1 4 6 4 6 a 27*1 4 6 4 6 a 27*1 4 6 4 6 a 27*1 4 6 4 6 a
  //   27*1 4 6 4 6 a 27*1 4 6 4 6 a 27*1 4 6 4 6 a 27*1 4 6 4 6 a 27*1 4 6 4 6 a 27*1 4 6 4 6 a 27*1 4 6 4
  //   6 a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
  //   contents of rom_3 (hex, n*v repeats v):
  //   61 c5 30*c1 61 c5 30*c1 61 c5 41 29*c1 61 c5 41 29*c1 61 c5 41 29*c1 61 c5 41 29*c1 61 c5 41 29*c1
  //   61 c5 41 29*c1 61 c5 41 29*c1 61 c5 41 29*c1 61 c5 41 29*c1 61 c5 41 285*c1 61 c5 61 c5 28*c1 61 c5
  //   61 c5 c1 c5 26*c1 61 c5 c1 c5 60*c1 61 c5 61 c5 28*c1 61 c5 61 c5 c1 c5 90*c1 61 c5 61 c5 c1 49
  //   58*c1 61 c5 61 c5 c0 c1 49 25*c1 61 c5 61 c5 c1 49 90*c1 61 c5 61 c5 c1 49 26*c1 61 c5 61 c5 156*c1
  //   61 c5 61 c5 c1 4b 26*c1 61 c5 61 c5 c1 4b 58*c1 61 c5 61 49 28*c1 61 c5 61 49 156*c1 61 c5 61 c1 c5
  //   27*c1 61 c5 61 c1 c5 155*c1 61 c5 61 c5 c0 c1 c5 121*c1 61 c5 41 c0 28*c1 61 c5 41 c0 60*c1 61 c5 61
  //   c5 c0 27*c1 61 c5 61 c5 c0 443*c1 61 c5 41 c0 28*c1 61 c5 41 c0 28*c1 61 c5 61 c5 c1 c5 c8 25*c1 61
  //   c5 41 c1 80 27*c1 61 c5 41 c1 80 27*c1 61 c5 61 c5 c1 c5 c1 88 88*c1 61 c5 51 29*c1 61 c5 61 93*c1
  //   61 c5 51 61*c1 61 c5 41 c0 28*c1 61 c5 61 c5 c0 27*c1 61 c5 61 c5 c0 27*c1 61 c5 61 c5 c0 59*c1 61
  //   c5 41 61*c1 61 c5 41 c0 28*c1 61 c5 41 c0 28*c1 61 c5 61 c5 c0 27*c1 61 c5 61 c5 c0 27*c1 61 c5 41
  //   c0 28*c1 61 c5 41 c0 28*c1 61 c5 61 c5 c0 27*c1 61 c5 61 c5 c0 4315*c1 61 c5 61 c5 28*c1 61 c5 61
  //   29*c1 61 c5 61 c5 28*c1 61 c5 61 69 61 c5 90*c1 61 c5 61 c1 c5 27*c1 61 c5 30*c1 61 c5 61 c1 c5
  //   27*c1 61 c5 61 c1 c5 61 c1 c5 24*c1 61 c5 c1 61 88 27*c1 61 c5 11 61 88 155*c1 61 c5 30*c1 61 c5
  //   30*c1 61 c5 41 29*c1 61 c5 41 29*c1 61 c5 41 29*c1 61 c5 41 29*c1 61 c5 41 29*c1 61 c5 41 29*c1 61
  //   c5 41 29*c1 61 c5 41 29*c1 61 c5 41 29*c1 61 c5 41 285*c1 61 c5 61 c5 28*c1 61 c5 61 c5 c1 c5 26*c1
  //   61 c5 c1 c5 60*c1 61 c5 61 c5 28*c1 61 c5 61 c5 c1 c5 90*c1 61 c5 61 c5 c1 49 58*c1 61 c5 61 c5 c0
  //   c1 49 25*c1 61 c5 61 c5 c1 49 90*c1 61 c5 61 c5 c1 49 26*c1 61 c5 61 c5 156*c1 61 c5 61 c5 c1 4b
  //   26*c1 61 c5 61 c5 c1 4b 58*c1 61 c5 61 49 28*c1 61 c5 61 49 156*c1 61 c5 61 c1 c5 27*c1 61 c5 61 c1
  //   c5 155*c1 61 c5 61 c5 c0 c1 c5 121*c1 61 c5 41 c0 28*c1 61 c5 41 c0 60*c1 61 c5 61 c5 c0 27*c1 61 c5
  //   61 c5 c0 443*c1 61 c5 41 c0 28*c1 61 c5 41 c0 28*c1 61 c5 61 c5 c1 c5 c8 25*c1 61 c5 41 c1 80 27*c1
  //   61 c5 41 c1 80 27*c1 61 c5 61 c5 c1 c5 c1 88 88*c1 61 c5 51 29*c1 61 c5 61 93*c1 61 c5 51 61*c1 61
  //   c5 41 c0 28*c1 61 c5 61 c5 c0 27*c1 61 c5 61 c5 c0 27*c1 61 c5 61 c5 c0 59*c1 61 c5 41 61*c1 61 c5
  //   41 c0 28*c1 61 c5 41 c0 28*c1 61 c5 61 c5 c0 27*c1 61 c5 61 c5 c0 27*c1 61 c5 41 c0 28*c1 61 c5 41
  //   c0 28*c1 61 c5 61 c5 c0 27*c1 61 c5 61 c5 c0 4315*c1 61 c5 61 c5 28*c1 61 c5 61 c5 28*c1 61 c5 61
  //   29*c1 61 c5 61 69 61 c5 90*c1 61 c5 61 c1 c5 27*c1 61 c5 61 c1 c5 27*c1 61 c5 30*c1 61 c5 61 c1 c5
  //   61 c1 c5 24*c1 61 c5 11 61 88 27*c1 61 c5 c1 61 88 156*c1 61 49 61 49 51 c1 c1 c5 24*c1 61 49 61 49
  //   51 c1 c1 c5 24*c1 61 49 61 49 51 c1 c1 c5 24*c1 61 49 61 49 51 c1 c1 c5 24*c1 61 49 61 49 51 c1 c1
  //   c5 24*c1 61 49 61 49 51 c1 c1 c5 24*c1 61 49 61 49 51 c1 c1 c5 24*c1 61 49 61 49 51 c1 c1 c5 24*c1
  //   61 49 61 49 51 c1 c1 c5 24*c1 61 49 61 49 51 c1 c1 c5 24*c1 61 49 61 49 51 c1 c1 c5 24*c1 61 49 61
  //   49 51 c1 c1 c5 24*c1 61 49 61 49 51 c1 c1 c5 24*c1 61 49 61 49 51 c1 c1 c5 24*c1 61 49 61 49 51 c1
  //   c1 c5 24*c1 61 49 61 49 51 c1 c1 c5 24*c1 61 49 61 49 51 c1 c1 c5 24*c1 61 49 61 49 51 c1 c1 c5
  //   24*c1 61 49 61 49 51 c1 c1 c5 24*c1 61 49 61 49 51 c1 c1 c5 24*c1 61 49 61 49 51 c1 c1 c5 24*c1 61
  //   49 61 49 51 c1 c1 c5 24*c1 61 49 61 49 51 c1 c1 c5 24*c1 61 49 61 49 51 c1 c1 c5 24*c1 61 49 61 49
  //   51 c1 c1 c5 24*c1 61 49 61 49 51 c1 c1 c5 24*c1 61 49 61 49 51 c1 c1 c5 24*c1 61 49 61 49 51 c1 c1
  //   c5 24*c1 61 49 61 49 51 c1 c1 c5 24*c1 61 49 61 49 51 c1 c1 c5 24*c1 61 49 61 49 51 c1 c1 c5 24*c1
  //   61 49 61 49 51 c1 c1 c5 24*c1 61 49 61 49 51 c1 c1 c5 24*c1 61 49 61 49 51 c1 c1 c5 24*c1 61 49 61
  //   49 51 c1 c1 c5 24*c1 61 49 61 49 51 c1 c1 c5 24*c1 61 49 61 49 51 c1 c1 c5 24*c1 61 49 61 49 51 c1
  //   c1 c5 24*c1 61 49 61 49 51 c1 c1 c5 24*c1 61 49 61 49 51 c1 c1 c5 24*c1 61 49 61 49 51 c1 c1 c5
  //   24*c1 61 49 61 49 51 c1 c1 c5 24*c1 61 49 61 49 51 c1 c1 c5 24*c1 61 49 61 49 51 c1 c1 c5 24*c1 61
  //   49 61 49 51 c1 c1 c5 24*c1 61 49 61 49 51 c1 c1 c5 24*c1 61 49 61 49 51 c1 c1 c5 24*c1 61 49 61 49
  //   51 c1 c1 c5 24*c1 61 49 61 49 51 c1 c1 c5 24*c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
  //   contents of rom_4 (hex, n*v repeats v):
  //   a4 9c c 29*8c a4 8c cc 9c c 27*8c a4 8c 9c c 28*8c a4 8c 9c c 28*8c a4 8c 9c c 28*8c a4 8c 9c c
  //   28*8c a4 8c 9c c 28*8c a4 8c 9c c 28*8c a4 8c 9c c 28*8c a4 8c 9c c 28*8c a4 8c 9c c 28*8c a4 8c 9c
  //   c 284*8c a4 8c 8c 9c c 27*8c a4 4*8c 9c c 25*8c a4 8c 8c 9c c 59*8c a4 8c 8c 9c c 27*8c a4 4*8c 9c c
  //   89*8c a4 4*8c 9c c 57*8c a4 5*8c 9c c 24*8c a4 4*8c 9c c 89*8c a4 4*8c 9d c 25*8c a4 8c 8c 9c c
  //   155*8c a4 4*8c 9c c 25*8c a4 4*8c 9d c 57*8c a4 8c 8c 9c c 27*8c a4 8c 8c 9c c 155*8c a4 8c 8c 8c 9c
  //   c 26*8c a4 8c 8c 8c 9c c 154*8c a4 5*8c 9c c 120*8c a4 8c 8c 9c c 27*8c a4 8c 8c 9c c 59*8c a4 8c 8c
  //   8c 9c c 26*8c a4 8c 8c 8c 9c c 442*8c a4 8c 8c 9c c 27*8c a4 8c 8c 9c c 27*8c a4 5*8c 9c c 24*8c a4
  //   8c 8c 8c 9c c 26*8c a4 8c 8c 8c 9c c 26*8c a4 6*8c 9c c 87*8c a4 8c 9c c 28*8c a4 8c 9c c 92*8c a4
  //   8c 9c c 60*8c a4 8c 8c 9c c 27*8c a4 8c 8c 8c 9c c 26*8c a4 8c 8c 8c 9c c 26*8c a4 8c 8c 8c 9c c
  //   58*8c a4 8c 9c c 60*8c a4 8c 8c 9c c 27*8c a4 8c 8c 9c c 27*8c a4 8c 8c 8c 9c c 26*8c a4 8c 8c 8c 9c
  //   c 26*8c a4 8c 8c 9c c 27*8c a4 8c 8c 9c c 27*8c a4 8c 8c 8c 9c c 26*8c a4 8c 8c 8c 9c c 4314*8c a4
  //   8c 8c 9c c 27*8c a4 8c 9c c 28*8c a4 8c 8c 9c c 27*8c a4 4*8c 9c c 89*8c a4 8c 8c 8c 9c c 26*8c a4
  //   8c 9c c 28*8c a4 8c 8c 8c 9c c 26*8c a4 6*8c 9c c 23*8c a4 8c 8c 8c 9c c 26*8c a4 8c 8c 8c 9c c
  //   154*8c a4 9c c 29*8c a4 8c cc 9c c 27*8c a4 8c 9c c 28*8c a4 8c 9c c 28*8c a4 8c 9c c 28*8c a4 8c 9c
  //   c 28*8c a4 8c 9c c 28*8c a4 8c 9c c 28*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
endmodule

module Control_Unit__principle (
  input  CLK,
  input  [7:0] Instruction_L,
  input  [3:0] Flags,
  input  [7:0] Instruction_H,
  input  [2:0] RST_NMI_IRQ,
  output OE0,
  output OE1,
  output OE2,
  output IE0,
  output IE1,
  output IE2,
  output INSTRUCTION_IE,
  output MAR_IE,
  output nALU_OE,
  output ALU0,
  output ALU1,
  output ALU2,
  output F_IE,
  output CARRY,
  output nTEMP_OE,
  output TEMP_IE,
  output IO__M,
  output RE,
  output BE0,
  output BE1,
  output IMM0,
  output IMM1,
  output nIMM_R_OE,
  output nIMM_L_OE,
  output out_30,
  output INTA
);

  wire clear, halt, INT_IE, INT_LATCH, interrupt_sample_register_1_irq, interrupt_sample_register_1_nmi,
       interrupt_sample_register_1_rst, n7477_1_q0, n7477_1_q1, n7477_1_q2, nINT_OE;
  wire [1:0] priority_encoder_1_out;
  wire [4:0] counter_1_q;
  wire [13:13] multiplexer_1_out;
  wire [29:29] rom_1_data;

  Interrupt_Sample_Register interrupt_sample_register_1 (
    .RST_NMI_IRQ(RST_NMI_IRQ), .nOE(nINT_OE), .IE(INT_IE), .CLK(CLK), .IRQ(interrupt_sample_register_1_irq),
    .NMI(interrupt_sample_register_1_nmi), .RST(interrupt_sample_register_1_rst));
  Counter #(.width(5), .max('h1f), .trigger("falling")) counter_1 (
    .Q(counter_1_q), .clk(CLK), .clr(clear));  // open: load, D, count, carry
  Multiplexer #(.select(2), .disabled(0), .enable("false")) multiplexer_1 (
    .in0(Flags[0]), .in1(Flags[1]), .in2(Flags[2]), .in3(Flags[3]), .out(multiplexer_1_out[13]),
    .sel(Instruction_H[7:6]));
  _7477 u_7477_1 (
    .D0(interrupt_sample_register_1_irq), .D1(interrupt_sample_register_1_nmi),
    .D2(interrupt_sample_register_1_rst), .Q0(n7477_1_q0), .E0_1(INT_LATCH), .Q1(n7477_1_q1),
    .Q2(n7477_1_q2), .E2_3(INT_LATCH));  // open: D3, Q3
  Priority_Encoder #(.select(2)) priority_encoder_1 (
    .in0(1'b1), .in1(n7477_1_q0), .in2(n7477_1_q1), .in3(n7477_1_q2), .out(priority_encoder_1_out));  // open: gs, en_out, en_in
  ROM #(.addrWidth(16), .dataWidth(32)) rom_1 (
    .addr({priority_encoder_1_out, multiplexer_1_out[13], Instruction_L, counter_1_q}),
    .data({clear, halt, rom_1_data[29], INTA, out_30, INT_LATCH, INT_IE, nINT_OE, nIMM_L_OE, nIMM_R_OE, IMM1, IMM0, BE1, BE0, RE, IO__M, TEMP_IE, nTEMP_OE, CARRY, F_IE, ALU2, ALU1, ALU0, nALU_OE, MAR_IE, INSTRUCTION_IE, IE2, IE1, IE0, OE2, OE1, OE0}),
    .sel(1'b1));

  // Notes on the sheet:
  //   TODO: HLT CIRCUIT
  //   The MPU samples the INTR at the last clock period of each instruction execution cycle. Its active high level must be maintained.
  //   contents of rom_1 (hex, n*v repeats v):
  //   46046a4 3c24140 81c04100 29*1c04100 46046a4 1c24140 3404611 81c04100 28*1c04100 46046a4 1c24140
  //   3404619 81c04100 28*1c04100 46046a4 1c24140 3404621 81c04100 28*1c04100 46046a4 1c24140 3404629
  //   81c04100 28*1c04100 46046a4 1c24140 3404631 81c04100 28*1c04100 46046a4 1c24140 340460a 81c04100
  //   28*1c04100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
endmodule

module IRQ_Controller (
  input  INTE,
  input  IRQ5,
  input  IRQ4,
  input  IRQ3,
  input  IRQ2,
  input  IRQ1,
  input  IRQ0,
  input  IRQ7,
  input  IRQ6,
  input  [7:0] INTM,
  input  INTA,
  input  INT_IE,
  output IRQ,
  output [15:0] DATABUS
);

  wire and_1_out, and_2_out, and_3_out, and_4_out, and_5_out, and_6_out, and_7_out, and_8_out, and_9_out,
       and_10_out, and_11_out, CLR0, CLR1, CLR2, CLR3, CLR4, CLR5, CLR6, CLR7, n7474_dual_d_ffs_1_q1,
       n7474_dual_d_ffs_1_q2, n7474_dual_d_ffs_2_q1, n7474_dual_d_ffs_2_q2, n7474_dual_d_ffs_3_q1,
       n7474_dual_d_ffs_3_q2, n7474_dual_d_ffs_4_q1, n7474_dual_d_ffs_4_q2, n7475_quad_latches_1_q0_2,
       n7475_quad_latches_1_q1_2, n7475_quad_latches_1_q2_2, n7475_quad_latches_1_q2_3,
       n7475_quad_latches_2_q0_2, n7475_quad_latches_2_q1_2, n7475_quad_latches_2_q2_2,
       n7475_quad_latches_2_q2_3, n74138_1_y2, n74138_1_y3, n74138_1_y4, n74138_1_y5, n74138_1_y6,
       n74138_1_y7, n74138_2_y0, n74138_2_y1, n74148_1_a0__9, n74148_1_a1__7, n74148_1_a2__6,
       n74148_1_eo__15, n74148_1_g5__14, n74148_2_a0__9, n74148_2_a1__7, n74148_2_a2__6, n74148_2_g5__14,
       nand_1_out, not_1_out;

  and and_1 (and_1_out, IRQ5, INTM[5]);
  and and_2 (and_2_out, IRQ4, INTM[4]);
  and and_3 (and_3_out, IRQ3, INTM[3]);
  and and_4 (and_4_out, IRQ2, INTM[2]);
  and and_5 (and_5_out, IRQ1, INTM[1]);
  and and_6 (and_6_out, IRQ0, INTM[0]);
  and and_7 (and_7_out, IRQ7, INTM[7]);
  and and_8 (and_8_out, IRQ6, INTM[6]);
  _7474_Dual_D_FFs u_7474_dual_d_ffs_1 (
    .PRE1(1'b1), .CLR1(CLR5), .CLK1(and_1_out), .D1(1'b1), .PRE2(1'b1), .CLR2(CLR4), .CLK2(and_2_out),
    .D2(1'b1), .Q1(n7474_dual_d_ffs_1_q1), .Q2(n7474_dual_d_ffs_1_q2));  // open: Q1_2, Q2_2
  _7474_Dual_D_FFs u_7474_dual_d_ffs_2 (
    .PRE1(1'b1), .CLR1(CLR3), .CLK1(and_3_out), .D1(1'b1), .PRE2(1'b1), .CLR2(CLR2), .CLK2(and_4_out),
    .D2(1'b1), .Q1(n7474_dual_d_ffs_2_q1), .Q2(n7474_dual_d_ffs_2_q2));  // open: Q1_2, Q2_2
  _7474_Dual_D_FFs u_7474_dual_d_ffs_3 (
    .PRE1(1'b1), .CLR1(CLR1), .CLK1(and_5_out), .D1(1'b1), .PRE2(1'b1), .CLR2(CLR0), .CLK2(and_6_out),
    .D2(1'b1), .Q1(n7474_dual_d_ffs_3_q1), .Q2(n7474_dual_d_ffs_3_q2));  // open: Q1_2, Q2_2
  _7474_Dual_D_FFs u_7474_dual_d_ffs_4 (
    .PRE1(1'b1), .CLR1(CLR7), .CLK1(and_7_out), .D1(1'b1), .PRE2(1'b1), .CLR2(CLR6), .CLK2(and_8_out),
    .D2(1'b1), .Q1(n7474_dual_d_ffs_4_q1), .Q2(n7474_dual_d_ffs_4_q2));  // open: Q1_2, Q2_2
  _7475_Quad_Latches u_7475_quad_latches_1 (
    .D0(n7474_dual_d_ffs_1_q1), .D1(n7474_dual_d_ffs_1_q2), .D2(n7474_dual_d_ffs_2_q1),
    .D3(n7474_dual_d_ffs_2_q2), .Q0_2(n7475_quad_latches_1_q0_2), .E0_1(INT_IE),
    .Q1_2(n7475_quad_latches_1_q1_2), .Q2_2(n7475_quad_latches_1_q2_2), .E2_3(INT_IE),
    .Q2_3(n7475_quad_latches_1_q2_3));  // open: Q0, Q1, Q2, Q3
  _7475_Quad_Latches u_7475_quad_latches_2 (
    .D0(n7474_dual_d_ffs_3_q1), .D1(n7474_dual_d_ffs_3_q2), .D2(n7474_dual_d_ffs_4_q1),
    .D3(n7474_dual_d_ffs_4_q2), .Q0_2(n7475_quad_latches_2_q0_2), .E0_1(INT_IE),
    .Q1_2(n7475_quad_latches_2_q1_2), .Q2_2(n7475_quad_latches_2_q2_2), .E2_3(INT_IE),
    .Q2_3(n7475_quad_latches_2_q2_3));  // open: Q0, Q1, Q2, Q3
  or or_1 (CLR5, n74138_1_y7, INTA);
  or or_2 (CLR4, n74138_1_y6, INTA);
  or or_3 (CLR3, n74138_1_y5, INTA);
  or or_4 (CLR2, n74138_1_y4, INTA);
  or or_5 (CLR1, n74138_1_y3, INTA);
  or or_6 (CLR0, n74138_1_y2, INTA);
  or or_7 (CLR7, n74138_2_y1, INTA);
  or or_8 (CLR6, n74138_2_y0, INTA);
  _74148 u_74148_1 (
    ._0__10(n7475_quad_latches_1_q0_2), ._1__11(n7475_quad_latches_1_q1_2),
    ._2__12(n7475_quad_latches_1_q2_2), ._3__13(n7475_quad_latches_1_q2_3),
    ._4__1(n7475_quad_latches_2_q0_2), ._5__2(n7475_quad_latches_2_q1_2), ._6__3(1'b1), ._7__4(1'b1),
    .EI__5(1'b0), .EO__15(n74148_1_eo__15), .G5__14(n74148_1_g5__14), .A0__9(n74148_1_a0__9),
    .A1__7(n74148_1_a1__7), .A2__6(n74148_1_a2__6));
  _74148 u_74148_2 (
    ._0__10(1'b1), ._1__11(1'b1), ._2__12(1'b1), ._3__13(1'b1), ._4__1(1'b1), ._5__2(1'b1),
    ._6__3(n7475_quad_latches_2_q2_2), ._7__4(n7475_quad_latches_2_q2_3), .EI__5(n74148_1_eo__15),
    .G5__14(n74148_2_g5__14), .A0__9(n74148_2_a0__9), .A1__7(n74148_2_a1__7), .A2__6(n74148_2_a2__6));  // open: EO__15
  _74138 u_74138_1 (
    .nE1(1'b0), .nE2(n74148_1_g5__14), .E3(1'b1), .A0(and_9_out), .A1(and_10_out), .A2(and_11_out),
    .Y2(n74138_1_y2), .Y3(n74138_1_y3), .Y4(n74138_1_y4), .Y5(n74138_1_y5), .Y6(n74138_1_y6), .Y7(n74138_1_y7));  // open: Y0, Y1
  _74138 u_74138_2 (
    .nE1(1'b0), .nE2(1'b0), .E3(n74148_1_g5__14), .A0(and_9_out), .A1(and_10_out), .A2(and_11_out),
    .Y0(n74138_2_y0), .Y1(n74138_2_y1));  // open: Y2, Y3, Y4, Y5, Y6, Y7
  not not_1 (not_1_out, INTE);
  nand nand_1 (nand_1_out, n74148_1_g5__14, n74148_2_g5__14);
  and and_9 (and_9_out, n74148_1_a0__9, n74148_2_a0__9);
  and and_10 (and_10_out, n74148_1_a1__7, n74148_2_a1__7);
  and and_11 (and_11_out, n74148_1_a2__6, n74148_2_a2__6);
  and and_12 (IRQ, not_1_out, nand_1_out);
  _74541 u_74541_1 (
    .A2(and_9_out), .A3(and_10_out), .A4(and_11_out), .A5(n74148_1_g5__14), .nOE1(INTA), .nOE2(INTA),
    .Y1(DATABUS[1]), .Y2(DATABUS[2]), .Y3(DATABUS[3]), .Y4(DATABUS[4]));  // open: A0, A6, A7, A8, Y0, Y5, Y6, Y7

  // Other names for the same wires on the sheet: M0 = INTM[0]; M1 = INTM[1]; M2 = INTM[2]; M3 = INTM[3]; M4 = INTM[4];
  //   M5 = INTM[5]; M6 = INTM[6]; M7 = INTM[7]

  // Notes on the sheet:
  //   From MSW
  //   From INTE flag (MSW)
  //   From Control Unit
  //   PULL DOWNS ON DATABUS ASSUMED
endmodule

module Register_8bit (
  input  [7:0] D,
  input  nOE,
  input  CLK,
  output [7:0] Q
);

  wire bus_to_8bit_1_out_2, bus_to_8bit_1_out_3, bus_to_8bit_1_out_4, bus_to_8bit_1_out_5,
       bus_to_8bit_1_out_6, bus_to_8bit_1_out_7, bus_to_8bit_1_out_8, bus_to_8bit_1_out_9,
       n74574_8x_d_flip_flop_1_q0, n74574_8x_d_flip_flop_1_q1, n74574_8x_d_flip_flop_1_q2,
       n74574_8x_d_flip_flop_1_q3, n74574_8x_d_flip_flop_1_q4, n74574_8x_d_flip_flop_1_q5,
       n74574_8x_d_flip_flop_1_q6, n74574_8x_d_flip_flop_1_q7;

  _74574___8x_D_Flip_Flop u_74574_8x_d_flip_flop_1 (
    .Clk(CLK), .nOE(nOE), .D0(bus_to_8bit_1_out_2), .D1(bus_to_8bit_1_out_3), .D2(bus_to_8bit_1_out_4),
    .D3(bus_to_8bit_1_out_5), .D4(bus_to_8bit_1_out_6), .D5(bus_to_8bit_1_out_7), .D6(bus_to_8bit_1_out_8),
    .D7(bus_to_8bit_1_out_9), .Q0(n74574_8x_d_flip_flop_1_q0), .Q1(n74574_8x_d_flip_flop_1_q1),
    .Q2(n74574_8x_d_flip_flop_1_q2), .Q3(n74574_8x_d_flip_flop_1_q3), .Q4(n74574_8x_d_flip_flop_1_q4),
    .Q5(n74574_8x_d_flip_flop_1_q5), .Q6(n74574_8x_d_flip_flop_1_q6), .Q7(n74574_8x_d_flip_flop_1_q7));
  bus_to_8bit bus_to_8bit_1 (
    .in_1(D), .out_2(bus_to_8bit_1_out_2), .out_3(bus_to_8bit_1_out_3), .out_4(bus_to_8bit_1_out_4),
    .out_5(bus_to_8bit_1_out_5), .out_6(bus_to_8bit_1_out_6), .out_7(bus_to_8bit_1_out_7),
    .out_8(bus_to_8bit_1_out_8), .out_9(bus_to_8bit_1_out_9));
  _8bit_to_bus u_8bit_to_bus_1 (
    .in_1(n74574_8x_d_flip_flop_1_q0), .in_2(n74574_8x_d_flip_flop_1_q1), .in_3(n74574_8x_d_flip_flop_1_q2),
    .in_4(n74574_8x_d_flip_flop_1_q3), .in_5(n74574_8x_d_flip_flop_1_q4), .in_6(n74574_8x_d_flip_flop_1_q5),
    .in_7(n74574_8x_d_flip_flop_1_q6), .in_8(n74574_8x_d_flip_flop_1_q7), .out_9(Q));
endmodule

module Buffer_tri_state_16bit (
  input  [15:0] IN,
  input  nOE,
  output [15:0] OUT
);

  wire bus_to_8bit_1_out_2, bus_to_8bit_1_out_3, bus_to_8bit_1_out_4, bus_to_8bit_1_out_5,
       bus_to_8bit_1_out_6, bus_to_8bit_1_out_7, bus_to_8bit_1_out_8, bus_to_8bit_1_out_9,
       bus_to_8bit_2_out_2, bus_to_8bit_2_out_3, bus_to_8bit_2_out_4, bus_to_8bit_2_out_5,
       bus_to_8bit_2_out_6, bus_to_8bit_2_out_7, bus_to_8bit_2_out_8, bus_to_8bit_2_out_9, n74541_1_y0,
       n74541_1_y1, n74541_1_y2, n74541_1_y3, n74541_1_y4, n74541_1_y5, n74541_1_y6, n74541_1_y7,
       n74541_2_y0, n74541_2_y1, n74541_2_y2, n74541_2_y3, n74541_2_y4, n74541_2_y5, n74541_2_y6, n74541_2_y7;

  _74541 u_74541_1 (
    .A0(bus_to_8bit_1_out_2), .A2(bus_to_8bit_1_out_3), .A3(bus_to_8bit_1_out_4), .A4(bus_to_8bit_1_out_5),
    .A5(bus_to_8bit_1_out_6), .A6(bus_to_8bit_1_out_7), .A7(bus_to_8bit_1_out_8), .A8(bus_to_8bit_1_out_9),
    .nOE1(nOE), .nOE2(nOE), .Y0(n74541_1_y0), .Y1(n74541_1_y1), .Y2(n74541_1_y2), .Y3(n74541_1_y3),
    .Y4(n74541_1_y4), .Y5(n74541_1_y5), .Y6(n74541_1_y6), .Y7(n74541_1_y7));
  bus_to_8bit bus_to_8bit_1 (
    .in_1(IN[7:0]), .out_2(bus_to_8bit_1_out_2), .out_3(bus_to_8bit_1_out_3), .out_4(bus_to_8bit_1_out_4),
    .out_5(bus_to_8bit_1_out_5), .out_6(bus_to_8bit_1_out_6), .out_7(bus_to_8bit_1_out_7),
    .out_8(bus_to_8bit_1_out_8), .out_9(bus_to_8bit_1_out_9));
  _74541 u_74541_2 (
    .A0(bus_to_8bit_2_out_2), .A2(bus_to_8bit_2_out_3), .A3(bus_to_8bit_2_out_4), .A4(bus_to_8bit_2_out_5),
    .A5(bus_to_8bit_2_out_6), .A6(bus_to_8bit_2_out_7), .A7(bus_to_8bit_2_out_8), .A8(bus_to_8bit_2_out_9),
    .nOE1(nOE), .nOE2(nOE), .Y0(n74541_2_y0), .Y1(n74541_2_y1), .Y2(n74541_2_y2), .Y3(n74541_2_y3),
    .Y4(n74541_2_y4), .Y5(n74541_2_y5), .Y6(n74541_2_y6), .Y7(n74541_2_y7));
  bus_to_8bit bus_to_8bit_2 (
    .in_1(IN[15:8]), .out_2(bus_to_8bit_2_out_2), .out_3(bus_to_8bit_2_out_3), .out_4(bus_to_8bit_2_out_4),
    .out_5(bus_to_8bit_2_out_5), .out_6(bus_to_8bit_2_out_6), .out_7(bus_to_8bit_2_out_7),
    .out_8(bus_to_8bit_2_out_8), .out_9(bus_to_8bit_2_out_9));
  _8bit_to_bus u_8bit_to_bus_1 (
    .in_1(n74541_1_y0), .in_2(n74541_1_y1), .in_3(n74541_1_y2), .in_4(n74541_1_y3), .in_5(n74541_1_y4),
    .in_6(n74541_1_y5), .in_7(n74541_1_y6), .in_8(n74541_1_y7), .out_9(OUT[7:0]));
  _8bit_to_bus u_8bit_to_bus_2 (
    .in_1(n74541_2_y0), .in_2(n74541_2_y1), .in_3(n74541_2_y2), .in_4(n74541_2_y3), .in_5(n74541_2_y4),
    .in_6(n74541_2_y5), .in_7(n74541_2_y6), .in_8(n74541_2_y7), .out_9(OUT[15:8]));
endmodule

module Buffer_tri_state_8bit (
  input  [7:0] IN,
  input  OE,
  output [7:0] OUT
);

  wire bus_to_8bit_1_out_2, bus_to_8bit_1_out_3, bus_to_8bit_1_out_4, bus_to_8bit_1_out_5,
       bus_to_8bit_1_out_6, bus_to_8bit_1_out_7, bus_to_8bit_1_out_8, bus_to_8bit_1_out_9, n74541_1_y0,
       n74541_1_y1, n74541_1_y2, n74541_1_y3, n74541_1_y4, n74541_1_y5, n74541_1_y6, n74541_1_y7;

  _74541 u_74541_1 (
    .A0(bus_to_8bit_1_out_2), .A2(bus_to_8bit_1_out_3), .A3(bus_to_8bit_1_out_4), .A4(bus_to_8bit_1_out_5),
    .A5(bus_to_8bit_1_out_6), .A6(bus_to_8bit_1_out_7), .A7(bus_to_8bit_1_out_8), .A8(bus_to_8bit_1_out_9),
    .nOE1(OE), .nOE2(OE), .Y0(n74541_1_y0), .Y1(n74541_1_y1), .Y2(n74541_1_y2), .Y3(n74541_1_y3),
    .Y4(n74541_1_y4), .Y5(n74541_1_y5), .Y6(n74541_1_y6), .Y7(n74541_1_y7));
  bus_to_8bit bus_to_8bit_1 (
    .in_1(IN), .out_2(bus_to_8bit_1_out_2), .out_3(bus_to_8bit_1_out_3), .out_4(bus_to_8bit_1_out_4),
    .out_5(bus_to_8bit_1_out_5), .out_6(bus_to_8bit_1_out_6), .out_7(bus_to_8bit_1_out_7),
    .out_8(bus_to_8bit_1_out_8), .out_9(bus_to_8bit_1_out_9));
  _8bit_to_bus u_8bit_to_bus_1 (
    .in_1(n74541_1_y0), .in_2(n74541_1_y1), .in_3(n74541_1_y2), .in_4(n74541_1_y3), .in_5(n74541_1_y4),
    .in_6(n74541_1_y5), .in_7(n74541_1_y6), .in_8(n74541_1_y7), .out_9(OUT));
endmodule

module Decode_2 (
  input  [2:0] OE,
  input  [2:0] IE,
  input  CLK,
  input  DMA_CLK,
  input  FLAGS_IE,
  input  INSTRUCTION_IE,
  input  MAR_IE,
  output [7:0] out_8,
  output [7:0] out_9,
  output FLAGS_CLK,
  output INSTRUCTION_CLK,
  output MAR_CLK
);

  wire n74138_1_y0, n74138_1_y1, n74138_1_y2, n74138_1_y3, n74138_1_y4, n74138_1_y5, n74138_1_y6,
       n74138_1_y7, n74238_1_y0, n74238_1_y1, n74238_1_y2, n74238_1_y3, n74238_1_y4, n74238_1_y5,
       n74238_1_y6, n74238_1_y7, or_1_out;

  or or_1 (or_1_out, CLK, DMA_CLK);
  and and_1 (FLAGS_CLK, CLK, FLAGS_IE);
  and and_2 (INSTRUCTION_CLK, CLK, INSTRUCTION_IE);
  and and_3 (MAR_CLK, CLK, MAR_IE);
  _74138 u_74138_1 (
    .nE1(1'b0), .nE2(1'b0), .E3(1'b1), .A0(OE[0]), .A1(OE[1]), .A2(OE[2]), .Y0(n74138_1_y0),
    .Y1(n74138_1_y1), .Y2(n74138_1_y2), .Y3(n74138_1_y3), .Y4(n74138_1_y4), .Y5(n74138_1_y5),
    .Y6(n74138_1_y6), .Y7(n74138_1_y7));
  _74238 u_74238_1 (
    .A0(IE[0]), .A1(IE[1]), .A2(IE[2]), .nE1(1'b0), .nE2(1'b0), .E3(or_1_out), .Y0(n74238_1_y0),
    .Y1(n74238_1_y1), .Y2(n74238_1_y2), .Y3(n74238_1_y3), .Y4(n74238_1_y4), .Y5(n74238_1_y5),
    .Y6(n74238_1_y6), .Y7(n74238_1_y7));
  _8bit_to_bus u_8bit_to_bus_1 (
    .in_1(n74138_1_y0), .in_2(n74138_1_y1), .in_3(n74138_1_y2), .in_4(n74138_1_y3), .in_5(n74138_1_y4),
    .in_6(n74138_1_y5), .in_7(n74138_1_y6), .in_8(n74138_1_y7), .out_9(out_8));
  _8bit_to_bus u_8bit_to_bus_2 (
    .in_1(n74238_1_y0), .in_2(n74238_1_y1), .in_3(n74238_1_y2), .in_4(n74238_1_y3), .in_5(n74238_1_y4),
    .in_6(n74238_1_y5), .in_7(n74238_1_y6), .in_8(n74238_1_y7), .out_9(out_9));
endmodule

module Immediate_Register (
  input  [1:0] D,
  input  nOE,
  output [15:0] Q
);

  wire n74541_1_y0, n74541_1_y1, n74541_1_y2, n74541_1_y3, n74541_1_y4, n74541_1_y5, n74541_1_y6,
       n74541_1_y7, n74541_2_y0, n74541_2_y1, n74541_2_y2, n74541_2_y3, n74541_2_y4, n74541_2_y5,
       n74541_2_y6, n74541_2_y7;

  _74541 u_74541_1 (
    .A0(D[0]), .A2(D[1]), .A3(1'b0), .A4(1'b0), .A5(1'b0), .A6(1'b0), .A7(1'b0), .A8(1'b0), .nOE1(nOE),
    .nOE2(nOE), .Y0(n74541_1_y0), .Y1(n74541_1_y1), .Y2(n74541_1_y2), .Y3(n74541_1_y3), .Y4(n74541_1_y4),
    .Y5(n74541_1_y5), .Y6(n74541_1_y6), .Y7(n74541_1_y7));
  _74541 u_74541_2 (
    .A0(1'b0), .A2(1'b0), .A3(1'b0), .A4(1'b0), .A5(1'b0), .A6(1'b0), .A7(1'b0), .A8(1'b0), .nOE1(nOE),
    .nOE2(nOE), .Y0(n74541_2_y0), .Y1(n74541_2_y1), .Y2(n74541_2_y2), .Y3(n74541_2_y3), .Y4(n74541_2_y4),
    .Y5(n74541_2_y5), .Y6(n74541_2_y6), .Y7(n74541_2_y7));
  _8bit_to_bus u_8bit_to_bus_1 (
    .in_1(n74541_1_y0), .in_2(n74541_1_y1), .in_3(n74541_1_y2), .in_4(n74541_1_y3), .in_5(n74541_1_y4),
    .in_6(n74541_1_y5), .in_7(n74541_1_y6), .in_8(n74541_1_y7), .out_9(Q[7:0]));
  _8bit_to_bus u_8bit_to_bus_2 (
    .in_1(n74541_2_y0), .in_2(n74541_2_y1), .in_3(n74541_2_y2), .in_4(n74541_2_y3), .in_5(n74541_2_y4),
    .in_6(n74541_2_y5), .in_7(n74541_2_y6), .in_8(n74541_2_y7), .out_9(Q[15:8]));
endmodule

module MSW (
  input  nOE,
  input  Flags_CLK,
  input  CLK,
  input  [15:0] IN,
  input  [4:0] Flags_IN,
  output INTE,
  output [15:0] OUT,
  output [4:0] Flags_OUT,
  output [7:0] INTM
);

  wire bus_to_8bit_1_out_2, bus_to_8bit_1_out_3, bus_to_8bit_1_out_4, bus_to_8bit_2_out_2,
       bus_to_8bit_2_out_3, bus_to_8bit_2_out_4, bus_to_8bit_2_out_5, bus_to_8bit_2_out_6,
       bus_to_8bit_2_out_7, bus_to_8bit_2_out_8, bus_to_8bit_2_out_9, n74541_1_y0, n74541_1_y1, n74541_1_y2,
       n74541_1_y3, n74541_1_y4, n74541_1_y5, n74541_1_y6, n74541_1_y7, n74541_2_y0, n74541_2_y1,
       n74541_2_y2, n74541_2_y3, n74541_2_y4, n74541_2_y5, n74541_2_y6, n74541_2_y7,
       n74574_8x_d_flip_flop_1_q0, n74574_8x_d_flip_flop_1_q1, n74574_8x_d_flip_flop_1_q2,
       n74574_8x_d_flip_flop_1_q3, n74574_8x_d_flip_flop_1_q4, n74574_8x_d_flip_flop_1_q5,
       n74574_8x_d_flip_flop_1_q6, n74574_8x_d_flip_flop_1_q7, n74574_8x_d_flip_flop_2_q1,
       n74574_8x_d_flip_flop_2_q2;

  bus_to_8bit bus_to_8bit_1 (
    .in_1(IN[7:0]), .out_2(bus_to_8bit_1_out_2), .out_3(bus_to_8bit_1_out_3), .out_4(bus_to_8bit_1_out_4));  // open: out_5, out_6, out_7, out_8, out_9
  _74574___8x_D_Flip_Flop u_74574_8x_d_flip_flop_1 (
    .Clk(CLK), .nOE(1'b0), .D0(bus_to_8bit_2_out_2), .D1(bus_to_8bit_2_out_3), .D2(bus_to_8bit_2_out_4),
    .D3(bus_to_8bit_2_out_5), .D4(bus_to_8bit_2_out_6), .D5(bus_to_8bit_2_out_7), .D6(bus_to_8bit_2_out_8),
    .D7(bus_to_8bit_2_out_9), .Q0(n74574_8x_d_flip_flop_1_q0), .Q1(n74574_8x_d_flip_flop_1_q1),
    .Q2(n74574_8x_d_flip_flop_1_q2), .Q3(n74574_8x_d_flip_flop_1_q3), .Q4(n74574_8x_d_flip_flop_1_q4),
    .Q5(n74574_8x_d_flip_flop_1_q5), .Q6(n74574_8x_d_flip_flop_1_q6), .Q7(n74574_8x_d_flip_flop_1_q7));
  bus_to_8bit bus_to_8bit_2 (
    .in_1(IN[15:8]), .out_2(bus_to_8bit_2_out_2), .out_3(bus_to_8bit_2_out_3), .out_4(bus_to_8bit_2_out_4),
    .out_5(bus_to_8bit_2_out_5), .out_6(bus_to_8bit_2_out_6), .out_7(bus_to_8bit_2_out_7),
    .out_8(bus_to_8bit_2_out_8), .out_9(bus_to_8bit_2_out_9));
  _74574___8x_D_Flip_Flop u_74574_8x_d_flip_flop_2 (
    .Clk(CLK), .nOE(1'b0), .D0(bus_to_8bit_1_out_2), .D1(bus_to_8bit_1_out_3), .D2(bus_to_8bit_1_out_4),
    .D3(1'b0), .D4(1'b0), .D5(1'b0), .D6(1'b0), .D7(1'b0), .Q0(INTE), .Q1(n74574_8x_d_flip_flop_2_q1),
    .Q2(n74574_8x_d_flip_flop_2_q2));  // open: Q3, Q4, Q5, Q6, Q7
  _74574___8x_D_Flip_Flop u_74574_8x_d_flip_flop_3 (
    .Clk(Flags_CLK), .nOE(1'b0), .D0(Flags_IN[0]), .D1(Flags_IN[1]), .D2(Flags_IN[2]), .D3(Flags_IN[3]),
    .D4(Flags_IN[4]), .D5(1'b0), .D6(1'b0), .D7(1'b0), .Q0(Flags_OUT[0]), .Q1(Flags_OUT[1]),
    .Q2(Flags_OUT[2]), .Q3(Flags_OUT[3]), .Q4(Flags_OUT[4]));  // open: Q5, Q6, Q7
  _74541 u_74541_1 (
    .A0(INTE), .A2(n74574_8x_d_flip_flop_2_q1), .A3(n74574_8x_d_flip_flop_2_q2), .A4(Flags_OUT[0]),
    .A5(Flags_OUT[1]), .A6(Flags_OUT[2]), .A7(Flags_OUT[3]), .A8(Flags_OUT[4]), .nOE1(nOE), .nOE2(nOE),
    .Y0(n74541_1_y0), .Y1(n74541_1_y1), .Y2(n74541_1_y2), .Y3(n74541_1_y3), .Y4(n74541_1_y4),
    .Y5(n74541_1_y5), .Y6(n74541_1_y6), .Y7(n74541_1_y7));
  _74541 u_74541_2 (
    .A0(n74574_8x_d_flip_flop_1_q0), .A2(n74574_8x_d_flip_flop_1_q1), .A3(n74574_8x_d_flip_flop_1_q2),
    .A4(n74574_8x_d_flip_flop_1_q3), .A5(n74574_8x_d_flip_flop_1_q4), .A6(n74574_8x_d_flip_flop_1_q5),
    .A7(n74574_8x_d_flip_flop_1_q6), .A8(n74574_8x_d_flip_flop_1_q7), .nOE1(nOE), .nOE2(nOE),
    .Y0(n74541_2_y0), .Y1(n74541_2_y1), .Y2(n74541_2_y2), .Y3(n74541_2_y3), .Y4(n74541_2_y4),
    .Y5(n74541_2_y5), .Y6(n74541_2_y6), .Y7(n74541_2_y7));
  _8bit_to_bus u_8bit_to_bus_1 (
    .in_1(n74541_1_y0), .in_2(n74541_1_y1), .in_3(n74541_1_y2), .in_4(n74541_1_y3), .in_5(n74541_1_y4),
    .in_6(n74541_1_y5), .in_7(n74541_1_y6), .in_8(n74541_1_y7), .out_9(OUT[7:0]));
  _8bit_to_bus u_8bit_to_bus_2 (
    .in_1(n74541_2_y0), .in_2(n74541_2_y1), .in_3(n74541_2_y2), .in_4(n74541_2_y3), .in_5(n74541_2_y4),
    .in_6(n74541_2_y5), .in_7(n74541_2_y6), .in_8(n74541_2_y7), .out_9(OUT[15:8]));
  _8bit_to_bus u_8bit_to_bus_3 (
    .in_1(n74574_8x_d_flip_flop_1_q0), .in_2(n74574_8x_d_flip_flop_1_q1), .in_3(n74574_8x_d_flip_flop_1_q2),
    .in_4(n74574_8x_d_flip_flop_1_q3), .in_5(n74574_8x_d_flip_flop_1_q4), .in_6(n74574_8x_d_flip_flop_1_q5),
    .in_7(n74574_8x_d_flip_flop_1_q6), .in_8(n74574_8x_d_flip_flop_1_q7), .out_9(INTM));

  // Other names for the same wires on the sheet: F_CLK = Flags_CLK; OE = nOE

  // Notes on the sheet:
  //   Interrupt Mask
  //   Other
  //   Flags
endmodule

module Interrupt_Sample_Register (
  input  [2:0] RST_NMI_IRQ,
  input  nOE,
  input  IE,
  input  CLK,
  output IRQ,
  output NMI,
  output RST
);

  wire and_1_out;

  _74574___8x_D_Flip_Flop u_74574_8x_d_flip_flop_1 (
    .Clk(and_1_out), .nOE(nOE), .D0(RST_NMI_IRQ[0]), .D1(RST_NMI_IRQ[1]), .D2(RST_NMI_IRQ[2]), .Q0(IRQ),
    .Q1(NMI), .Q2(RST));  // open: D3, D4, D5, D6, D7, Q3, Q4, Q5, Q6, Q7
  and and_1 (and_1_out, IE, CLK);
  Pull_Resistor pull_resistor_1 (.node(IRQ));
  Pull_Resistor pull_resistor_2 (.node(RST));
  Pull_Resistor pull_resistor_3 (.node(NMI));
endmodule

module Temp_Left (
  input  [15:0] DATABUS,
  input  [1:0] S,
  input  CLK,
  input  OE,
  output [15:0] LEFTBUS
);

  wire n74194_1_qa, n74194_1_qb, n74194_1_qc, n74194_1_qd, n74194_2_qa, n74194_2_qb, n74194_2_qc,
       n74194_2_qd, n74194_3_qa, n74194_3_qb, n74194_3_qc, n74194_3_qd, n74194_4_qa, n74194_4_qb,
       n74194_4_qc, n74194_4_qd;

  _74194 u_74194_1 (
    .S1(S[1]), .S0(S[0]), .SHR_IN(1'b0), .CLK(CLK), .CLEAR(1'b1), .SHL_IN(1'b0), .A(DATABUS[15]),
    .B(DATABUS[14]), .C(DATABUS[13]), .D(DATABUS[12]), .QA(n74194_1_qa), .QB(n74194_1_qb), .QC(n74194_1_qc),
    .QD(n74194_1_qd));
  _74194 u_74194_2 (
    .S1(S[1]), .S0(S[0]), .SHR_IN(n74194_1_qd), .CLK(CLK), .CLEAR(1'b1), .SHL_IN(1'b0), .A(DATABUS[11]),
    .B(DATABUS[10]), .C(DATABUS[9]), .D(DATABUS[8]), .QA(n74194_2_qa), .QB(n74194_2_qb), .QC(n74194_2_qc),
    .QD(n74194_2_qd));
  _74194 u_74194_3 (
    .S1(S[1]), .S0(S[0]), .SHR_IN(n74194_2_qd), .CLK(CLK), .CLEAR(1'b1), .SHL_IN(1'b0), .A(DATABUS[7]),
    .B(DATABUS[6]), .C(DATABUS[5]), .D(DATABUS[4]), .QA(n74194_3_qa), .QB(n74194_3_qb), .QC(n74194_3_qc),
    .QD(n74194_3_qd));
  _74194 u_74194_4 (
    .S1(S[1]), .S0(S[0]), .SHR_IN(n74194_3_qd), .CLK(CLK), .CLEAR(1'b1), .SHL_IN(1'b0), .A(DATABUS[3]),
    .B(DATABUS[2]), .C(DATABUS[1]), .D(DATABUS[0]), .QA(n74194_4_qa), .QB(n74194_4_qb), .QC(n74194_4_qc),
    .QD(n74194_4_qd));
  _74541 u_74541_1 (
    .A0(n74194_4_qd), .A2(n74194_4_qc), .A3(n74194_4_qb), .A4(n74194_4_qa), .A5(n74194_3_qd),
    .A6(n74194_3_qc), .A7(n74194_3_qb), .A8(n74194_3_qa), .nOE1(OE), .nOE2(OE), .Y0(LEFTBUS[0]),
    .Y1(LEFTBUS[1]), .Y2(LEFTBUS[2]), .Y3(LEFTBUS[3]), .Y4(LEFTBUS[4]), .Y5(LEFTBUS[5]), .Y6(LEFTBUS[6]),
    .Y7(LEFTBUS[7]));
  _74541 u_74541_2 (
    .A0(n74194_2_qd), .A2(n74194_2_qc), .A3(n74194_2_qb), .A4(n74194_2_qa), .A5(n74194_1_qd),
    .A6(n74194_1_qc), .A7(n74194_1_qb), .A8(n74194_1_qa), .nOE1(OE), .nOE2(OE), .Y0(LEFTBUS[8]),
    .Y1(LEFTBUS[9]), .Y2(LEFTBUS[10]), .Y3(LEFTBUS[11]), .Y4(LEFTBUS[12]), .Y5(LEFTBUS[13]),
    .Y6(LEFTBUS[14]), .Y7(LEFTBUS[15]));

  // Notes on the sheet:
  //   S=00: HOLD
  //   S=01: SHR
  //   S=11: LOAD
endmodule
module DMA_Interface (
  input  HALT,
  input  CONT,
  input  DMA,
  input  EXEC,
  input  [3:0] ACTION,
  input  [15:0] INPUT,
  input  [2:0] REGSEL,
  output HALT_2,
  output CONT_2,
  output DMA_2,
  output [15:0] DATABUS,
  output DATA_CLK,
  output RE,
  output [15:0] ADDR_BUS,
  output REG_CLK,
  output [2:0] OE,
  output [2:0] IE
);

  wire ADDR_CLK, and_1_out, and_3_out, and_4_out, bus_to_8bit_1_out_2, bus_to_8bit_1_out_3,
       bus_to_8bit_1_out_4, bus_to_8bit_1_out_5, bus_to_8bit_1_out_6, bus_to_8bit_1_out_7,
       bus_to_8bit_1_out_8, bus_to_8bit_1_out_9, bus_to_8bit_2_out_2, bus_to_8bit_2_out_3,
       bus_to_8bit_2_out_4, bus_to_8bit_2_out_5, bus_to_8bit_2_out_6, bus_to_8bit_2_out_7,
       bus_to_8bit_2_out_8, bus_to_8bit_2_out_9, LD_ADDR, n74161_1_q0, n74161_1_q1, n74161_1_q2, n74161_1_q3,
       n74161_1_tc, n74161_2_q0, n74161_2_q1, n74161_2_q2, n74161_2_q3, n74161_2_tc, n74161_3_q0,
       n74161_3_q1, n74161_3_q2, n74161_3_q3, n74161_3_tc, n74161_4_q0, n74161_4_q1, n74161_4_q2,
       n74541_2_y0, n74541_2_y1, n74541_2_y2, n74541_2_y3, n74541_2_y4, n74541_2_y5, n74541_2_y6,
       n74541_2_y7, n74541_3_y0, n74541_3_y1, n74541_3_y2, n74541_3_y3, n74541_3_y4, n74541_3_y5,
       n74541_3_y6, n74541_3_y7, n74541_4_y0, n74541_4_y1, n74541_4_y2, n74541_4_y3, n74541_4_y4,
       n74541_4_y5, n74541_4_y6, n74541_4_y7, n74541_5_y0, n74541_5_y1, n74541_5_y2, n74541_5_y3,
       n74541_5_y4, n74541_5_y5, n74541_5_y6, n74541_5_y7, nDMA;

  not not_1 (nDMA, DMA);
  and and_1 (and_1_out, DMA, EXEC);
  and and_2 (DATA_CLK, and_1_out, ACTION[0]);
  not not_2 (LD_ADDR, ACTION[1]);
  and and_3 (and_3_out, ACTION[1], and_1_out);
  and and_4 (and_4_out, ACTION[2], and_1_out);
  and and_5 (REG_CLK, ACTION[3], and_1_out);
  _74541 u_74541_1 (
    .A0(REGSEL[0]), .A2(REGSEL[1]), .A3(REGSEL[2]), .A4(1'b0), .A5(1'b0), .A6(REGSEL[0]), .A7(REGSEL[1]),
    .A8(REGSEL[2]), .nOE1(nDMA), .nOE2(nDMA), .Y0(OE[0]), .Y1(OE[1]), .Y2(OE[2]), .Y5(IE[0]), .Y6(IE[1]),
    .Y7(IE[2]));  // open: Y3, Y4
  Transistor #(.\type ("n")) transistor_1 (.in(1'b0), .out(ADDR_CLK), .gate(DATA_CLK));
  Transistor #(.\type ("n")) transistor_2 (.in(1'b0), .out(ADDR_CLK), .gate(and_3_out));
  Transistor #(.\type ("n")) transistor_3 (.in(1'b0), .out(ADDR_CLK), .gate(and_4_out));
  Pull_Resistor #(.pull(1)) pull_resistor_1 (.node(ADDR_CLK));
  _74161 u_74161_1 (
    .CET(DMA), .CEP(DMA), .PE(LD_ADDR), .CLK(ADDR_CLK), .MR(1'b1), .D0(INPUT[1]), .D1(INPUT[2]),
    .D2(INPUT[3]), .D3(INPUT[4]), .Q0(n74161_1_q0), .Q1(n74161_1_q1), .Q2(n74161_1_q2), .Q3(n74161_1_q3),
    .TC(n74161_1_tc));
  _74161 u_74161_2 (
    .CET(n74161_1_tc), .CEP(DMA), .PE(LD_ADDR), .CLK(ADDR_CLK), .MR(1'b1), .D0(INPUT[5]), .D1(INPUT[6]),
    .D2(INPUT[7]), .D3(INPUT[8]), .Q0(n74161_2_q0), .Q1(n74161_2_q1), .Q2(n74161_2_q2), .Q3(n74161_2_q3),
    .TC(n74161_2_tc));
  _74161 u_74161_3 (
    .CET(n74161_2_tc), .CEP(DMA), .PE(LD_ADDR), .CLK(ADDR_CLK), .MR(1'b1), .D0(INPUT[9]), .D1(INPUT[10]),
    .D2(INPUT[11]), .D3(INPUT[12]), .Q0(n74161_3_q0), .Q1(n74161_3_q1), .Q2(n74161_3_q2), .Q3(n74161_3_q3),
    .TC(n74161_3_tc));
  _74161 u_74161_4 (
    .CET(n74161_3_tc), .CEP(DMA), .PE(LD_ADDR), .CLK(ADDR_CLK), .MR(1'b1), .D0(INPUT[13]), .D1(INPUT[14]),
    .D2(INPUT[15]), .D3(1'b0), .Q0(n74161_4_q0), .Q1(n74161_4_q1), .Q2(n74161_4_q2));  // open: Q3, TC
  _74541 u_74541_2 (
    .A0(bus_to_8bit_1_out_2), .A2(bus_to_8bit_1_out_3), .A3(bus_to_8bit_1_out_4), .A4(bus_to_8bit_1_out_5),
    .A5(bus_to_8bit_1_out_6), .A6(bus_to_8bit_1_out_7), .A7(bus_to_8bit_1_out_8), .A8(bus_to_8bit_1_out_9),
    .nOE1(ACTION[2]), .nOE2(nDMA), .Y0(n74541_2_y0), .Y1(n74541_2_y1), .Y2(n74541_2_y2), .Y3(n74541_2_y3),
    .Y4(n74541_2_y4), .Y5(n74541_2_y5), .Y6(n74541_2_y6), .Y7(n74541_2_y7));
  bus_to_8bit bus_to_8bit_1 (
    .in_1(INPUT[7:0]), .out_2(bus_to_8bit_1_out_2), .out_3(bus_to_8bit_1_out_3), .out_4(bus_to_8bit_1_out_4),
    .out_5(bus_to_8bit_1_out_5), .out_6(bus_to_8bit_1_out_6), .out_7(bus_to_8bit_1_out_7),
    .out_8(bus_to_8bit_1_out_8), .out_9(bus_to_8bit_1_out_9));
  _74541 u_74541_3 (
    .A0(bus_to_8bit_2_out_2), .A2(bus_to_8bit_2_out_3), .A3(bus_to_8bit_2_out_4), .A4(bus_to_8bit_2_out_5),
    .A5(bus_to_8bit_2_out_6), .A6(bus_to_8bit_2_out_7), .A7(bus_to_8bit_2_out_8), .A8(bus_to_8bit_2_out_9),
    .nOE1(ACTION[2]), .nOE2(nDMA), .Y0(n74541_3_y0), .Y1(n74541_3_y1), .Y2(n74541_3_y2), .Y3(n74541_3_y3),
    .Y4(n74541_3_y4), .Y5(n74541_3_y5), .Y6(n74541_3_y6), .Y7(n74541_3_y7));
  bus_to_8bit bus_to_8bit_2 (
    .in_1(INPUT[15:8]), .out_2(bus_to_8bit_2_out_2), .out_3(bus_to_8bit_2_out_3),
    .out_4(bus_to_8bit_2_out_4), .out_5(bus_to_8bit_2_out_5), .out_6(bus_to_8bit_2_out_6),
    .out_7(bus_to_8bit_2_out_7), .out_8(bus_to_8bit_2_out_8), .out_9(bus_to_8bit_2_out_9));
  _74541 u_74541_4 (
    .A0(1'b0), .A2(n74161_1_q0), .A3(n74161_1_q1), .A4(n74161_1_q2), .A5(n74161_1_q3), .A6(n74161_2_q0),
    .A7(n74161_2_q1), .A8(n74161_2_q2), .nOE1(nDMA), .nOE2(nDMA), .Y0(n74541_4_y0), .Y1(n74541_4_y1),
    .Y2(n74541_4_y2), .Y3(n74541_4_y3), .Y4(n74541_4_y4), .Y5(n74541_4_y5), .Y6(n74541_4_y6), .Y7(n74541_4_y7));
  _74541 u_74541_5 (
    .A0(n74161_2_q3), .A2(n74161_3_q0), .A3(n74161_3_q1), .A4(n74161_3_q2), .A5(n74161_3_q3),
    .A6(n74161_4_q0), .A7(n74161_4_q1), .A8(n74161_4_q2), .nOE1(nDMA), .nOE2(nDMA), .Y0(n74541_5_y0),
    .Y1(n74541_5_y1), .Y2(n74541_5_y2), .Y3(n74541_5_y3), .Y4(n74541_5_y4), .Y5(n74541_5_y5),
    .Y6(n74541_5_y6), .Y7(n74541_5_y7));
  _8bit_to_bus u_8bit_to_bus_1 (
    .in_1(n74541_2_y0), .in_2(n74541_2_y1), .in_3(n74541_2_y2), .in_4(n74541_2_y3), .in_5(n74541_2_y4),
    .in_6(n74541_2_y5), .in_7(n74541_2_y6), .in_8(n74541_2_y7), .out_9(DATABUS[7:0]));
  _8bit_to_bus u_8bit_to_bus_2 (
    .in_1(n74541_3_y0), .in_2(n74541_3_y1), .in_3(n74541_3_y2), .in_4(n74541_3_y3), .in_5(n74541_3_y4),
    .in_6(n74541_3_y5), .in_7(n74541_3_y6), .in_8(n74541_3_y7), .out_9(DATABUS[15:8]));
  _8bit_to_bus u_8bit_to_bus_3 (
    .in_1(n74541_4_y0), .in_2(n74541_4_y1), .in_3(n74541_4_y2), .in_4(n74541_4_y3), .in_5(n74541_4_y4),
    .in_6(n74541_4_y5), .in_7(n74541_4_y6), .in_8(n74541_4_y7), .out_9(ADDR_BUS[7:0]));
  _8bit_to_bus u_8bit_to_bus_4 (
    .in_1(n74541_5_y0), .in_2(n74541_5_y1), .in_3(n74541_5_y2), .in_4(n74541_5_y3), .in_5(n74541_5_y4),
    .in_6(n74541_5_y5), .in_7(n74541_5_y6), .in_8(n74541_5_y7), .out_9(ADDR_BUS[15:8]));

  assign CONT_2 = CONT;
  assign DMA_2 = DMA;
  assign HALT_2 = HALT;
  assign RE = ACTION[2];

  // Notes on the sheet:
  //   From rotary switch
  //   Connects to CU. Must HALT before using DMA
  //   OE
  //   IE
  //   PROG
  //   LD MEM
  //   EXAMINE
  //   NOTE: D0 takes input
  //    from bit 1, and not bit 0
endmodule

module _7405 (
  input  I0,
  input  I1,
  input  I2,
  input  I3,
  input  I4,
  input  I5,
  output O0,
  output O1,
  output O2,
  output O3,
  output O4,
  output O5
);

  Transistor #(.\type ("n")) transistor_1 (.in(1'b0), .out(O0), .gate(I0));
  Transistor #(.\type ("n")) transistor_2 (.in(1'b0), .out(O1), .gate(I1));
  Transistor #(.\type ("n")) transistor_3 (.in(1'b0), .out(O2), .gate(I2));
  Transistor #(.\type ("n")) transistor_4 (.in(1'b0), .out(O3), .gate(I3));
  Transistor #(.\type ("n")) transistor_5 (.in(1'b0), .out(O4), .gate(I4));
  Transistor #(.\type ("n")) transistor_6 (.in(1'b0), .out(O5), .gate(I5));

  // Notes on the sheet:
  //   Hex inverter with open drain output
endmodule

module _7473_Dual_JK_FFs (
  input  _1J,
  input  _1K,
  input  _1CLK,
  input  _1_CLR,
  input  _2J,
  input  _2K,
  input  _2CLK,
  input  _2_CLR,
  output _1Q,
  output _1_Q,
  output _2Q,
  output _2_Q
);

  wire not_1_out, not_2_out;

  not not_1 (not_1_out, _1_CLR);
  not not_2 (not_2_out, _2_CLR);
  J_K_Flip_Flop j_k_ff_1 (.J(_1J), .clk(_1CLK), .K(_1K), .Q(_1Q), .Qn(_1_Q), .reset(not_1_out));  // open: preset, en
  J_K_Flip_Flop j_k_ff_2 (.J(_2J), .clk(_2CLK), .K(_2K), .Q(_2Q), .Qn(_2_Q), .reset(not_2_out));  // open: preset, en
endmodule

module _7474_Dual_D_FFs (
  input  PRE1,
  input  CLR1,
  input  CLK1,
  input  D1,
  input  PRE2,
  input  CLR2,
  input  CLK2,
  input  D2,
  output Q1,
  output Q1_2,
  output Q2,
  output Q2_2
);

  wire not_1_out, not_2_out, not_3_out, not_4_out;

  not not_1 (not_1_out, PRE1);
  not not_2 (not_2_out, CLR1);
  not not_3 (not_3_out, PRE2);
  not not_4 (not_4_out, CLR2);
  D_Flip_Flop d_ff_1 (.clk(CLK1), .D(D1), .Q(Q1), .Qn(Q1_2), .preset(not_1_out), .reset(not_2_out));  // open: en
  D_Flip_Flop d_ff_2 (.clk(CLK2), .D(D2), .Q(Q2), .Qn(Q2_2), .preset(not_3_out), .reset(not_4_out));  // open: en
endmodule

module _7475_Quad_Latches (
  input  D0,
  input  E0_1,
  input  D1,
  input  D2,
  input  E2_3,
  input  D3,
  output Q0,
  output Q0_2,
  output Q1,
  output Q1_2,
  output Q2,
  output Q2_2,
  output Q3,
  output Q2_3
);

  wire controlled_buffer_1_out, controlled_buffer_2_out, controlled_buffer_3_out, controlled_buffer_4_out,
       not_1_out, not_2_out, not_3_out, not_4_out;

  assign controlled_buffer_1_out = E0_1 ? D0 : 1'bz;  // Controlled_Buffer controlled_buffer_1
  assign controlled_buffer_2_out = E0_1 ? D1 : 1'bz;  // Controlled_Buffer controlled_buffer_2
  assign controlled_buffer_3_out = E2_3 ? D2 : 1'bz;  // Controlled_Buffer controlled_buffer_3
  assign controlled_buffer_4_out = E2_3 ? D3 : 1'bz;  // Controlled_Buffer controlled_buffer_4
  not not_1 (not_1_out, controlled_buffer_1_out);
  not not_2 (not_2_out, controlled_buffer_2_out);
  not not_3 (not_3_out, controlled_buffer_3_out);
  not not_4 (not_4_out, controlled_buffer_4_out);
  D_Flip_Flop d_ff_1 (.Q(Q0), .Qn(Q0_2), .preset(controlled_buffer_1_out), .reset(not_1_out));  // open: clk, D, en
  D_Flip_Flop d_ff_2 (.Q(Q1), .Qn(Q1_2), .preset(controlled_buffer_2_out), .reset(not_2_out));  // open: clk, D, en
  D_Flip_Flop d_ff_3 (.Q(Q2), .Qn(Q2_2), .preset(controlled_buffer_3_out), .reset(not_3_out));  // open: clk, D, en
  D_Flip_Flop d_ff_4 (.Q(Q3), .Qn(Q2_3), .preset(controlled_buffer_4_out), .reset(not_4_out));  // open: clk, D, en
endmodule

module _7477 (
  input  D0,
  input  E0_1,
  input  D1,
  input  D2,
  input  E2_3,
  input  D3,
  output Q0,
  output Q1,
  output Q2,
  output Q3
);

  wire controlled_buffer_1_out, controlled_buffer_2_out, controlled_buffer_3_out, controlled_buffer_4_out,
       not_1_out, not_2_out, not_3_out, not_4_out;

  assign controlled_buffer_1_out = E0_1 ? D0 : 1'bz;  // Controlled_Buffer controlled_buffer_1
  assign controlled_buffer_2_out = E0_1 ? D1 : 1'bz;  // Controlled_Buffer controlled_buffer_2
  assign controlled_buffer_3_out = E2_3 ? D2 : 1'bz;  // Controlled_Buffer controlled_buffer_3
  assign controlled_buffer_4_out = E2_3 ? D3 : 1'bz;  // Controlled_Buffer controlled_buffer_4
  not not_1 (not_1_out, controlled_buffer_1_out);
  not not_2 (not_2_out, controlled_buffer_2_out);
  not not_3 (not_3_out, controlled_buffer_3_out);
  not not_4 (not_4_out, controlled_buffer_4_out);
  D_Flip_Flop d_ff_1 (.Q(Q0), .preset(controlled_buffer_1_out), .reset(not_1_out));  // open: clk, D, Qn, en
  D_Flip_Flop d_ff_2 (.Q(Q1), .preset(controlled_buffer_2_out), .reset(not_2_out));  // open: clk, D, Qn, en
  D_Flip_Flop d_ff_3 (.Q(Q2), .preset(controlled_buffer_3_out), .reset(not_3_out));  // open: clk, D, Qn, en
  D_Flip_Flop d_ff_4 (.Q(Q3), .preset(controlled_buffer_4_out), .reset(not_4_out));  // open: clk, D, Qn, en
endmodule

module _74138 (
  input  nE1,
  input  nE2,
  input  E3,
  input  A0,
  input  A1,
  input  A2,
  output Y0,
  output Y1,
  output Y2,
  output Y3,
  output Y4,
  output Y5,
  output Y6,
  output Y7
);

  wire and_1_out, not_1_out, not_2_out, not_3_out, not_4_out, not_5_out, not_6_out, not_7_out, not_8_out;

  not not_1 (not_1_out, nE1);
  not not_2 (not_2_out, nE2);
  not not_3 (not_3_out, A0);
  not not_4 (not_4_out, A1);
  not not_5 (not_5_out, A2);
  and and_1 (and_1_out, not_1_out, not_2_out, E3);
  not not_6 (not_6_out, not_3_out);
  not not_7 (not_7_out, not_4_out);
  not not_8 (not_8_out, not_5_out);
  nand nand_1 (Y0, not_3_out, not_4_out, not_5_out, and_1_out);
  nand nand_2 (Y1, not_6_out, not_4_out, not_5_out, and_1_out);
  nand nand_3 (Y2, not_3_out, not_7_out, not_5_out, and_1_out);
  nand nand_4 (Y3, not_6_out, not_7_out, not_5_out, and_1_out);
  nand nand_5 (Y4, not_3_out, not_4_out, not_8_out, and_1_out);
  nand nand_6 (Y5, not_4_out, not_8_out, not_6_out, and_1_out);
  nand nand_7 (Y6, not_3_out, not_8_out, not_7_out, and_1_out);
  nand nand_8 (Y7, and_1_out, not_7_out, not_6_out, not_8_out);
endmodule

module _74139 (
  input  nEA,
  input  SA0,
  input  SA1,
  input  nEB,
  input  SB0,
  input  SB1,
  output A0,
  output A1,
  output A2,
  output A3,
  output B0,
  output B1,
  output B2,
  output B3
);

  wire decoder_1_out0, decoder_1_out1, decoder_1_out2, decoder_1_out3, decoder_2_out0, decoder_2_out1,
       decoder_2_out2, decoder_2_out3, not_1_out, not_2_out;

  Decoder #(.select(2), .disabled(0)) decoder_1 (
    .out0(decoder_1_out0), .out1(decoder_1_out1), .out2(decoder_1_out2), .out3(decoder_1_out3),
    .sel({SA1, SA0}), .en(not_1_out));
  not not_1 (not_1_out, nEA);
  Decoder #(.select(2), .disabled(0)) decoder_2 (
    .out0(decoder_2_out0), .out1(decoder_2_out1), .out2(decoder_2_out2), .out3(decoder_2_out3),
    .sel({SB1, SB0}), .en(not_2_out));
  not not_2 (not_2_out, nEB);
  not not_3 (A0, decoder_1_out0);
  not not_4 (A1, decoder_1_out1);
  not not_5 (A2, decoder_1_out2);
  not not_6 (A3, decoder_1_out3);
  not not_7 (B0, decoder_2_out0);
  not not_8 (B1, decoder_2_out1);
  not not_9 (B2, decoder_2_out2);
  not not_10 (B3, decoder_2_out3);

  // Notes on the sheet:
  //   dual 2 to 4-line decoder/demultiplexer, inverting outputs
endmodule

module _74148 (
  input  _0__10,
  input  _1__11,
  input  _2__12,
  input  _3__13,
  input  _4__1,
  input  _5__2,
  input  _6__3,
  input  _7__4,
  input  EI__5,
  output EO__15,
  output G5__14,
  output A0__9,
  output A1__7,
  output A2__6
);

  wire and_1_out, and_2_out, and_3_out, and_4_out, and_5_out, and_6_out, and_7_out, and_8_out, and_9_out,
       and_10_out, and_11_out, and_12_out, not_1_out, not_2_out, not_3_out, not_4_out, not_5_out, not_6_out,
       not_7_out, not_8_out, not_9_out, not_10_out, not_11_out, not_12_out;

  not not_1 (not_1_out, _1__11);
  not not_2 (not_2_out, _2__12);
  not not_3 (not_3_out, _3__13);
  not not_4 (not_4_out, _4__1);
  not not_5 (not_5_out, _5__2);
  not not_6 (not_6_out, _6__3);
  not not_7 (not_7_out, _7__4);
  not not_8 (not_8_out, EI__5);
  not not_9 (not_9_out, not_2_out);
  not not_10 (not_10_out, not_4_out);
  not not_11 (not_11_out, not_5_out);
  not not_12 (not_12_out, not_6_out);
  nand nand_1 (EO__15, _0__10, _1__11, _2__12, _3__13, _4__1, _5__2, _6__3, _7__4, not_8_out);
  and and_1 (and_1_out, not_1_out, not_9_out, not_10_out, not_12_out, not_8_out);
  and and_2 (and_2_out, not_3_out, not_10_out, not_12_out, not_8_out);
  and and_3 (and_3_out, not_5_out, not_12_out, not_8_out);
  and and_4 (and_4_out, not_7_out, not_8_out);
  and and_5 (and_5_out, not_2_out, not_10_out, not_11_out, not_8_out);
  and and_6 (and_6_out, not_3_out, not_10_out, not_11_out, not_8_out);
  and and_7 (and_7_out, not_6_out, not_8_out);
  and and_8 (and_8_out, not_7_out, not_8_out);
  and and_9 (and_9_out, not_4_out, not_8_out);
  and and_10 (and_10_out, not_5_out, not_8_out);
  and and_11 (and_11_out, not_6_out, not_8_out);
  and and_12 (and_12_out, not_7_out, not_8_out);
  nand nand_2 (G5__14, EO__15, not_8_out);
  nor nor_1 (A0__9, and_1_out, and_2_out, and_3_out, and_4_out);
  nor nor_2 (A1__7, and_5_out, and_6_out, and_7_out, and_8_out);
  nor nor_3 (A2__6, and_9_out, and_10_out, and_11_out, and_12_out);

  // Notes on the sheet:
  //   8 line to 3 priority encoder
endmodule

module _74151 (
  input  I0,
  input  I1,
  input  I2,
  input  I3,
  input  I4,
  input  I5,
  input  I6,
  input  I7,
  input  S0,
  input  S1,
  input  S2,
  input  E,
  output Y,
  output Y_2
);

  wire multiplexer_1_out, not_1_out;

  Multiplexer #(.select(3), .enable("false")) multiplexer_1 (
    .in0(I0), .in1(I1), .in2(I2), .in3(I3), .in4(I4), .in5(I5), .in6(I6), .in7(I7), .out(multiplexer_1_out),
    .sel({S2, S1, S0}));
  not not_1 (not_1_out, multiplexer_1_out);
  and and_1 (Y, multiplexer_1_out, ~E);  // AND_Gate
  and and_2 (Y_2, not_1_out, ~E);  // AND_Gate

  // Notes on the sheet:
  //   8 line to 1 MUX
endmodule

module _74153 (
  input  _1_G,
  input  _1C0,
  input  _1C1,
  input  _1C2,
  input  _1C3,
  input  B,
  input  A,
  input  _2C0,
  input  _2C1,
  input  _2C2,
  input  _2C3,
  input  _2_G,
  output _1Y,
  output _2Y
);

  wire and_1_out, and_2_out, and_3_out, and_4_out, and_5_out, and_6_out, and_7_out, and_8_out, not_1_out,
       not_2_out, not_3_out, not_4_out, not_5_out, not_6_out;

  not not_1 (not_1_out, _1_G);
  not not_2 (not_2_out, not_3_out);
  not not_3 (not_3_out, B);
  not not_4 (not_4_out, not_5_out);
  not not_5 (not_5_out, A);
  not not_6 (not_6_out, _2_G);
  and and_1 (and_1_out, not_1_out, not_3_out, not_5_out, _1C0);
  and and_2 (and_2_out, not_1_out, not_3_out, not_4_out, _1C1);
  and and_3 (and_3_out, not_1_out, not_2_out, not_5_out, _1C2);
  and and_4 (and_4_out, not_1_out, not_2_out, not_4_out, _1C3);
  and and_5 (and_5_out, _2C0, not_3_out, not_5_out, not_6_out);
  and and_6 (and_6_out, _2C1, not_3_out, not_4_out, not_6_out);
  and and_7 (and_7_out, _2C2, not_2_out, not_5_out, not_6_out);
  and and_8 (and_8_out, _2C3, not_2_out, not_4_out, not_6_out);
  or or_1 (_1Y, and_1_out, and_2_out, and_3_out, and_4_out);
  or or_2 (_2Y, and_5_out, and_6_out, and_7_out, and_8_out);

  // Notes on the sheet:
  //   Data1
  //   Select
  //   Data2
  //   Enable
  //   Enable
endmodule

module _74157_2_1_MUX (
  input  S,
  input  nE,
  input  _1B,
  input  _1A,
  input  _2B,
  input  _2A,
  input  _3B,
  input  _3A,
  input  _4B,
  input  _4A,
  output Y1,
  output Y2,
  output Y3,
  output Y4
);

  wire and_1_out, and_2_out, and_3_out, and_4_out, and_5_out, and_6_out, and_7_out, and_8_out, nor_1_out,
       nor_2_out, nor_3_out, nor_4_out, nor_5_out, nor_6_out, not_1_out;

  not not_1 (not_1_out, S);
  nor nor_1 (nor_1_out, not_1_out, nE);
  nor nor_2 (nor_2_out, S, nE);
  and and_1 (and_1_out, nor_1_out, _1B);
  and and_2 (and_2_out, nor_2_out, _1A);
  and and_3 (and_3_out, nor_1_out, _2B);
  and and_4 (and_4_out, nor_2_out, _2A);
  and and_5 (and_5_out, nor_1_out, _3B);
  and and_6 (and_6_out, nor_2_out, _3A);
  and and_7 (and_7_out, nor_1_out, _4B);
  and and_8 (and_8_out, nor_2_out, _4A);
  nor nor_3 (nor_3_out, and_1_out, and_2_out);
  nor nor_4 (nor_4_out, and_3_out, and_4_out);
  nor nor_5 (nor_5_out, and_5_out, and_6_out);
  nor nor_6 (nor_6_out, and_7_out, and_8_out);
  not not_2 (Y1, nor_3_out);
  not not_3 (Y2, nor_4_out);
  not not_4 (Y3, nor_5_out);
  not not_5 (Y4, nor_6_out);

  // Notes on the sheet:
  //   2-line to 1 data selector / multiplexer
endmodule

module _74161 (
  input  D0,
  input  D1,
  input  D2,
  input  D3,
  input  CET,
  input  CEP,
  input  PE,
  input  CLK,
  input  MR,
  output Q0,
  output Q1,
  output Q2,
  output Q3,
  output TC
);

  wire and_1_out, and_2_out, and_3_out, and_4_out, and_5_out, and_6_out, and_7_out, and_8_out, and_9_out,
       d_ff_1_qn, d_ff_2_qn, d_ff_3_qn, d_ff_4_qn, nand_1_out, nor_1_out, nor_2_out, nor_3_out, nor_4_out,
       not_1_out, not_2_out, not_3_out, not_4_out, or_1_out, or_2_out, or_3_out, or_4_out, or_5_out,
       xnor_1_out, xnor_2_out, xnor_3_out;

  not not_1 (not_1_out, PE);
  not not_2 (not_2_out, MR);
  nand nand_1 (nand_1_out, CET, CEP);
  not not_3 (not_3_out, not_1_out);
  not not_4 (not_4_out, nand_1_out);
  xnor xnor_1 (xnor_1_out, not_4_out, d_ff_1_qn);
  and and_1 (and_1_out, xnor_1_out, not_3_out);
  and and_2 (and_2_out, D0, not_1_out);
  or or_1 (or_1_out, and_2_out, and_1_out);
  D_Flip_Flop d_ff_1 (.clk(CLK), .D(or_1_out), .Q(Q0), .Qn(d_ff_1_qn), .reset(not_2_out));  // open: preset, en
  nor nor_1 (nor_1_out, nand_1_out, d_ff_1_qn);
  xnor xnor_2 (xnor_2_out, nor_1_out, d_ff_2_qn);
  and and_3 (and_3_out, D1, not_1_out);
  or or_2 (or_2_out, and_3_out, and_4_out);
  and and_4 (and_4_out, xnor_2_out, not_3_out);
  D_Flip_Flop d_ff_2 (.clk(CLK), .D(or_2_out), .Q(Q1), .Qn(d_ff_2_qn), .reset(not_2_out));  // open: preset, en
  and and_5 (and_5_out, D2, not_1_out);
  nor nor_2 (nor_2_out, nand_1_out, d_ff_2_qn, d_ff_1_qn);
  xnor xnor_3 (xnor_3_out, nor_2_out, d_ff_3_qn);
  and and_6 (and_6_out, xnor_3_out, not_3_out);
  or or_3 (or_3_out, and_5_out, and_6_out);
  D_Flip_Flop d_ff_3 (.clk(CLK), .D(or_3_out), .Q(Q2), .Qn(d_ff_3_qn), .reset(not_2_out));  // open: preset, en
  nor nor_3 (nor_3_out, nand_1_out, d_ff_3_qn, d_ff_2_qn, d_ff_1_qn);
  and and_7 (and_7_out, nor_3_out, d_ff_4_qn);
  or or_4 (or_4_out, and_7_out, nor_4_out);
  and and_8 (and_8_out, D3, not_1_out);
  and and_9 (and_9_out, not_3_out, or_4_out);
  or or_5 (or_5_out, and_8_out, and_9_out);
  nor nor_4 (nor_4_out, nor_3_out, d_ff_4_qn);
  D_Flip_Flop d_ff_4 (.clk(CLK), .D(or_5_out), .Q(Q3), .Qn(d_ff_4_qn), .reset(not_2_out));  // open: preset, en
  and and_10 (TC, Q3, Q2, Q1, Q0, CET);

  // Notes on the sheet:
  //   4-bit presettable synchrounous counter with async clear
  //   Preset (PE) overrides Count enable (CEP & CET)
endmodule

module _74175___4x_D_flip_flops (
  input  D1,
  input  D2,
  input  D3,
  input  D4,
  input  CLK,
  input  nCLR,
  output Q1,
  output nQ1,
  output Q2,
  output nQ2,
  output Q3,
  output nQ3,
  output Q4,
  output nQ4
);

  wire not_1_out;

  not not_1 (not_1_out, nCLR);
  D_Flip_Flop d_ff_1 (.clk(CLK), .D(D1), .Q(Q1), .Qn(nQ1), .reset(not_1_out));  // open: preset, en
  D_Flip_Flop d_ff_2 (.clk(CLK), .D(D2), .Q(Q2), .Qn(nQ2), .reset(not_1_out));  // open: preset, en
  D_Flip_Flop d_ff_3 (.clk(CLK), .D(D3), .Q(Q3), .Qn(nQ3), .reset(not_1_out));  // open: preset, en
  D_Flip_Flop d_ff_4 (.clk(CLK), .D(D4), .Q(Q4), .Qn(nQ4), .reset(not_1_out));  // open: preset, en
endmodule

module _74193 (
  input  D0,
  input  D1,
  input  D2,
  input  D3,
  input  nPL,
  input  CPU,
  input  CPD,
  input  MR,
  output nTCU,
  output nTCD,
  output Q0,
  output Q1,
  output Q2,
  output Q3
);

  wire and_1_out, and_2_out, and_3_out, and_4_out, and_5_out, and_6_out, nand_1_out, nand_2_out, nand_3_out,
       nand_4_out, nand_5_out, nand_6_out, nand_7_out, nand_8_out, nor_1_out, nor_2_out, nor_3_out,
       nor_4_out, not_1_out, not_2_out, not_3_out, not_4_out, not_5_out, not_6_out, not_7_out, not_8_out,
       or_1_out, or_2_out, or_3_out, or_4_out, t_ff_1_qn, t_ff_2_qn, t_ff_3_qn, t_ff_4_qn;

  not not_1 (not_1_out, nPL);
  not not_2 (not_2_out, CPU);
  not not_3 (not_3_out, CPD);
  not not_4 (not_4_out, MR);
  nand nand_1 (nand_1_out, not_1_out, not_4_out, D0);
  nor nor_1 (nor_1_out, not_2_out, not_3_out);
  not not_5 (not_5_out, nand_1_out);
  nand nand_2 (nand_2_out, nand_1_out, not_1_out);
  T_Flip_Flop t_ff_1 (
    .clk(nor_1_out), .T(1'b1), .Q(Q0), .Qn(t_ff_1_qn), .preset(not_5_out), .reset(or_1_out));  // open: en
  or or_1 (or_1_out, ~not_4_out, ~nand_2_out);  // OR_Gate
  and and_1 (and_1_out, not_2_out, Q0);
  and and_2 (and_2_out, t_ff_1_qn, not_3_out);
  nand nand_3 (nand_3_out, not_1_out, not_4_out, D1);
  nor nor_2 (nor_2_out, and_1_out, and_2_out);
  not not_6 (not_6_out, nand_3_out);
  nand nand_4 (nand_4_out, nand_3_out, not_1_out);
  T_Flip_Flop t_ff_2 (
    .clk(nor_2_out), .T(1'b1), .Q(Q1), .Qn(t_ff_2_qn), .preset(not_6_out), .reset(or_2_out));  // open: en
  or or_2 (or_2_out, ~not_4_out, ~nand_4_out);  // OR_Gate
  and and_3 (and_3_out, not_2_out, Q0, Q1);
  and and_4 (and_4_out, t_ff_2_qn, t_ff_1_qn, not_3_out);
  nand nand_5 (nand_5_out, not_1_out, not_4_out, D2);
  nor nor_3 (nor_3_out, and_3_out, and_4_out);
  not not_7 (not_7_out, nand_5_out);
  T_Flip_Flop t_ff_3 (
    .clk(nor_3_out), .T(1'b1), .Q(Q2), .Qn(t_ff_3_qn), .preset(not_7_out), .reset(or_3_out));  // open: en
  or or_3 (or_3_out, ~not_4_out, ~nand_6_out);  // OR_Gate
  nand nand_6 (nand_6_out, nand_5_out, not_1_out);
  and and_5 (and_5_out, not_2_out, Q0, Q1, Q2);
  and and_6 (and_6_out, t_ff_3_qn, t_ff_2_qn, t_ff_1_qn, not_3_out);
  nand nand_7 (nand_7_out, not_1_out, not_4_out, D3);
  nor nor_4 (nor_4_out, and_5_out, and_6_out);
  not not_8 (not_8_out, nand_7_out);
  T_Flip_Flop t_ff_4 (
    .clk(nor_4_out), .T(1'b1), .Q(Q3), .Qn(t_ff_4_qn), .preset(not_8_out), .reset(or_4_out));  // open: en
  or or_4 (or_4_out, ~not_4_out, ~nand_8_out);  // OR_Gate
  nand nand_8 (nand_8_out, nand_7_out, not_1_out);
  nand nand_9 (nTCU, not_2_out, Q0, Q1, Q2, Q3);
  nand nand_10 (nTCD, t_ff_4_qn, t_ff_3_qn, t_ff_2_qn, t_ff_1_qn, not_3_out);

  // Notes on the sheet:
  //   4bit presettable up/down counter
  //   counting should be done with one of the cnt dirs set to high, otherwise unpredictable behaviour will occur
endmodule

module _74194 (
  input  A,
  input  B,
  input  C,
  input  D,
  input  S1,
  input  S0,
  input  SHR_IN,
  input  SHL_IN,
  input  CLK,
  input  CLEAR,
  output QA,
  output QB,
  output QC,
  output QD
);

  wire and_1_out, and_2_out, and_3_out, and_4_out, and_5_out, and_6_out, and_7_out, and_8_out, and_9_out,
       and_10_out, and_11_out, and_12_out, and_13_out, and_14_out, and_15_out, and_16_out, nor_1_out,
       nor_2_out, nor_3_out, nor_4_out, not_1_out, not_2_out, not_3_out, not_4_out, not_5_out, not_6_out,
       not_7_out, not_8_out, not_9_out;

  not not_1 (not_1_out, S1);
  not not_2 (not_2_out, S0);
  not not_3 (not_3_out, not_1_out);
  not not_4 (not_4_out, not_2_out);
  not not_5 (not_5_out, CLEAR);
  and and_1 (and_1_out, SHR_IN, not_1_out, not_4_out);
  and and_2 (and_2_out, not_4_out, not_3_out, A);
  nor nor_1 (nor_1_out, and_1_out, and_2_out, and_4_out, and_3_out);
  and and_3 (and_3_out, not_2_out, not_1_out, QA);
  and and_4 (and_4_out, not_2_out, not_3_out, QB);
  not not_6 (not_6_out, nor_1_out);
  S_R_Flip_Flop s_r_ff_1 (.S(not_6_out), .clk(CLK), .R(nor_1_out), .Q(QA), .reset(not_5_out));  // open: Qn, preset, en
  and and_5 (and_5_out, not_4_out, not_3_out, B);
  and and_6 (and_6_out, QA, not_1_out, not_4_out);
  and and_7 (and_7_out, not_2_out, not_1_out, QB);
  and and_8 (and_8_out, not_2_out, not_3_out, QC);
  nor nor_2 (nor_2_out, and_6_out, and_5_out, and_8_out, and_7_out);
  not not_7 (not_7_out, nor_2_out);
  S_R_Flip_Flop s_r_ff_2 (.S(not_7_out), .clk(CLK), .R(nor_2_out), .Q(QB), .reset(not_5_out));  // open: Qn, preset, en
  and and_9 (and_9_out, not_4_out, not_3_out, C);
  and and_10 (and_10_out, QB, not_1_out, not_4_out);
  and and_11 (and_11_out, not_2_out, not_3_out, QD);
  and and_12 (and_12_out, not_2_out, not_1_out, QC);
  nor nor_3 (nor_3_out, and_10_out, and_9_out, and_11_out, and_12_out);
  not not_8 (not_8_out, nor_3_out);
  S_R_Flip_Flop s_r_ff_3 (.S(not_8_out), .clk(CLK), .R(nor_3_out), .Q(QC), .reset(not_5_out));  // open: Qn, preset, en
  and and_13 (and_13_out, QC, not_1_out, not_4_out);
  and and_14 (and_14_out, not_2_out, not_3_out, SHL_IN);
  and and_15 (and_15_out, not_4_out, not_3_out, D);
  nor nor_4 (nor_4_out, and_13_out, and_15_out, and_14_out, and_16_out);
  not not_9 (not_9_out, nor_4_out);
  and and_16 (and_16_out, not_2_out, not_1_out, QD);
  S_R_Flip_Flop s_r_ff_4 (.S(not_9_out), .clk(CLK), .R(nor_4_out), .Q(QD), .reset(not_5_out));  // open: Qn, preset, en

  // Notes on the sheet:
  //   4bit universal shift register
endmodule

module _74238 (
  input  A0,
  input  A1,
  input  A2,
  input  nE1,
  input  nE2,
  input  E3,
  output Y0,
  output Y1,
  output Y2,
  output Y3,
  output Y4,
  output Y5,
  output Y6,
  output Y7
);

  wire n74138_1_y0, n74138_1_y1, n74138_1_y2, n74138_1_y3, n74138_1_y4, n74138_1_y5, n74138_1_y6, n74138_1_y7;

  _74138 u_74138_1 (
    .nE1(nE1), .nE2(nE2), .E3(E3), .A0(A0), .A1(A1), .A2(A2), .Y0(n74138_1_y0), .Y1(n74138_1_y1),
    .Y2(n74138_1_y2), .Y3(n74138_1_y3), .Y4(n74138_1_y4), .Y5(n74138_1_y5), .Y6(n74138_1_y6), .Y7(n74138_1_y7));
  not not_1 (Y0, n74138_1_y0);
  not not_2 (Y1, n74138_1_y1);
  not not_3 (Y2, n74138_1_y2);
  not not_4 (Y3, n74138_1_y3);
  not not_5 (Y4, n74138_1_y4);
  not not_6 (Y5, n74138_1_y5);
  not not_7 (Y6, n74138_1_y6);
  not not_8 (Y7, n74138_1_y7);
endmodule

module _74283 (
  input  B3,
  input  A3,
  input  B2,
  input  A2,
  input  B1,
  input  A1,
  input  B0,
  input  A0,
  input  Ci,
  output Co,
  output S3,
  output S2,
  output S1,
  output S0
);

  wire and_1_out, and_2_out, and_3_out, and_4_out, and_5_out, and_6_out, and_7_out, and_8_out, and_9_out,
       and_10_out, and_11_out, and_12_out, and_13_out, and_14_out, nand_1_out, nand_2_out, nand_3_out,
       nand_4_out, nor_1_out, nor_2_out, nor_3_out, nor_4_out, nor_6_out, nor_7_out, nor_8_out, not_1_out,
       not_2_out;

  nand nand_1 (nand_1_out, B3, A3);
  nor nor_1 (nor_1_out, B3, A3);
  nand nand_2 (nand_2_out, B2, A2);
  nor nor_2 (nor_2_out, B2, A2);
  nand nand_3 (nand_3_out, B1, A1);
  nor nor_3 (nor_3_out, B1, A1);
  nand nand_4 (nand_4_out, B0, A0);
  nor nor_4 (nor_4_out, B0, A0);
  not not_1 (not_1_out, Ci);
  and and_1 (and_1_out, nor_2_out, nand_1_out);
  and and_2 (and_2_out, nor_3_out, nand_1_out, nand_2_out);
  and and_3 (and_3_out, nor_4_out, nand_1_out, nand_2_out, nand_3_out);
  and and_4 (and_4_out, nand_1_out, nand_2_out, nand_3_out, nand_4_out, not_1_out);
  and and_5 (and_5_out, nand_1_out, ~nor_1_out);  // AND_Gate
  and and_6 (and_6_out, nor_3_out, nand_2_out);
  and and_7 (and_7_out, nor_4_out, nand_2_out, nand_3_out);
  and and_8 (and_8_out, nand_2_out, nand_3_out, nand_4_out, not_1_out);
  and and_9 (and_9_out, nand_2_out, ~nor_2_out);  // AND_Gate
  and and_10 (and_10_out, nor_4_out, nand_3_out);
  and and_11 (and_11_out, nand_3_out, nand_4_out, not_1_out);
  and and_12 (and_12_out, nand_3_out, ~nor_3_out);  // AND_Gate
  and and_13 (and_13_out, nand_4_out, not_1_out);
  and and_14 (and_14_out, nand_4_out, ~nor_4_out);  // AND_Gate
  not not_2 (not_2_out, not_1_out);
  nor nor_5 (Co, nor_1_out, and_1_out, and_2_out, and_3_out, and_4_out);
  nor nor_6 (nor_6_out, nor_2_out, and_6_out, and_7_out, and_8_out);
  nor nor_7 (nor_7_out, nor_3_out, and_10_out, and_11_out);
  nor nor_8 (nor_8_out, nor_4_out, and_13_out);
  xor xor_1 (S3, and_5_out, nor_6_out);
  xor xor_2 (S2, and_9_out, nor_7_out);
  xor xor_3 (S1, and_12_out, nor_8_out);
  xor xor_4 (S0, and_14_out, not_2_out);
endmodule

module _74393 (
  input  nCLK1,
  input  CLR1,
  input  nCLK2,
  input  CLR2,
  output _1A,
  output _1B,
  output _1C,
  output _1D,
  output _2A,
  output _2B,
  output _2C,
  output _2D
);

  wire d_ff_1_qn, d_ff_2_qn, d_ff_3_qn, d_ff_4_qn, d_ff_5_qn, d_ff_6_qn, d_ff_7_qn, d_ff_8_qn, not_1_out,
       not_2_out;

  not not_1 (not_1_out, nCLK1);
  not not_2 (not_2_out, nCLK2);
  D_Flip_Flop d_ff_1 (.clk(not_1_out), .D(d_ff_1_qn), .Q(_1A), .Qn(d_ff_1_qn), .reset(CLR1));  // open: preset, en
  D_Flip_Flop d_ff_2 (.clk(not_2_out), .D(d_ff_2_qn), .Q(_2A), .Qn(d_ff_2_qn), .reset(CLR2));  // open: preset, en
  D_Flip_Flop d_ff_3 (.clk(d_ff_1_qn), .D(d_ff_3_qn), .Q(_1B), .Qn(d_ff_3_qn), .reset(CLR1));  // open: preset, en
  D_Flip_Flop d_ff_4 (.clk(d_ff_2_qn), .D(d_ff_4_qn), .Q(_2B), .Qn(d_ff_4_qn), .reset(CLR2));  // open: preset, en
  D_Flip_Flop d_ff_5 (.clk(d_ff_3_qn), .D(d_ff_5_qn), .Q(_1C), .Qn(d_ff_5_qn), .reset(CLR1));  // open: preset, en
  D_Flip_Flop d_ff_6 (.clk(d_ff_4_qn), .D(d_ff_6_qn), .Q(_2C), .Qn(d_ff_6_qn), .reset(CLR2));  // open: preset, en
  D_Flip_Flop d_ff_7 (.clk(d_ff_5_qn), .D(d_ff_7_qn), .Q(_1D), .Qn(d_ff_7_qn), .reset(CLR1));  // open: preset, en
  D_Flip_Flop d_ff_8 (.clk(d_ff_6_qn), .D(d_ff_8_qn), .Q(_2D), .Qn(d_ff_8_qn), .reset(CLR2));  // open: preset, en

  // Notes on the sheet:
  //   Dual 4bit counter
endmodule

module _74541 (
  input  A0,
  input  A2,
  input  A3,
  input  A4,
  input  A5,
  input  A6,
  input  A7,
  input  A8,
  input  nOE1,
  input  nOE2,
  output Y0,
  output Y1,
  output Y2,
  output Y3,
  output Y4,
  output Y5,
  output Y6,
  output Y7
);

  wire and_1_out;

  and and_1 (and_1_out, ~nOE1, ~nOE2);  // AND_Gate
  assign Y0 = and_1_out ? A0 : 1'bz;  // Controlled_Buffer controlled_buffer_1
  assign Y1 = and_1_out ? A2 : 1'bz;  // Controlled_Buffer controlled_buffer_2
  assign Y2 = and_1_out ? A3 : 1'bz;  // Controlled_Buffer controlled_buffer_3
  assign Y3 = and_1_out ? A4 : 1'bz;  // Controlled_Buffer controlled_buffer_4
  assign Y4 = and_1_out ? A5 : 1'bz;  // Controlled_Buffer controlled_buffer_5
  assign Y5 = and_1_out ? A6 : 1'bz;  // Controlled_Buffer controlled_buffer_6
  assign Y6 = and_1_out ? A7 : 1'bz;  // Controlled_Buffer controlled_buffer_7
  assign Y7 = and_1_out ? A8 : 1'bz;  // Controlled_Buffer controlled_buffer_8
endmodule

module _74574___8x_D_Flip_Flop (
  input  D0,
  input  D1,
  input  D2,
  input  D3,
  input  D4,
  input  D5,
  input  D6,
  input  D7,
  input  Clk,
  input  nOE,
  output Q0,
  output Q1,
  output Q2,
  output Q3,
  output Q4,
  output Q5,
  output Q6,
  output Q7
);

  wire d_ff_1_qn, d_ff_2_qn, d_ff_3_qn, d_ff_4_qn, d_ff_5_qn, d_ff_6_qn, d_ff_7_qn, d_ff_8_qn, not_1_out;

  D_Flip_Flop d_ff_1 (.clk(Clk), .D(D0), .Qn(d_ff_1_qn));  // open: Q, preset, en, reset
  not not_1 (not_1_out, nOE);
  assign Q0 = not_1_out ? ~d_ff_1_qn : 1'bz;  // Controlled_Inverter controlled_inverter_1
  D_Flip_Flop d_ff_2 (.clk(Clk), .D(D1), .Qn(d_ff_2_qn));  // open: Q, preset, en, reset
  assign Q1 = not_1_out ? ~d_ff_2_qn : 1'bz;  // Controlled_Inverter controlled_inverter_2
  D_Flip_Flop d_ff_3 (.clk(Clk), .D(D2), .Qn(d_ff_3_qn));  // open: Q, preset, en, reset
  assign Q2 = not_1_out ? ~d_ff_3_qn : 1'bz;  // Controlled_Inverter controlled_inverter_3
  D_Flip_Flop d_ff_4 (.clk(Clk), .D(D3), .Qn(d_ff_4_qn));  // open: Q, preset, en, reset
  assign Q3 = not_1_out ? ~d_ff_4_qn : 1'bz;  // Controlled_Inverter controlled_inverter_4
  D_Flip_Flop d_ff_5 (.clk(Clk), .D(D4), .Qn(d_ff_5_qn));  // open: Q, preset, en, reset
  assign Q4 = not_1_out ? ~d_ff_5_qn : 1'bz;  // Controlled_Inverter controlled_inverter_5
  D_Flip_Flop d_ff_6 (.clk(Clk), .D(D5), .Qn(d_ff_6_qn));  // open: Q, preset, en, reset
  assign Q5 = not_1_out ? ~d_ff_6_qn : 1'bz;  // Controlled_Inverter controlled_inverter_6
  D_Flip_Flop d_ff_7 (.clk(Clk), .D(D6), .Qn(d_ff_7_qn));  // open: Q, preset, en, reset
  assign Q6 = not_1_out ? ~d_ff_7_qn : 1'bz;  // Controlled_Inverter controlled_inverter_7
  D_Flip_Flop d_ff_8 (.clk(Clk), .D(D7), .Qn(d_ff_8_qn));  // open: Q, preset, en, reset
  assign Q7 = not_1_out ? ~d_ff_8_qn : 1'bz;  // Controlled_Inverter controlled_inverter_8
endmodule

module Am25LS2517 (
  input  Cn,
  input  [3:0] A,
  input  [3:0] B,
  input  [2:0] Op,
  output Cn_4,
  output OVR,
  output [3:0] Out
);

  wire c1, c2, c3, O1, O2, O3;
  wire [3:0] and_1_out, n4bit_addsub_1_out, n4bit_addsub_2_out, n4bit_addsub_3_out, or_1_out, xor_1_out;

  _4bit_AddSub u_4bit_addsub_1 (.A(B), .B(A), .Out(n4bit_addsub_1_out), .Sub__Add(1'b1), .Cn(Cn), .Cn_4(c1), .OVR(O1));
  _4bit_AddSub u_4bit_addsub_2 (.A(A), .B(B), .Out(n4bit_addsub_2_out), .Sub__Add(1'b1), .Cn(Cn), .Cn_4(c2), .OVR(O2));
  _4bit_AddSub u_4bit_addsub_3 (.A(A), .B(B), .Out(n4bit_addsub_3_out), .Sub__Add(1'b0), .Cn(Cn), .Cn_4(c3), .OVR(O3));
  assign xor_1_out = A ^ B;  // XOR_Gate xor_1, 4 bits wide
  assign or_1_out = A | B;  // OR_Gate or_1, 4 bits wide
  assign and_1_out = A & B;  // AND_Gate and_1, 4 bits wide
  Multiplexer #(.select(3), .width(4), .enable("false")) multiplexer_1 (
    .in0(4'b0000), .in1(n4bit_addsub_1_out), .in2(n4bit_addsub_2_out), .in3(n4bit_addsub_3_out),
    .in4(xor_1_out), .in5(or_1_out), .in6(and_1_out), .in7(4'b1111), .out(Out), .sel(Op));
  Multiplexer #(.select(3), .enable("false")) multiplexer_2 (
    .in0(1'b0), .in1(c1), .in2(c2), .in3(c3), .in4(1'b0), .in5(1'b0), .in6(1'b0), .in7(1'b0), .out(Cn_4),
    .sel(Op));
  Multiplexer #(.select(3), .enable("false")) multiplexer_3 (
    .in0(1'b0), .in1(O1), .in2(O2), .in3(O3), .in4(1'b0), .in5(1'b0), .in6(1'b0), .in7(1'b0), .out(OVR),
    .sel(Op));
endmodule

module _4bit_AddSub (
  input  Sub__Add,
  input  Cn,
  input  [3:0] A,
  input  [3:0] B,
  output [3:0] Out,
  output Cn_4,
  output OVR
);

  wire adder_1_cout, adder_2_cout, adder_3_cout, xor_1_out, xor_2_out, xor_3_out, xor_4_out;

  xor xor_1 (xor_1_out, Sub__Add, B[0]);
  xor xor_2 (xor_2_out, Sub__Add, B[1]);
  xor xor_3 (xor_3_out, Sub__Add, B[2]);
  xor xor_4 (xor_4_out, Sub__Add, B[3]);
  Adder #(.width(1)) adder_1 (.a(A[0]), .b(xor_1_out), .out(Out[0]), .cin(Cn), .cout(adder_1_cout));
  Adder #(.width(1)) adder_2 (.a(A[1]), .b(xor_2_out), .out(Out[1]), .cin(adder_1_cout), .cout(adder_2_cout));
  Adder #(.width(1)) adder_3 (.a(A[2]), .b(xor_3_out), .out(Out[2]), .cin(adder_2_cout), .cout(adder_3_cout));
  Adder #(.width(1)) adder_4 (.a(A[3]), .b(xor_4_out), .out(Out[3]), .cin(adder_3_cout), .cout(Cn_4));
  xor xor_5 (OVR, Cn_4, adder_3_cout);
endmodule

module _8bit_to_bus (
  input  in_1,
  input  in_2,
  input  in_3,
  input  in_4,
  input  in_5,
  input  in_6,
  input  in_7,
  input  in_8,
  output [7:0] out_9
);


  assign out_9 = {in_8, in_7, in_6, in_5, in_4, in_3, in_2, in_1};
endmodule

module bus_to_8bit (
  input  [7:0] in_1,
  output out_2,
  output out_3,
  output out_4,
  output out_5,
  output out_6,
  output out_7,
  output out_8,
  output out_9
);


  assign out_2 = in_1[0];
  assign out_3 = in_1[1];
  assign out_4 = in_1[2];
  assign out_5 = in_1[3];
  assign out_6 = in_1[4];
  assign out_7 = in_1[5];
  assign out_8 = in_1[6];
  assign out_9 = in_1[7];
endmodule

module IRQ_Tester (
  input  IRQ,
  input  reset,
  input  INTA,
  output IRQ_2
);

  wire controlled_buffer_1_out, s_r_ff_1_qn;

  S_R_Flip_Flop s_r_ff_1 (.Qn(s_r_ff_1_qn), .preset(IRQ), .reset(reset));  // open: S, clk, R, Q, en
  assign controlled_buffer_1_out = s_r_ff_1_qn ? IRQ : 1'bz;  // Controlled_Buffer controlled_buffer_1
  Pull_Resistor pull_resistor_1 (.node(controlled_buffer_1_out));
  S_R_Flip_Flop s_r_ff_2 (.Q(IRQ_2), .preset(controlled_buffer_1_out), .reset(INTA));  // open: S, clk, R, Qn, en
endmodule

module Byte_Selector (
  input  WE,
  input  BYTE,
  input  MAR_0,
  input  WE_2,
  input  BYTE_2,
  input  MAR_0_2,
  input  [3:0] in_7,
  input  in_8,
  input  [3:0] in_9,
  input  M__IO,
  input  RE,
  input  WE_3,
  output BE0,
  output BE1,
  output BE0_2,
  output BE1_2
);

  wire and_1_out, and_2_out, and_5_out, nand_1_out, nand_2_out, not_1_out, not_2_out, not_3_out, not_4_out,
       not_5_out, not_6_out, not_7_out, or_1_out;
  wire [3:0] ram_1_data;

  not not_1 (not_1_out, MAR_0);
  not not_2 (not_2_out, MAR_0_2);
  and and_1 (and_1_out, BYTE, MAR_0);
  not not_3 (not_3_out, and_1_out);
  and and_2 (and_2_out, not_1_out, BYTE);
  not not_4 (not_4_out, and_2_out);
  nand nand_1 (nand_1_out, BYTE_2, MAR_0_2);
  nand nand_2 (nand_2_out, not_2_out, BYTE_2);
  and and_3 (BE0, WE, not_3_out);
  and and_4 (BE1, WE, not_4_out);
  nand nand_3 (BE0_2, WE_2, nand_1_out);
  nand nand_4 (BE1_2, WE_2, nand_2_out);
  not not_5 (not_5_out, M__IO);
  not not_6 (not_6_out, RE);
  not not_7 (not_7_out, WE_3);
  or or_1 (or_1_out, not_6_out, not_7_out);
  and and_5 (and_5_out, not_5_out, or_1_out);
  RAM #(.addrWidth(4), .dataWidth(4), .bus("asynch")) ram_1 (
    .addr(in_9), .data(ram_1_data), .sel(and_5_out), .ld(not_6_out));  // open: clr
  Hex_Digit_Display hex_digit_display_1 (.value(ram_1_data));  // open: dp
  assign ram_1_data = in_8 ? in_7 : 4'bz;  // Controlled_Buffer controlled_buffer_1
endmodule

module clk_test (
  input  CLK_IN,
  input  in_2,
  input  in_3,
  input  in_4,
  output [7:0] out_5
);

  wire CLK_OUT, CLK_OUT_t, j_k_ff_2_qn, n8bit_counter_register_1_p4;

  J_K_Flip_Flop j_k_ff_1 (
    .J(j_k_ff_2_qn), .clk(CLK_IN), .K(1'b1), .Q(CLK_OUT_t), .Qn(CLK_OUT));  // open: preset, en, reset
  J_K_Flip_Flop j_k_ff_2 (.J(in_2), .clk(CLK_IN), .K(in_3), .Qn(j_k_ff_2_qn));  // open: Q, preset, en, reset
  // _8bit_Counter_Register 8bit_counter_register_1: pin names not known; wires that end beside it: 1'b1, out_5, in_4, n8bit_counter_register_1_p4
  Pull_Resistor pull_resistor_1 (.node(n8bit_counter_register_1_p4));

  // Other names for the same wires on the sheet: continue = in_3; halt = in_2

  // Notes on the sheet:
  //   74 73
  //   Normal system clock
endmodule

module CU_INT_test (
  input  in_1,
  input  in_2,
  input  in_3,
  input  in_4
);

  wire not_1_out, not_2_out, not_3_out;

  not not_1 (not_1_out, in_2);
  not not_2 (not_2_out, in_3);
  not not_3 (not_3_out, in_4);
  _74148 u_74148_1 (
    ._0__10(1'b1), ._1__11(1'b1), ._2__12(1'b1), ._3__13(1'b1), ._4__1(not_1_out), ._5__2(not_2_out),
    ._6__3(not_3_out), ._7__4(1'b1), .EI__5(in_1));  // open: EO__15, G5__14, A0__9, A1__7, A2__6
endmodule

module IRQ_Daisy_Chain_test (
  input  INT,
  input  INT_2,
  input  nINTA,
  output [7:0] DATABUS,
  output nINT
);

  wire not_1_out, not_2_out, or_1_out, or_2_out, or_3_out, or_4_out;

  Pull_Resistor #(.pull(1)) pull_resistor_1 (.node(nINT));
  Buffer_tri_state_8bit INT_VECT_0 (.IN(8'h4), .OE(or_1_out), .OUT(DATABUS));
  or or_1 (or_1_out, nINTA, not_1_out);
  not not_1 (not_1_out, INT);
  or or_2 (or_2_out, INT, nINTA);
  Transistor #(.\type ("n")) transistor_1 (.in(1'b0), .out(nINT), .gate(INT));
  or or_3 (or_3_out, or_2_out, not_2_out);
  Buffer_tri_state_8bit INT_VECT_1 (.IN(8'h8), .OE(or_3_out), .OUT(DATABUS));
  not not_2 (not_2_out, INT_2);
  or or_4 (or_4_out, INT_2, or_2_out);
  Transistor #(.\type ("n")) transistor_2 (.in(1'b0), .out(nINT), .gate(INT_2));
endmodule
